// Logisim project cpu24.circ as structural Verilog
module \单周期MIPS  (
  input  IR1,
  input  IR2,
  input  IR3,
  output RegWrite,
  output MemWrite,
  output [31:0] PC,
  output [31:0] IR,
  output [31:0] RDin,
  output [31:0] MDin,
  output [31:0] LedData
);

  wire and_1_out, and_2_out, and_3_out, and_4_out, CLK, clock_2_out, comparator_1_eq, comparator_1_lt,
       d_ff_1_q, equal, ERET, Go, IR1_t, IR2_t, IR3_t, IRA, IRB, IRC, nand_1_out, not_1_out, not_2_out,
       or_1_out, power, RST, SignedExt, Syscall, W1, W2, W3, \单周期硬布线控制器_1_alu_src , \单周期硬布线控制器_1_beq ,
       \单周期硬布线控制器_1_bne , \单周期硬布线控制器_1_jal , \单周期硬布线控制器_1_memtoreg , \单周期硬布线控制器_1_regdst ;
  wire [1:0] \单周期硬布线控制器_1_jr ;
  wire [3:0] adder_1_out_2, \单周期硬布线控制器_1_alu_op ;
  wire [4:0] multiplexer_3_out, multiplexer_4_out, multiplexer_5_out, multiplexer_7_out;
  wire [7:0] multiplexer_12_out;
  wire [12:0] CNT_num;
  wire [15:0] adder_2_out, \总周期数 ;
  wire [27:0] adder_1_out;
  wire [31:0] adder_3_out, bit_extender_1_out, bit_extender_2_out, mips_alu_1_result, multiplexer_1_out,
       multiplexer_2_out, multiplexer_6_out, multiplexer_9_out, multiplexer_10_out, multiplexer_11_out, R1,
       ram_1_data, shifter_1_out;

  Clock #(.highDuration(1), .lowDuration(1)) clock_1 ();  // open: out
  Button _1 (.out(IRA));
  Button _2 (.out(IRB));
  Button _3 (.out(IRC));
  Button \u_继续运行  (.out(Go));
  LED #(.active("true")) led_1 (.in(W1));
  LED #(.active("true")) led_2 (.in(W2));
  LED #(.active("true")) led_3 (.in(W3));
  Button button_1 (.out(RST));
  or or_1 (or_1_out, and_2_out, and_3_out);
  Multiplexer #(.select(1), .width(32), .disabled("Z"), .enable("false")) multiplexer_1 (
    .in0({adder_1_out_2, adder_1_out}), .in1(adder_3_out), .out(multiplexer_1_out), .sel(or_1_out));
  D_Flip_Flop #(.trigger("high"), .Pre_Clr_Positions("LEGACY"), .NegatePresetClear("false"), .enable("true"), .NewFFLayout("false")) d_ff_1 (.Q(d_ff_1_q));  // open: clk, D, Qn, preset, en, reset
  // Probe on 13'h607
  Hex_Digit_Display hex_digit_display_1 (.value(LedData[31:28]));  // open: dp
  Comparator #(.width(13), .mode("twosComplement")) comparator_1 (
    .a(CNT_num), .b(13'h607), .eq(comparator_1_eq), .lt(comparator_1_lt));  // open: gt
  Clock #(.highDuration(1), .lowDuration(1)) clock_2 (.out(clock_2_out));
  Hex_Digit_Display hex_digit_display_2 (.value(LedData[23:20]));  // open: dp
  Hex_Digit_Display hex_digit_display_3 (.value(LedData[27:24]));  // open: dp
  Multiplexer #(.select(2), .width(32), .disabled("Z"), .enable("false")) multiplexer_2 (
    .in0(multiplexer_1_out), .in1(R1), .in2({adder_1_out_2, IR[25:0], 2'b00}), .in3(R1),
    .out(multiplexer_2_out), .sel(\单周期硬布线控制器_1_jr ));
  Register #(.width(32), .trigger("rising"), .Select("low")) u_PC (
    .D(multiplexer_2_out), .en(power), .Q(PC), .clk(CLK), .clr(RST));
  nand nand_1 (nand_1_out, d_ff_1_q, comparator_1_eq);
  Counter #(.width(13), .max('h1fff), .ongoal("stay"), .trigger("rising"), .behavior("old")) counter_1 (
    .count(comparator_1_lt), .Q(CNT_num), .clk(clock_2_out));  // open: load, D, carry, clr, preset
  Hex_Digit_Display hex_digit_display_4 (.value(LedData[19:16]));  // open: dp
  Hex_Digit_Display hex_digit_display_5 (.value(LedData[15:12]));  // open: dp
  Register #(.width(16), .trigger("rising"), .Select("low")) register_1 (
    .D(adder_2_out), .en(power), .Q(\总周期数 ), .clk(CLK), .clr(RST));
  Hex_Digit_Display hex_digit_display_6 (.value(LedData[11:8]));  // open: dp
  Hex_Digit_Display hex_digit_display_7 (.value(LedData[7:4]));  // open: dp
  // Probe on \总周期数 
  Adder #(.width(32)) adder_1 (.a(PC), .b(32'h4), .out({adder_1_out_2, adder_1_out}));  // open: cin, cout
  Adder #(.width(16)) adder_2 (.a(\总周期数 ), .b(16'h1), .out(adder_2_out));  // open: cin, cout
  assign CLK = nand_1_out ? clock_2_out : 1'bz;  // Controlled_Buffer controlled_buffer_1
  Pull_Resistor #(.pull(1)) pull_resistor_1 (.node(CLK));
  Hex_Digit_Display hex_digit_display_8 (.value(LedData[3:0]));  // open: dp
  ROM #(.addrWidth(10), .dataWidth(32), .Select("high")) rom_1 (.addr(PC[11:2]), .data(IR));
  or or_2 (IR1_t, IR1, IRA);
  not not_1 (not_1_out, equal);
  or or_3 (IR2_t, IR2, IRB);
  and and_1 (and_1_out, Syscall, not_1_out);
  // Mips_Probe mips_probe_1: pin names not known; wires that end beside it: IR, IR
  J_K_Flip_Flop #(.trigger("rising"), .Pre_Clr_Positions("ABOVE_BELOW"), .NegatePresetClear("false"), .enable("false"), .NewFFLayout("true")) j_k_ff_1 (
    .J(and_1_out), .clk(CLK), .K(Go), .Qn(power), .reset(Go));  // open: Q, preset
  or or_4 (IR3_t, IR3, IRC);
  assign bit_extender_1_out = {{16{1'b0}}, IR[15:0]};  // Bit_Extender bit_extender_1
  assign bit_extender_2_out = {{16{IR[15]}}, IR[15:0]};  // Bit_Extender bit_extender_2
  \单周期硬布线控制器  \u_单周期硬布线控制器_1  (
    .Func(IR[5:0]), .OP(IR[31:26]), .ALU_OP(\单周期硬布线控制器_1_alu_op ), .MemToReg(\单周期硬布线控制器_1_memtoreg ),
    .MemWrite(MemWrite), .ALU_SRC(\单周期硬布线控制器_1_alu_src ), .RegWrite(RegWrite), .SysCALL(Syscall),
    .SignedExt(SignedExt), .RegDst(\单周期硬布线控制器_1_regdst ), .JR(\单周期硬布线控制器_1_jr [0]),
    .JMP(\单周期硬布线控制器_1_jr [1]), .Beq(\单周期硬布线控制器_1_beq ), .JAL(\单周期硬布线控制器_1_jal ), .Bne(\单周期硬布线控制器_1_bne ),
    .ERET(ERET));  // open: LUI, LB, BGTZ
  Multiplexer #(.select(1), .width(5), .disabled("Z"), .enable("false")) multiplexer_3 (
    .in0(IR[25:21]), .in1(5'b00010), .out(multiplexer_3_out), .sel(Syscall));
  Multiplexer #(.select(1), .width(5), .disabled("Z"), .enable("false")) multiplexer_4 (
    .in0(IR[20:16]), .in1(5'b00100), .out(multiplexer_4_out), .sel(Syscall));
  Multiplexer #(.select(1), .width(5), .disabled("Z"), .enable("false")) multiplexer_5 (
    .in0(IR[20:16]), .in1(IR[15:11]), .out(multiplexer_5_out), .sel(\单周期硬布线控制器_1_regdst ));
  Multiplexer #(.select(1), .width(32), .disabled("Z"), .enable("false")) multiplexer_6 (
    .in0(bit_extender_1_out), .in1(bit_extender_2_out), .out(multiplexer_6_out), .sel(SignedExt));
  and and_2 (and_2_out, \单周期硬布线控制器_1_beq , equal);
  Multiplexer #(.select(1), .width(5), .disabled("Z"), .enable("false")) multiplexer_7 (
    .in0(multiplexer_5_out), .in1({5{1'b1}}), .out(multiplexer_7_out), .sel(\单周期硬布线控制器_1_jal ));
  Multiplexer #(.select(1), .width(32), .disabled("Z"), .enable("false")) multiplexer_8 (
    .in0(multiplexer_11_out), .in1({adder_1_out_2, adder_1_out}), .out(RDin), .sel(\单周期硬布线控制器_1_jal ));
  MIPS_Regifile mips_regifile_1 (
    .Din(RDin), .Clk(CLK), .R1(R1), .R2(MDin), .WE(RegWrite), .W_num(multiplexer_7_out),
    .R1_num(multiplexer_3_out), .R2_num(multiplexer_4_out));
  Shifter #(.width(32), .shift("ll")) shifter_1 (.in(multiplexer_6_out), .\dist (5'b00010), .out(shifter_1_out));
  and and_3 (and_3_out, \单周期硬布线控制器_1_bne , not_2_out);
  not not_2 (not_2_out, equal);
  Adder #(.width(32)) adder_3 (
    .a(shifter_1_out), .b({adder_1_out_2, adder_1_out}), .out(adder_3_out));  // open: cin, cout
  Multiplexer #(.select(1), .width(32), .disabled("Z"), .enable("false")) multiplexer_9 (
    .in0(MDin), .in1(multiplexer_6_out), .out(multiplexer_9_out), .sel(\单周期硬布线控制器_1_alu_src ));
  and and_4 (and_4_out, Syscall, equal);
  Multiplexer #(.select(1), .width(32), .disabled("Z"), .enable("false")) multiplexer_10 (
    .in0(multiplexer_9_out), .in1(32'h22), .out(multiplexer_10_out), .sel(Syscall));
  MIPS_ALU mips_alu_1 (
    .X(R1), .Y(multiplexer_10_out), .AluOP(\单周期硬布线控制器_1_alu_op ), .Equal(equal), .Result(mips_alu_1_result),
    .shamt(IR[10:6]));  // open: Result_2
  Register #(.width(32), .trigger("rising"), .Select("low")) register_2 (
    .D(MDin), .en(and_4_out), .Q(LedData), .clk(CLK), .clr(RST));
  RAM #(.addrWidth(10), .dataWidth(32), .bus("separate"), .Select("high")) ram_1 (
    .addr(mips_alu_1_result[11:2]), .din(MDin), .data(ram_1_data), .str(MemWrite), .clk(CLK), .clr(RST));  // open: sel, ld
  Multiplexer #(.select(1), .width(32), .disabled("Z"), .enable("false")) multiplexer_11 (
    .in0(mips_alu_1_result), .in1(ram_1_data), .out(multiplexer_11_out), .sel(\单周期硬布线控制器_1_memtoreg ));
  Multiplexer #(.select(2), .width(8), .disabled("Z"), .enable("false")) multiplexer_12 (
    .in0(multiplexer_11_out[7:0]), .in1(multiplexer_11_out[15:8]), .in2(multiplexer_11_out[23:16]),
    .in3(multiplexer_11_out[31:24]), .out(multiplexer_12_out), .sel(mips_alu_1_result[1:0]));
  Bit_Extender #(.in_width(8), .out_width(16), .\type ("sign")) bit_extender_3 (.in(multiplexer_12_out));  // open: out

  // Other names for the same wires on the sheet: R2[31:0] = MDin

  // Notes on the sheet:
  //   中断源
  //   中断等待指示
  //   总复位信号应将除ROM以外所有存储组件全部清零
  //   控制位
  //   暂停节拍，不能为0
  //   戳工具置1进入计数暂停模式，ctrl+k时钟自动运行到对应节拍暂停
  //   ctrl+k关闭时钟连续运行，将控制位置零，进入单步调试模式调试
  //   用这个时钟源需要去掉电路中的其他时钟源
  //   数码管输出
  //   可计数暂停的时钟源
  //   数码管输出应该用寄存器锁存，否则显示数据只能一闪而过
  //   指令存储器
  //   指令字
  //   contents of rom_1 (hex, n*v repeats v):
  //   20110001 8000c05 20110001 20120002 20130003 8000c09 20110001 20120002 20130003 8000c0d 20110001
  //   20120002 20130003 8000c11 20110001 20120002 20130003 c000cb8 20100001 20110001 118fc0 112020
  //   20020022 c 118882 12200001 8000c15 112020 20020022 c 20110001 118880 112020 20020022 c 12200001
  //   8000c1f 20110001 118fc0 112020 20020022 c 1188c3 112020 20020022 c 118903 112020 20020022 c 118903
  //   112020 20020022 c 118903 112020 20020022 c 118903 112020 20020022 c 118903 112020 20020022 c 118903
  //   112020 20020022 c 118903 112020 20020022 c 20100001 109fc0 139fc3 8021 2012000c 24160003 26100001
  //   3210000f 20080008 20090001 139900 2709825 132020 20020022 c 1094022 1500fff9 22100001 2018000f
  //   2188024 108700 20080008 20090001 139902 2709825 132021 20020022 c 1094022 1500fff9 108702 2c9b022
  //   12c00001 8000c50 4020 1084027 84400 3508ffff 82021 20020022 c 2010ffff 20110000 ae300000 22100001
  //   22310004 ae300000 22100001 22310004 ae300000 22100001 22310004 ae300000 22100001 22310004 ae300000
  //   22100001 22310004 ae300000 22100001 22310004 ae300000 22100001 22310004 ae300000 22100001 22310004
  //   ae300000 22100001 22310004 ae300000 22100001 22310004 ae300000 22100001 22310004 ae300000 22100001
  //   22310004 ae300000 22100001 22310004 ae300000 22100001 22310004 ae300000 22100001 22310004 ae300000
  //   22100001 22310004 22100001 8020 2011003c 8e130000 8e340000 274402a 11000002 ae330000 ae140000
  //   2231fffc 1611fff8 102020 20020022 c 22100004 2011003c 1611fff2 20020032 c 20100000 22100001 102020
  //   20020022 c 22100002 102020 20020022 c 22100003 102020 20020022 c 22100004 102020 20020022 c 22100005
  //   102020 20020022 c 22100006 102020 20020022 c 22100007 102020 20020022 c 22100008 102020 20020022
  //   20020022 c 3e00008
  //   OP
  //   Func
  //   rs
  //   rt
  //   rd
  //   im
  //   ii
  //   JMP
  //   JR
  //   OP
  //   Func
  //   Beq
  //   Bne
  //   MemToReg
  //   MemWrite
  //   AluOP
  //   AluSrcB
  //   RegWrite
  //   JAL
  //   RegDst
  //   Syscall
  //   为方便自动评测，需要输出PC，IR，寄存器堆写如数据RDin
  //   RAM写使能MemWrite、RAM写入数据MDin等信号
endmodule

// 单周期硬布线控制器
module \单周期硬布线控制器  (
  input  [5:0] OP,
  input  [5:0] Func,
  output [3:0] ALU_OP,
  output MemToReg,
  output MemWrite,
  output ALU_SRC,
  output RegWrite,
  output SysCALL,
  output SignedExt,
  output RegDst,
  output Beq,
  output Bne,
  output JR,
  output JMP,
  output JAL,
  output LUI,
  output LB,
  output BGTZ,
  output ERET
);

  \运算控制器自动生成  \u_运算控制器自动生成_1  (
    .OP0(OP[0]), .OP1(OP[1]), .OP2(OP[2]), .OP3(OP[3]), .OP4(OP[4]), .OP5(OP[5]), .F0(Func[0]), .F1(Func[1]),
    .F2(Func[2]), .F3(Func[3]), .F4(Func[4]), .F5(Func[5]), .S0(ALU_OP[0]), .S1(ALU_OP[1]), .S2(ALU_OP[2]),
    .S3(ALU_OP[3]));
  \控制信号自动生成  \u_控制信号自动生成_1  (
    .OP0(OP[0]), .OP1(OP[1]), .OP2(OP[2]), .MemToReg(MemToReg), .OP3(OP[3]), .OP4(OP[4]), .OP5(OP[5]),
    .MemWrite(MemWrite), .F0(Func[0]), .F1(Func[1]), .F2(Func[2]), .F3(Func[3]), .F4(Func[4]), .F5(Func[5]),
    .ALU_SRC(ALU_SRC), .RegWrite(RegWrite), .SysCALL(SysCALL), .SignedExt(SignedExt), .RegDst(RegDst),
    .BEQ(Beq), .BNE(Bne), .JR(JR), .JUMP(JMP), .JAL(JAL), .LUI(LUI), .LB(LB), .BGTZ(BGTZ), .ERET(ERET));

  // Other names for the same wires on the sheet: OP_CODE[5:0] = OP

  // Notes on the sheet:
  //   运算器控制器，根据指令生成运算器功能选择信号
  //   控制信号生成，产生数据通路需要的其他控制信号
endmodule

// 运算器控制器
module \运算控制器自动生成  (
  input  OP0,
  input  OP1,
  input  OP2,
  input  OP3,
  input  OP4,
  input  OP5,
  input  F0,
  input  F1,
  input  F2,
  input  F3,
  input  F4,
  input  F5,
  output S0,
  output S1,
  output S2,
  output S3
);

  wire and_1_out, and_2_out, and_3_out, and_4_out, and_5_out, and_6_out, and_7_out, and_8_out, and_9_out,
       and_10_out, and_11_out, and_12_out, and_13_out, and_14_out, and_15_out, and_16_out, and_17_out,
       and_18_out, and_19_out, and_20_out, and_21_out, and_22_out, and_23_out, and_24_out, and_25_out,
       and_26_out, and_27_out, and_28_out, and_29_out, and_30_out, and_31_out, and_32_out, and_33_out,
       and_34_out, and_35_out, and_36_out, and_37_out, and_38_out, and_39_out, not_1_out, not_2_out,
       not_3_out, not_4_out, not_5_out, not_6_out, not_7_out, not_8_out, not_9_out, not_10_out, not_11_out,
       not_12_out, not_13_out, not_14_out, not_15_out, not_16_out, not_17_out, not_18_out, not_19_out,
       not_20_out, not_21_out, not_22_out, not_23_out, not_24_out, not_25_out, not_26_out, not_27_out,
       not_28_out, not_29_out, not_30_out, not_31_out, not_32_out, not_33_out, not_34_out, not_35_out,
       not_36_out, not_37_out, not_38_out, not_39_out, not_40_out, not_41_out, not_42_out, not_43_out,
       not_44_out, not_45_out, not_46_out, not_47_out, not_48_out, not_49_out, not_50_out, not_51_out,
       not_52_out, not_53_out, not_54_out, not_55_out, not_56_out, not_57_out, not_58_out, not_59_out,
       not_60_out, not_61_out, not_62_out, not_63_out, not_64_out, not_65_out, not_66_out, not_67_out,
       not_68_out, not_69_out, not_70_out, not_71_out, not_72_out, not_73_out, not_74_out, not_75_out,
       not_76_out, not_77_out, not_78_out, not_79_out, not_80_out, not_81_out, not_82_out, not_83_out,
       not_84_out, not_85_out, not_86_out, not_87_out, not_88_out, not_89_out, not_90_out, not_91_out,
       not_92_out, not_93_out, not_94_out, not_95_out, not_96_out, not_97_out, not_98_out, not_99_out,
       not_100_out, not_101_out, not_102_out, not_103_out, not_104_out, not_105_out, not_106_out,
       not_107_out, not_108_out, not_109_out, not_110_out, not_111_out, not_112_out, not_113_out,
       not_114_out, not_115_out, not_116_out, not_117_out, not_118_out, not_119_out, not_120_out,
       not_121_out, not_122_out, not_123_out, not_124_out, not_125_out, not_126_out, not_127_out,
       not_128_out, not_129_out, not_130_out, not_131_out, not_132_out, not_133_out, not_134_out,
       not_135_out, not_136_out, not_137_out, not_138_out, not_139_out, not_140_out, not_141_out,
       not_142_out, not_143_out, not_144_out, not_145_out, not_146_out, not_147_out, not_148_out,
       not_149_out, not_150_out, not_151_out, not_152_out, not_153_out, not_154_out, not_155_out,
       not_156_out, not_157_out, not_158_out, not_159_out, not_160_out, not_161_out, not_162_out,
       not_163_out, not_164_out, not_165_out, not_166_out, not_167_out, not_168_out, not_169_out,
       not_170_out, not_171_out, not_172_out, not_173_out, not_174_out, not_175_out, not_176_out,
       not_177_out, not_178_out, not_179_out, not_180_out, not_181_out, not_182_out, not_183_out,
       not_184_out, not_185_out, not_186_out, not_187_out, not_188_out, not_189_out, not_190_out,
       not_191_out, not_192_out, not_193_out, not_194_out, not_195_out, not_196_out, not_197_out,
       not_198_out, not_199_out, not_200_out, not_201_out, not_202_out, not_203_out, not_204_out,
       not_205_out, not_206_out, not_207_out, not_208_out, not_209_out, not_210_out, not_211_out,
       not_212_out, not_213_out, not_214_out, not_215_out, not_216_out, not_217_out, not_218_out,
       not_219_out, not_220_out, not_221_out, not_222_out, not_223_out, not_224_out, not_225_out,
       not_226_out, not_227_out, not_228_out, not_229_out, not_230_out, not_231_out, not_232_out;

  not not_1 (not_1_out, OP5);
  not not_2 (not_2_out, OP4);
  not not_3 (not_3_out, OP3);
  not not_4 (not_4_out, OP2);
  not not_5 (not_5_out, OP1);
  not not_6 (not_6_out, OP0);
  not not_7 (not_7_out, F5);
  not not_8 (not_8_out, F4);
  not not_9 (not_9_out, F3);
  not not_10 (not_10_out, F2);
  not not_11 (not_11_out, OP5);
  not not_12 (not_12_out, OP4);
  not not_13 (not_13_out, OP3);
  not not_14 (not_14_out, OP2);
  not not_15 (not_15_out, OP1);
  not not_16 (not_16_out, OP0);
  not not_17 (not_17_out, F4);
  not not_18 (not_18_out, F3);
  not not_19 (not_19_out, F2);
  not not_20 (not_20_out, F1);
  not not_21 (not_21_out, F0);
  not not_22 (not_22_out, OP5);
  not not_23 (not_23_out, OP4);
  not not_24 (not_24_out, OP3);
  not not_25 (not_25_out, OP2);
  not not_26 (not_26_out, OP1);
  not not_27 (not_27_out, OP0);
  not not_28 (not_28_out, F4);
  not not_29 (not_29_out, F3);
  not not_30 (not_30_out, F2);
  not not_31 (not_31_out, F1);
  not not_32 (not_32_out, OP5);
  not not_33 (not_33_out, OP4);
  not not_34 (not_34_out, OP3);
  not not_35 (not_35_out, OP2);
  not not_36 (not_36_out, OP1);
  not not_37 (not_37_out, OP0);
  not not_38 (not_38_out, F4);
  not not_39 (not_39_out, F3);
  not not_40 (not_40_out, F1);
  not not_41 (not_41_out, F0);
  not not_42 (not_42_out, OP5);
  not not_43 (not_43_out, OP4);
  not not_44 (not_44_out, OP3);
  not not_45 (not_45_out, OP2);
  not not_46 (not_46_out, OP1);
  not not_47 (not_47_out, OP0);
  not not_48 (not_48_out, F4);
  not not_49 (not_49_out, F2);
  not not_50 (not_50_out, F0);
  not not_51 (not_51_out, OP5);
  not not_52 (not_52_out, OP4);
  not not_53 (not_53_out, OP3);
  not not_54 (not_54_out, OP1);
  not not_55 (not_55_out, OP0);
  not not_56 (not_56_out, OP5);
  not not_57 (not_57_out, OP4);
  not not_58 (not_58_out, OP3);
  not not_59 (not_59_out, OP1);
  not not_60 (not_60_out, OP5);
  not not_61 (not_61_out, OP4);
  not not_62 (not_62_out, OP2);
  not not_63 (not_63_out, OP1);
  not not_64 (not_64_out, OP0);
  not not_65 (not_65_out, OP5);
  not not_66 (not_66_out, OP4);
  not not_67 (not_67_out, OP1);
  not not_68 (not_68_out, OP0);
  not not_69 (not_69_out, OP5);
  not not_70 (not_70_out, OP4);
  not not_71 (not_71_out, OP2);
  not not_72 (not_72_out, OP1);
  not not_73 (not_73_out, OP5);
  not not_74 (not_74_out, OP4);
  not not_75 (not_75_out, OP2);
  not not_76 (not_76_out, OP0);
  not not_77 (not_77_out, OP4);
  not not_78 (not_78_out, OP3);
  not not_79 (not_79_out, OP2);
  not not_80 (not_80_out, OP4);
  not not_81 (not_81_out, OP2);
  not not_82 (not_82_out, OP4);
  not not_83 (not_83_out, OP3);
  not not_84 (not_84_out, OP2);
  not not_85 (not_85_out, OP1);
  not not_86 (not_86_out, OP0);
  not not_87 (not_87_out, OP5);
  not not_88 (not_88_out, OP4);
  not not_89 (not_89_out, OP3);
  not not_90 (not_90_out, OP5);
  not not_91 (not_91_out, OP4);
  not not_92 (not_92_out, OP3);
  not not_93 (not_93_out, OP2);
  not not_94 (not_94_out, OP1);
  not not_95 (not_95_out, OP0);
  not not_96 (not_96_out, F5);
  not not_97 (not_97_out, F4);
  not not_98 (not_98_out, F3);
  not not_99 (not_99_out, F2);
  not not_100 (not_100_out, F0);
  not not_101 (not_101_out, OP5);
  not not_102 (not_102_out, OP4);
  not not_103 (not_103_out, OP3);
  not not_104 (not_104_out, OP2);
  not not_105 (not_105_out, OP1);
  not not_106 (not_106_out, OP0);
  not not_107 (not_107_out, F4);
  not not_108 (not_108_out, F3);
  not not_109 (not_109_out, F2);
  not not_110 (not_110_out, F0);
  not not_111 (not_111_out, OP5);
  not not_112 (not_112_out, OP4);
  not not_113 (not_113_out, OP3);
  not not_114 (not_114_out, OP2);
  not not_115 (not_115_out, OP1);
  not not_116 (not_116_out, OP0);
  not not_117 (not_117_out, F4);
  not not_118 (not_118_out, F3);
  not not_119 (not_119_out, F1);
  not not_120 (not_120_out, F0);
  not not_121 (not_121_out, OP5);
  not not_122 (not_122_out, OP4);
  not not_123 (not_123_out, OP3);
  not not_124 (not_124_out, OP2);
  not not_125 (not_125_out, OP1);
  not not_126 (not_126_out, OP0);
  not not_127 (not_127_out, F4);
  not not_128 (not_128_out, F3);
  not not_129 (not_129_out, OP5);
  not not_130 (not_130_out, OP4);
  not not_131 (not_131_out, OP3);
  not not_132 (not_132_out, OP2);
  not not_133 (not_133_out, OP1);
  not not_134 (not_134_out, OP0);
  not not_135 (not_135_out, F4);
  not not_136 (not_136_out, F2);
  not not_137 (not_137_out, F0);
  not not_138 (not_138_out, OP5);
  not not_139 (not_139_out, OP4);
  not not_140 (not_140_out, OP3);
  not not_141 (not_141_out, OP1);
  not not_142 (not_142_out, OP0);
  not not_143 (not_143_out, OP5);
  not not_144 (not_144_out, OP4);
  not not_145 (not_145_out, OP3);
  not not_146 (not_146_out, OP1);
  not not_147 (not_147_out, OP5);
  not not_148 (not_148_out, OP4);
  not not_149 (not_149_out, OP1);
  not not_150 (not_150_out, OP0);
  not not_151 (not_151_out, OP5);
  not not_152 (not_152_out, OP4);
  not not_153 (not_153_out, OP2);
  not not_154 (not_154_out, OP0);
  not not_155 (not_155_out, OP5);
  not not_156 (not_156_out, OP4);
  not not_157 (not_157_out, OP3);
  not not_158 (not_158_out, OP0);
  not not_159 (not_159_out, OP1);
  not not_160 (not_160_out, OP2);
  not not_161 (not_161_out, OP3);
  not not_162 (not_162_out, OP4);
  not not_163 (not_163_out, F0);
  not not_164 (not_164_out, F1);
  not not_165 (not_165_out, F3);
  not not_166 (not_166_out, F4);
  not not_167 (not_167_out, OP0);
  not not_168 (not_168_out, OP1);
  not not_169 (not_169_out, OP2);
  not not_170 (not_170_out, OP3);
  not not_171 (not_171_out, OP4);
  not not_172 (not_172_out, F0);
  not not_173 (not_173_out, F2);
  not not_174 (not_174_out, F3);
  not not_175 (not_175_out, F4);
  not not_176 (not_176_out, OP0);
  not not_177 (not_177_out, OP1);
  not not_178 (not_178_out, OP2);
  not not_179 (not_179_out, OP3);
  not not_180 (not_180_out, OP4);
  not not_181 (not_181_out, F1);
  not not_182 (not_182_out, F2);
  not not_183 (not_183_out, F3);
  not not_184 (not_184_out, F4);
  not not_185 (not_185_out, OP0);
  not not_186 (not_186_out, OP1);
  not not_187 (not_187_out, OP2);
  not not_188 (not_188_out, OP3);
  not not_189 (not_189_out, OP4);
  not not_190 (not_190_out, F2);
  not not_191 (not_191_out, F4);
  not not_192 (not_192_out, OP0);
  not not_193 (not_193_out, OP1);
  not not_194 (not_194_out, OP2);
  not not_195 (not_195_out, OP3);
  not not_196 (not_196_out, OP4);
  not not_197 (not_197_out, OP0);
  not not_198 (not_198_out, OP1);
  not not_199 (not_199_out, OP4);
  not not_200 (not_200_out, OP5);
  not not_201 (not_201_out, OP2);
  not not_202 (not_202_out, OP4);
  not not_203 (not_203_out, OP5);
  not not_204 (not_204_out, OP2);
  not not_205 (not_205_out, OP4);
  not not_206 (not_206_out, OP0);
  not not_207 (not_207_out, OP1);
  not not_208 (not_208_out, OP3);
  not not_209 (not_209_out, OP4);
  not not_210 (not_210_out, OP5);
  not not_211 (not_211_out, F2);
  not not_212 (not_212_out, F4);
  not not_213 (not_213_out, OP0);
  not not_214 (not_214_out, OP1);
  not not_215 (not_215_out, OP3);
  not not_216 (not_216_out, OP4);
  not not_217 (not_217_out, OP5);
  not not_218 (not_218_out, F3);
  not not_219 (not_219_out, F4);
  not not_220 (not_220_out, OP1);
  not not_221 (not_221_out, OP3);
  not not_222 (not_222_out, OP4);
  not not_223 (not_223_out, OP5);
  not not_224 (not_224_out, OP2);
  not not_225 (not_225_out, OP4);
  not not_226 (not_226_out, OP5);
  not not_227 (not_227_out, OP1);
  not not_228 (not_228_out, OP4);
  not not_229 (not_229_out, OP5);
  not not_230 (not_230_out, OP3);
  not not_231 (not_231_out, OP4);
  not not_232 (not_232_out, OP5);
  and and_1 (and_1_out, not_1_out, not_2_out, not_3_out, not_4_out, not_5_out, not_6_out, not_7_out, not_8_out, not_9_out, not_10_out, F1, F0);
  and and_2 (and_2_out, not_11_out, not_12_out, not_13_out, not_14_out, not_15_out, not_16_out, F5, not_17_out, not_18_out, not_19_out, not_20_out, not_21_out);
  and and_3 (and_3_out, not_22_out, not_23_out, not_24_out, not_25_out, not_26_out, not_27_out, F5, not_28_out, not_29_out, not_30_out, not_31_out, F0);
  and and_4 (and_4_out, not_32_out, not_33_out, not_34_out, not_35_out, not_36_out, not_37_out, F5, not_38_out, not_39_out, F2, not_40_out, not_41_out);
  and and_5 (and_5_out, not_42_out, not_43_out, not_44_out, not_45_out, not_46_out, not_47_out, F5, not_48_out, F3, not_49_out, F1, not_50_out);
  and and_6 (and_6_out, not_51_out, not_52_out, not_53_out, OP2, not_54_out, not_55_out);
  and and_7 (and_7_out, not_56_out, not_57_out, not_58_out, OP2, not_59_out, OP0);
  and and_8 (and_8_out, not_60_out, not_61_out, OP3, not_62_out, not_63_out, not_64_out);
  and and_9 (and_9_out, not_65_out, not_66_out, OP3, OP2, not_67_out, not_68_out);
  and and_10 (and_10_out, not_69_out, not_70_out, OP3, not_71_out, not_72_out, OP0);
  and and_11 (and_11_out, not_73_out, not_74_out, OP3, not_75_out, OP1, not_76_out);
  and and_12 (and_12_out, OP5, not_77_out, not_78_out, not_79_out, OP1, OP0);
  and and_13 (and_13_out, OP5, not_80_out, OP3, not_81_out, OP1, OP0);
  and and_14 (and_14_out, OP5, not_82_out, not_83_out, not_84_out, not_85_out, not_86_out);
  and and_15 (and_15_out, not_87_out, not_88_out, not_89_out, OP2, OP1, OP0);
  and and_16 (and_16_out, not_90_out, not_91_out, not_92_out, not_93_out, not_94_out, not_95_out, not_96_out, not_97_out, not_98_out, not_99_out, F1, not_100_out);
  and and_17 (and_17_out, not_101_out, not_102_out, not_103_out, not_104_out, not_105_out, not_106_out, F5, not_107_out, not_108_out, not_109_out, F1, not_110_out);
  and and_18 (and_18_out, not_111_out, not_112_out, not_113_out, not_114_out, not_115_out, not_116_out, F5, not_117_out, not_118_out, F2, not_119_out, not_120_out);
  and and_19 (and_19_out, not_121_out, not_122_out, not_123_out, not_124_out, not_125_out, not_126_out, F5, not_127_out, not_128_out, F2, F1, F0);
  and and_20 (and_20_out, not_129_out, not_130_out, not_131_out, not_132_out, not_133_out, not_134_out, F5, not_135_out, F3, not_136_out, F1, not_137_out);
  and and_21 (and_21_out, not_138_out, not_139_out, not_140_out, OP2, not_141_out, not_142_out);
  and and_22 (and_22_out, not_143_out, not_144_out, not_145_out, OP2, not_146_out, OP0);
  and and_23 (and_23_out, not_147_out, not_148_out, OP3, OP2, not_149_out, not_150_out);
  and and_24 (and_24_out, not_151_out, not_152_out, OP3, not_153_out, OP1, not_154_out);
  and and_25 (and_25_out, not_155_out, not_156_out, not_157_out, OP2, OP1, OP0);
  and and_26 (and_26_out, not_158_out, not_159_out, not_160_out, not_161_out, not_162_out, not_163_out, not_164_out, not_165_out, not_166_out, F5);
  and and_27 (and_27_out, not_167_out, not_168_out, not_169_out, not_170_out, not_171_out, not_172_out, not_173_out, not_174_out, not_175_out, F5);
  and and_28 (and_28_out, not_176_out, not_177_out, not_178_out, not_179_out, not_180_out, not_181_out, not_182_out, not_183_out, not_184_out, F5);
  and and_29 (and_29_out, not_185_out, not_186_out, not_187_out, not_188_out, not_189_out, F0, F1, not_190_out, F3, not_191_out, F5);
  and and_30 (and_30_out, not_192_out, not_193_out, not_194_out, not_195_out, not_196_out, OP5);
  and and_31 (and_31_out, not_197_out, not_198_out, OP3, not_199_out, not_200_out);
  and and_32 (and_32_out, OP0, not_201_out, OP3, not_202_out, not_203_out);
  and and_33 (and_33_out, OP0, OP1, not_204_out, not_205_out, OP5);
  and and_34 (and_34_out, not_206_out, not_207_out, not_208_out, not_209_out, not_210_out, F1, not_211_out, F3, not_212_out, F5);
  and and_35 (and_35_out, not_213_out, not_214_out, not_215_out, not_216_out, not_217_out, F0, F2, not_218_out, not_219_out, F5);
  and and_36 (and_36_out, not_220_out, OP2, not_221_out, not_222_out, not_223_out);
  and and_37 (and_37_out, OP1, not_224_out, OP3, not_225_out, not_226_out);
  and and_38 (and_38_out, OP0, not_227_out, OP2, not_228_out, not_229_out);
  and and_39 (and_39_out, OP0, OP2, not_230_out, not_231_out, not_232_out);
  or or_1 (S1, and_16_out, and_17_out, and_18_out, and_19_out, and_20_out, and_21_out, and_22_out, and_23_out, and_24_out, and_25_out);
  or or_2 (S2, and_26_out, and_27_out, and_28_out, and_29_out, and_30_out, and_31_out, and_32_out, and_33_out);
  or or_3 (S3, and_34_out, and_35_out, and_36_out, and_37_out, and_38_out, and_39_out);
  or or_4 (S0, and_1_out, and_2_out, and_3_out, and_4_out, and_5_out, and_6_out, and_7_out, and_8_out, and_9_out, and_10_out, and_11_out, and_12_out, and_13_out, and_14_out, and_15_out);
endmodule

// 控制信号生成
module \控制信号自动生成  (
  input  OP0,
  input  OP1,
  input  OP2,
  input  OP3,
  input  OP4,
  input  OP5,
  input  F0,
  input  F1,
  input  F2,
  input  F3,
  input  F4,
  input  F5,
  output MemToReg,
  output MemWrite,
  output ALU_SRC,
  output RegWrite,
  output SysCALL,
  output SignedExt,
  output RegDst,
  output BEQ,
  output BNE,
  output JR,
  output JUMP,
  output JAL,
  output LUI,
  output LB,
  output BGTZ,
  output ERET
);

  wire and_1_out, and_2_out, and_4_out, and_5_out, and_6_out, and_7_out, and_8_out, and_9_out, and_10_out,
       and_11_out, and_12_out, and_13_out, and_14_out, and_15_out, and_16_out, and_17_out, and_18_out,
       and_20_out, and_21_out, and_22_out, and_23_out, and_24_out, and_25_out, and_26_out, and_27_out,
       and_28_out, and_29_out, and_33_out, and_34_out, not_1_out, not_2_out, not_3_out, not_4_out, not_5_out,
       not_6_out, not_7_out, not_8_out, not_9_out, not_10_out, not_11_out, not_12_out, not_13_out,
       not_14_out, not_15_out, not_16_out, not_17_out, not_18_out, not_19_out, not_20_out, not_21_out,
       not_22_out, not_23_out, not_24_out, not_25_out, not_26_out, not_27_out, not_28_out, not_29_out,
       not_30_out, not_31_out, not_32_out, not_33_out, not_34_out, not_35_out, not_36_out, not_37_out,
       not_38_out, not_39_out, not_40_out, not_41_out, not_42_out, not_43_out, not_44_out, not_45_out,
       not_46_out, not_47_out, not_48_out, not_49_out, not_50_out, not_51_out, not_52_out, not_53_out,
       not_54_out, not_55_out, not_56_out, not_57_out, not_58_out, not_59_out, not_60_out, not_61_out,
       not_62_out, not_63_out, not_64_out, not_65_out, not_66_out, not_67_out, not_68_out, not_69_out,
       not_70_out, not_71_out, not_72_out, not_73_out, not_74_out, not_75_out, not_76_out, not_77_out,
       not_78_out, not_79_out, not_80_out, not_81_out, not_82_out, not_83_out, not_84_out, not_85_out,
       not_86_out, not_87_out, not_88_out, not_89_out, not_90_out, not_91_out, not_92_out, not_93_out,
       not_94_out, not_95_out, not_96_out, not_97_out, not_98_out, not_99_out, not_100_out, not_101_out,
       not_102_out, not_103_out, not_104_out, not_105_out, not_106_out, not_107_out, not_108_out,
       not_109_out, not_110_out, not_111_out, not_112_out, not_113_out, not_114_out, not_115_out,
       not_116_out, not_117_out, not_118_out, not_119_out, not_120_out, not_121_out, not_122_out,
       not_123_out, not_124_out, not_125_out, not_126_out, not_127_out, not_128_out, not_129_out,
       not_130_out, not_131_out, not_132_out, not_133_out, not_134_out, not_135_out, not_136_out,
       not_137_out, not_138_out, not_139_out, not_140_out, not_141_out, not_142_out, not_143_out,
       not_144_out, not_145_out, not_146_out, not_147_out, not_148_out, not_149_out, not_150_out,
       not_151_out, not_152_out, not_153_out, not_154_out, not_155_out, not_156_out, not_157_out,
       not_158_out, not_159_out, not_160_out, not_161_out, not_162_out, not_163_out, not_164_out,
       not_165_out, not_166_out, not_167_out, not_168_out, not_169_out, not_170_out, not_171_out,
       not_172_out, not_173_out, not_174_out, not_175_out, not_176_out, not_177_out, not_178_out,
       not_179_out, not_180_out, not_181_out, not_182_out, not_183_out, not_184_out, not_185_out,
       not_186_out, not_187_out, not_188_out, not_189_out, not_190_out, not_191_out, not_192_out,
       not_193_out, not_194_out, not_195_out, not_196_out, not_197_out, not_198_out, not_199_out,
       not_200_out, not_201_out, not_202_out, not_203_out, not_204_out, not_205_out, not_206_out,
       not_207_out, not_208_out, not_209_out;

  not not_1 (not_1_out, OP0);
  not not_2 (not_2_out, OP1);
  not not_3 (not_3_out, OP2);
  not not_4 (not_4_out, OP3);
  not not_5 (not_5_out, OP4);
  not not_6 (not_6_out, OP2);
  not not_7 (not_7_out, OP3);
  not not_8 (not_8_out, OP4);
  not not_9 (not_9_out, OP2);
  not not_10 (not_10_out, OP4);
  not not_11 (not_11_out, OP0);
  not not_12 (not_12_out, OP1);
  not not_13 (not_13_out, OP2);
  not not_14 (not_14_out, OP3);
  not not_15 (not_15_out, OP4);
  not not_16 (not_16_out, OP1);
  not not_17 (not_17_out, OP4);
  not not_18 (not_18_out, OP5);
  not not_19 (not_19_out, OP2);
  not not_20 (not_20_out, OP4);
  not not_21 (not_21_out, OP5);
  not not_22 (not_22_out, OP4);
  not not_23 (not_23_out, OP5);
  not not_24 (not_24_out, OP2);
  not not_25 (not_25_out, OP4);
  not not_26 (not_26_out, OP0);
  not not_27 (not_27_out, OP1);
  not not_28 (not_28_out, OP2);
  not not_29 (not_29_out, OP3);
  not not_30 (not_30_out, OP4);
  not not_31 (not_31_out, F0);
  not not_32 (not_32_out, F2);
  not not_33 (not_33_out, F3);
  not not_34 (not_34_out, F4);
  not not_35 (not_35_out, OP0);
  not not_36 (not_36_out, OP1);
  not not_37 (not_37_out, OP2);
  not not_38 (not_38_out, OP3);
  not not_39 (not_39_out, OP4);
  not not_40 (not_40_out, F1);
  not not_41 (not_41_out, F3);
  not not_42 (not_42_out, F4);
  not not_43 (not_43_out, OP0);
  not not_44 (not_44_out, OP1);
  not not_45 (not_45_out, OP2);
  not not_46 (not_46_out, OP3);
  not not_47 (not_47_out, OP4);
  not not_48 (not_48_out, F2);
  not not_49 (not_49_out, F3);
  not not_50 (not_50_out, F4);
  not not_51 (not_51_out, F5);
  not not_52 (not_52_out, OP0);
  not not_53 (not_53_out, OP1);
  not not_54 (not_54_out, OP2);
  not not_55 (not_55_out, OP3);
  not not_56 (not_56_out, OP4);
  not not_57 (not_57_out, F2);
  not not_58 (not_58_out, F4);
  not not_59 (not_59_out, OP0);
  not not_60 (not_60_out, OP1);
  not not_61 (not_61_out, OP2);
  not not_62 (not_62_out, OP3);
  not not_63 (not_63_out, OP4);
  not not_64 (not_64_out, F3);
  not not_65 (not_65_out, F4);
  not not_66 (not_66_out, OP0);
  not not_67 (not_67_out, OP1);
  not not_68 (not_68_out, OP2);
  not not_69 (not_69_out, OP3);
  not not_70 (not_70_out, OP4);
  not not_71 (not_71_out, OP1);
  not not_72 (not_72_out, OP4);
  not not_73 (not_73_out, OP5);
  not not_74 (not_74_out, OP2);
  not not_75 (not_75_out, OP4);
  not not_76 (not_76_out, OP5);
  not not_77 (not_77_out, OP4);
  not not_78 (not_78_out, OP5);
  not not_79 (not_79_out, OP2);
  not not_80 (not_80_out, OP3);
  not not_81 (not_81_out, OP4);
  not not_82 (not_82_out, OP0);
  not not_83 (not_83_out, OP1);
  not not_84 (not_84_out, OP2);
  not not_85 (not_85_out, OP3);
  not not_86 (not_86_out, OP4);
  not not_87 (not_87_out, OP5);
  not not_88 (not_88_out, F0);
  not not_89 (not_89_out, F1);
  not not_90 (not_90_out, F4);
  not not_91 (not_91_out, F5);
  not not_92 (not_92_out, OP0);
  not not_93 (not_93_out, OP1);
  not not_94 (not_94_out, OP2);
  not not_95 (not_95_out, OP3);
  not not_96 (not_96_out, OP4);
  not not_97 (not_97_out, OP2);
  not not_98 (not_98_out, OP4);
  not not_99 (not_99_out, OP5);
  not not_100 (not_100_out, OP1);
  not not_101 (not_101_out, OP3);
  not not_102 (not_102_out, OP4);
  not not_103 (not_103_out, OP5);
  not not_104 (not_104_out, OP2);
  not not_105 (not_105_out, OP4);
  not not_106 (not_106_out, OP4);
  not not_107 (not_107_out, OP5);
  not not_108 (not_108_out, OP0);
  not not_109 (not_109_out, OP1);
  not not_110 (not_110_out, OP2);
  not not_111 (not_111_out, OP3);
  not not_112 (not_112_out, OP4);
  not not_113 (not_113_out, OP5);
  not not_114 (not_114_out, F0);
  not not_115 (not_115_out, F2);
  not not_116 (not_116_out, F3);
  not not_117 (not_117_out, F4);
  not not_118 (not_118_out, OP0);
  not not_119 (not_119_out, OP1);
  not not_120 (not_120_out, OP2);
  not not_121 (not_121_out, OP3);
  not not_122 (not_122_out, OP4);
  not not_123 (not_123_out, OP5);
  not not_124 (not_124_out, F1);
  not not_125 (not_125_out, F3);
  not not_126 (not_126_out, F4);
  not not_127 (not_127_out, OP0);
  not not_128 (not_128_out, OP1);
  not not_129 (not_129_out, OP2);
  not not_130 (not_130_out, OP3);
  not not_131 (not_131_out, OP4);
  not not_132 (not_132_out, OP5);
  not not_133 (not_133_out, F2);
  not not_134 (not_134_out, F3);
  not not_135 (not_135_out, F4);
  not not_136 (not_136_out, F5);
  not not_137 (not_137_out, OP0);
  not not_138 (not_138_out, OP1);
  not not_139 (not_139_out, OP2);
  not not_140 (not_140_out, OP3);
  not not_141 (not_141_out, OP4);
  not not_142 (not_142_out, OP5);
  not not_143 (not_143_out, F2);
  not not_144 (not_144_out, F4);
  not not_145 (not_145_out, OP0);
  not not_146 (not_146_out, OP1);
  not not_147 (not_147_out, OP2);
  not not_148 (not_148_out, OP3);
  not not_149 (not_149_out, OP4);
  not not_150 (not_150_out, OP5);
  not not_151 (not_151_out, F3);
  not not_152 (not_152_out, F4);
  not not_153 (not_153_out, OP0);
  not not_154 (not_154_out, OP1);
  not not_155 (not_155_out, OP3);
  not not_156 (not_156_out, OP4);
  not not_157 (not_157_out, OP5);
  not not_158 (not_158_out, OP1);
  not not_159 (not_159_out, OP3);
  not not_160 (not_160_out, OP4);
  not not_161 (not_161_out, OP5);
  not not_162 (not_162_out, OP0);
  not not_163 (not_163_out, OP1);
  not not_164 (not_164_out, OP2);
  not not_165 (not_165_out, OP3);
  not not_166 (not_166_out, OP4);
  not not_167 (not_167_out, OP5);
  not not_168 (not_168_out, F0);
  not not_169 (not_169_out, F1);
  not not_170 (not_170_out, F2);
  not not_171 (not_171_out, F4);
  not not_172 (not_172_out, F5);
  not not_173 (not_173_out, OP0);
  not not_174 (not_174_out, OP2);
  not not_175 (not_175_out, OP3);
  not not_176 (not_176_out, OP4);
  not not_177 (not_177_out, OP5);
  not not_178 (not_178_out, F0);
  not not_179 (not_179_out, F1);
  not not_180 (not_180_out, F2);
  not not_181 (not_181_out, F4);
  not not_182 (not_182_out, F5);
  not not_183 (not_183_out, OP2);
  not not_184 (not_184_out, OP3);
  not not_185 (not_185_out, OP4);
  not not_186 (not_186_out, OP5);
  not not_187 (not_187_out, OP2);
  not not_188 (not_188_out, OP3);
  not not_189 (not_189_out, OP4);
  not not_190 (not_190_out, OP5);
  not not_191 (not_191_out, OP4);
  not not_192 (not_192_out, OP5);
  not not_193 (not_193_out, OP0);
  not not_194 (not_194_out, OP1);
  not not_195 (not_195_out, OP2);
  not not_196 (not_196_out, OP3);
  not not_197 (not_197_out, OP4);
  not not_198 (not_198_out, OP3);
  not not_199 (not_199_out, OP4);
  not not_200 (not_200_out, OP5);
  not not_201 (not_201_out, OP5);
  not not_202 (not_202_out, OP3);
  not not_203 (not_203_out, OP2);
  not not_204 (not_204_out, OP1);
  not not_205 (not_205_out, OP0);
  not not_206 (not_206_out, F5);
  not not_207 (not_207_out, F2);
  not not_208 (not_208_out, F1);
  not not_209 (not_209_out, F0);
  and and_1 (and_1_out, not_1_out, not_2_out, not_3_out, not_4_out, not_5_out, OP5);
  and and_2 (and_2_out, OP0, OP1, not_6_out, not_7_out, not_8_out, OP5);
  and and_3 (MemWrite, OP0, OP1, not_9_out, OP3, not_10_out, OP5);
  and and_4 (and_4_out, not_11_out, not_12_out, not_13_out, not_14_out, not_15_out, OP5);
  and and_5 (and_5_out, not_16_out, OP3, not_17_out, not_18_out);
  and and_6 (and_6_out, not_19_out, OP3, not_20_out, not_21_out);
  and and_7 (and_7_out, OP0, OP3, not_22_out, not_23_out);
  and and_8 (and_8_out, OP0, OP1, not_24_out, not_25_out, OP5);
  and and_9 (and_9_out, not_26_out, not_27_out, not_28_out, not_29_out, not_30_out, not_31_out, not_32_out, not_33_out, not_34_out);
  and and_10 (and_10_out, not_35_out, not_36_out, not_37_out, not_38_out, not_39_out, not_40_out, not_41_out, not_42_out, F5);
  and and_11 (and_11_out, not_43_out, not_44_out, not_45_out, not_46_out, not_47_out, F1, not_48_out, not_49_out, not_50_out, not_51_out);
  and and_12 (and_12_out, not_52_out, not_53_out, not_54_out, not_55_out, not_56_out, F1, not_57_out, F3, not_58_out, F5);
  and and_13 (and_13_out, not_59_out, not_60_out, not_61_out, not_62_out, not_63_out, F0, F2, not_64_out, not_65_out, F5);
  and and_14 (and_14_out, not_66_out, not_67_out, not_68_out, not_69_out, not_70_out, OP5);
  and and_15 (and_15_out, not_71_out, OP3, not_72_out, not_73_out);
  and and_16 (and_16_out, not_74_out, OP3, not_75_out, not_76_out);
  and and_17 (and_17_out, OP0, OP3, not_77_out, not_78_out);
  and and_18 (and_18_out, OP0, OP1, not_79_out, not_80_out, not_81_out);
  and and_19 (SysCALL, not_82_out, not_83_out, not_84_out, not_85_out, not_86_out, not_87_out, not_88_out, not_89_out, F2, F3, not_90_out, not_91_out);
  and and_20 (and_20_out, not_92_out, not_93_out, not_94_out, not_95_out, not_96_out, OP5);
  and and_21 (and_21_out, not_97_out, OP3, not_98_out, not_99_out);
  and and_22 (and_22_out, not_100_out, OP2, not_101_out, not_102_out, not_103_out);
  and and_23 (and_23_out, OP0, OP1, not_104_out, not_105_out, OP5);
  and and_24 (and_24_out, OP0, OP1, OP2, not_106_out, not_107_out);
  and and_25 (and_25_out, not_108_out, not_109_out, not_110_out, not_111_out, not_112_out, not_113_out, not_114_out, not_115_out, not_116_out, not_117_out);
  and and_26 (and_26_out, not_118_out, not_119_out, not_120_out, not_121_out, not_122_out, not_123_out, not_124_out, not_125_out, not_126_out, F5);
  and and_27 (and_27_out, not_127_out, not_128_out, not_129_out, not_130_out, not_131_out, not_132_out, F1, not_133_out, not_134_out, not_135_out, not_136_out);
  and and_28 (and_28_out, not_137_out, not_138_out, not_139_out, not_140_out, not_141_out, not_142_out, F1, not_143_out, F3, not_144_out, F5);
  and and_29 (and_29_out, not_145_out, not_146_out, not_147_out, not_148_out, not_149_out, not_150_out, F0, F2, not_151_out, not_152_out, F5);
  and and_30 (BEQ, not_153_out, not_154_out, OP2, not_155_out, not_156_out, not_157_out);
  and and_31 (BNE, OP0, not_158_out, OP2, not_159_out, not_160_out, not_161_out);
  and and_32 (JR, not_162_out, not_163_out, not_164_out, not_165_out, not_166_out, not_167_out, not_168_out, not_169_out, not_170_out, F3, not_171_out, not_172_out);
  and and_33 (and_33_out, not_173_out, not_174_out, not_175_out, not_176_out, not_177_out, not_178_out, not_179_out, not_180_out, F3, not_181_out, not_182_out);
  and and_34 (and_34_out, OP1, not_183_out, not_184_out, not_185_out, not_186_out);
  and and_35 (JAL, OP0, OP1, not_187_out, not_188_out, not_189_out, not_190_out);
  and and_36 (LUI, OP0, OP1, OP2, OP3, not_191_out, not_192_out);
  and and_37 (LB, not_193_out, not_194_out, not_195_out, not_196_out, not_197_out, OP5);
  and and_38 (BGTZ, OP0, OP1, OP2, not_198_out, not_199_out, not_200_out);
  and and_39 (ERET, not_201_out, OP4, not_202_out, not_203_out, not_204_out, not_205_out, not_206_out, F4, F3, not_207_out, not_208_out, not_209_out);
  or or_1 (MemToReg, and_1_out, and_2_out);
  or or_2 (ALU_SRC, and_4_out, and_5_out, and_6_out, and_7_out, and_8_out);
  or or_3 (RegWrite, and_9_out, and_10_out, and_11_out, and_12_out, and_13_out, and_14_out, and_15_out, and_16_out, and_17_out, and_18_out);
  or or_4 (SignedExt, and_20_out, and_21_out, and_22_out, and_23_out, and_24_out);
  or or_5 (RegDst, and_25_out, and_26_out, and_27_out, and_28_out, and_29_out);
  or or_6 (JUMP, and_33_out, and_34_out);
endmodule

// ALU
module MIPS_ALU (
  input  [4:0] shamt,
  input  [31:0] X,
  input  [31:0] Y,
  input  [3:0] AluOP,
  output Equal,
  output [31:0] Result,
  output [31:0] Result_2
);

  wire [0:0] comparator_1_lt, comparator_2_lt;
  wire [31:0] adder_1_out, AND_out, divider_1_out, divider_1_rem, multiplier_1_cout, multiplier_1_out,
       NOR_out, OR_out, shifter_1_out, shifter_2_out, shifter_3_out, subtractor_1_out, XOR_out;

  assign AND_out = X & Y;  // AND_Gate AND, 32 bits wide
  assign OR_out = X | Y;  // OR_Gate OR, 32 bits wide
  Shifter #(.width(32), .shift("ll")) shifter_1 (.in(Y), .\dist (shamt), .out(shifter_1_out));
  Shifter #(.width(32), .shift("ar")) shifter_2 (.in(Y), .\dist (shamt), .out(shifter_2_out));
  Shifter #(.width(32), .shift("lr")) shifter_3 (.in(Y), .\dist (shamt), .out(shifter_3_out));
  Multiplier #(.width(32)) multiplier_1 (.a(X), .b(Y), .out(multiplier_1_out), .cout(multiplier_1_cout));  // open: cin
  Divider #(.width(32)) divider_1 (.a(X), .b(Y), .out(divider_1_out), .rem(divider_1_rem));  // open: upper
  Adder #(.width(32)) adder_1 (.a(X), .b(Y), .out(adder_1_out));  // open: cin, cout
  Subtractor #(.width(32)) subtractor_1 (.a(X), .b(Y), .out(subtractor_1_out));  // open: bin, bout
  assign XOR_out = X ^ Y;  // XOR_Gate XOR, 32 bits wide
  assign NOR_out = ~(X | Y);  // NOR_Gate NOR, 32 bits wide
  Comparator #(.width(32), .mode("twosComplement")) comparator_1 (
    .a(X), .b(Y), .eq(Equal), .lt(comparator_1_lt[0]));  // open: gt
  Comparator #(.width(32), .mode("unsigned")) comparator_2 (.a(X), .b(Y), .lt(comparator_2_lt[0]));  // open: gt, eq
  Multiplexer #(.select(4), .width(32), .disabled("Z"), .enable("false")) multiplexer_1 (
    .in0(shifter_1_out), .in1(shifter_2_out), .in2(shifter_3_out), .in3(multiplier_1_out),
    .in4(divider_1_out), .in5(adder_1_out), .in6(subtractor_1_out), .in7(AND_out), .in8(OR_out),
    .in9(XOR_out), .in10(NOR_out), .in11({{31{1'b0}}, comparator_1_lt[0]}),
    .in12({{31{1'b0}}, comparator_2_lt[0]}), .in13({32{1'b0}}), .in14({32{1'b0}}), .in15({32{1'b0}}),
    .out(Result), .sel(AluOP));
  Multiplexer #(.select(4), .width(32), .disabled("Z"), .enable("false")) multiplexer_2 (
    .in0({32{1'b0}}), .in1({32{1'b0}}), .in2({32{1'b0}}), .in3(multiplier_1_cout), .in4(divider_1_rem),
    .in5({32{1'b0}}), .in6({32{1'b0}}), .in7({32{1'b0}}), .in8({32{1'b0}}), .in9({32{1'b0}}),
    .in10({32{1'b0}}), .in11({32{1'b0}}), .in12({32{1'b0}}), .in13({32{1'b0}}), .in14({32{1'b0}}),
    .in15({32{1'b0}}), .out(Result_2), .sel(AluOP));

  // Other names for the same wires on the sheet: Result2[31:0] = Result_2; S[3:0] = AluOP

  // Notes on the sheet:
  //   不要改变此引脚区域内容，也不要改变ALU封装形式
  //   输入引脚
  //   输出引脚
endmodule

module MIPS_Regifile (
  input  [31:0] Din,
  input  Clk,
  input  WE,
  input  [4:0] R1_num,
  input  [4:0] W_num,
  input  [4:0] R2_num,
  output [31:0] R1,
  output [31:0] R2
);

  // RegisterFile registerfile_1: pin names not known; wires that end beside it: Din, Clk, WE, W_num, R1_num, R2_num, R1, R2
endmodule

module \理想流水线  (
  output RegWrite,
  output MemWrite,
  output [31:0] IF_PC,
  output [31:0] ID_PC,
  output [31:0] EX_PC,
  output [31:0] M_PC,
  output [31:0] WB_PC,
  output [31:0] RDin,
  output [31:0] MDin,
  output [31:0] LedData
);

  wire and_1_out, and_2_out, and_3_out, CLK, clock_1_out, clock_2_out, comparator_1_eq, comparator_1_lt,
       d_ff_1_q, equal, ex_mem_1_memtorego, ex_mem_1_regwriteo, Go, ID_EX_alu_srco, ID_EX_beqo, ID_EX_jro,
       ID_EX_memtorego, ID_EX_memwriteo, ID_EX_regwriteo, IR1, IR2, IR3, mem_wb_1_memtorego, nand_1_out,
       not_1_out, not_2_out, or_1_out, RST, SignedExt, Syscall, W1, W2, W3, \单周期硬布线控制器_1_alu_src ,
       \单周期硬布线控制器_1_beq , \单周期硬布线控制器_1_bne , \单周期硬布线控制器_1_jal , \单周期硬布线控制器_1_memtoreg ,
       \单周期硬布线控制器_1_memwrite , \单周期硬布线控制器_1_regdst , \单周期硬布线控制器_1_regwrite ;
  wire [1:0] \单周期硬布线控制器_1_jr ;
  wire [3:0] ID_EX_alu_opo, \单周期硬布线控制器_1_alu_op ;
  wire [4:0] ex_mem_1_wdino, ID_EX_shamti_2, ID_EX_wdino, multiplexer_4_out, multiplexer_5_out,
       multiplexer_6_out, multiplexer_8_out, W_num;
  wire [7:0] undriven_2, undriven_3, undriven_4;
  wire [12:0] CNT_num;
  wire [15:0] \LoadUse次数 , \总周期数 , \插入气泡数 , \无条件分支数 , \条件分支成功数 ;
  wire [27:0] if_id_1_pc_4o;
  wire [31:0] adder_1_out, adder_2_out, bit_extender_1_out, bit_extender_2_out, EX_IR, ex_mem_1_alu_ro,
       ID_EX_imextendo, ID_IR, IF_IR, IR, MEM_IR, mem_wb_1_alu_ro, mem_wb_1_memrdo, mips_alu_1_result,
       mips_regifile_1_r1, mips_regifile_1_r2, multiplexer_1_out, multiplexer_2_out, multiplexer_7_out,
       multiplexer_10_out, multiplexer_11_out, R1, R2, ram_1_data, rom_1_data, shifter_1_out, WB_IR;
  wire [31:2] undriven;

  Button \u_总复位  (.out(RST));
  Button _1 (.out(IR1));
  Button _2 (.out(IR2));
  Button _3 (.out(IR3));
  // Probe on \总周期数 
  // Probe on \总周期数 
  Button \u_继续运行  (.out(Go));
  LED #(.active("true")) led_1 (.in(W1));
  LED #(.active("true")) led_2 (.in(W2));
  LED #(.active("true")) led_3 (.in(W3));
  Button button_1 (.out(RST));
  or or_1 (or_1_out, and_2_out, and_3_out);
  Multiplexer #(.select(1), .width(32), .disabled("Z"), .enable("false")) multiplexer_1 (
    .in0(adder_1_out), .in1(adder_2_out), .out(multiplexer_1_out), .sel(or_1_out));
  Hex_Digit_Display hex_digit_display_1 (.value(LedData[31:28]));  // open: dp
  // Probe on IF_PC[19:0]
  // Mips_Probe mips_probe_1: pin names not known; wires that end beside it: IF_IR
  Hex_Digit_Display hex_digit_display_2 (.value(LedData[23:20]));  // open: dp
  Hex_Digit_Display hex_digit_display_3 (.value(LedData[27:24]));  // open: dp
  // Probe on ID_PC[19:0]
  // Mips_Probe mips_probe_2: pin names not known; wires that end beside it: ID_IR
  Multiplexer #(.select(2), .width(32), .disabled("Z"), .enable("false")) multiplexer_2 (
    .in0(multiplexer_1_out), .in1(R1), .in2({undriven, 2'b00}), .in3(R1), .out(multiplexer_2_out),
    .sel(\单周期硬布线控制器_1_jr ));
  Register #(.width(32), .trigger("rising"), .Select("low")) PC (
    .D(multiplexer_2_out), .en(1'b1), .Q(IF_PC), .clk(CLK), .clr(RST));
  Multiplexer #(.select(1), .width(1), .disabled("Z"), .enable("false")) multiplexer_3 (
    .in1(Go), .sel(and_1_out));  // open: in0, out
  Hex_Digit_Display hex_digit_display_4 (.value(LedData[19:16]));  // open: dp
  Hex_Digit_Display hex_digit_display_5 (.value(LedData[15:12]));  // open: dp
  Register #(.width(16), .trigger("rising"), .Select("low")) register_1 (
    .en(1'b1), .Q(\总周期数 ), .clk(CLK), .clr(RST));  // open: D
  Hex_Digit_Display hex_digit_display_6 (.value(LedData[7:4]));  // open: dp
  Hex_Digit_Display hex_digit_display_7 (.value(LedData[11:8]));  // open: dp
  Clock #(.highDuration(1), .lowDuration(1)) clock_1 (.out(clock_1_out));
  // Probe on EX_PC[19:0]
  // Mips_Probe mips_probe_3: pin names not known; wires that end beside it: clock_1_out, EX_IR, CLK
  Adder #(.width(32)) adder_1 (.a(IF_PC), .b(32'h4), .out(adder_1_out));  // open: cin, cout
  Hex_Digit_Display hex_digit_display_8 (.value(LedData[3:0]));  // open: dp
  ROM #(.addrWidth(10), .dataWidth(32), .Select("high")) rom_1 (.addr(IF_PC[11:2]), .data(rom_1_data));
  and and_1 (and_1_out, Syscall, not_1_out);
  not not_1 (not_1_out, equal);
  // Probe on \总周期数 
  // Probe on M_PC[19:0]
  // Mips_Probe mips_probe_4: pin names not known; wires that end beside it: MEM_IR
  // Probe on \总周期数 
  // Probe on \无条件分支数 
  // Probe on \条件分支成功数 
  // Probe on \插入气泡数 
  // Probe on \LoadUse次数 
  IF_ID if_id_1 (
    .IRI(rom_1_data), .IRO(IR), .CLR(RST), .WE(1'b1), .CLK(CLK), .PC_4I(adder_1_out),
    .PC_4O({undriven[31:28], if_id_1_pc_4o}), .PPCI(IF_PC), .PPCO(ID_PC), .J(1'b0));
  // Probe on IF_PC[11:0]
  // Probe on WB_PC[19:0]
  // Mips_Probe mips_probe_5: pin names not known; wires that end beside it: WB_IR
  // Mips_Probe mips_probe_6: pin names not known; wires that end beside it: rom_1_data, adder_1_out, IR
  // Probe on EX_PC[11:0]
  // Probe on ID_PC[11:0]
  // Probe on M_PC[11:0]
  D_Flip_Flop #(.trigger("high"), .Pre_Clr_Positions("LEGACY"), .NegatePresetClear("false"), .enable("true"), .NewFFLayout("false")) d_ff_1 (.Q(d_ff_1_q));  // open: clk, D, Qn, preset, en, reset
  // Probe on 13'hc
  \单周期硬布线控制器  \u_单周期硬布线控制器_1  (
    .Func(IR[5:0]), .OP(IR[31:26]), .ALU_OP(\单周期硬布线控制器_1_alu_op ), .MemToReg(\单周期硬布线控制器_1_memtoreg ),
    .MemWrite(\单周期硬布线控制器_1_memwrite ), .ALU_SRC(\单周期硬布线控制器_1_alu_src ), .RegWrite(\单周期硬布线控制器_1_regwrite ),
    .SysCALL(Syscall), .SignedExt(SignedExt), .RegDst(\单周期硬布线控制器_1_regdst ), .JR(\单周期硬布线控制器_1_jr [0]),
    .JMP(\单周期硬布线控制器_1_jr [1]), .Beq(\单周期硬布线控制器_1_beq ), .JAL(\单周期硬布线控制器_1_jal ), .Bne(\单周期硬布线控制器_1_bne ));  // open: LUI, LB, BGTZ, ERET
  Multiplexer #(.select(1), .width(5), .disabled("Z"), .enable("false")) multiplexer_4 (
    .in0(IR[25:21]), .in1(5'b00010), .out(multiplexer_4_out), .sel(Syscall));
  Multiplexer #(.select(1), .width(5), .disabled("Z"), .enable("false")) multiplexer_5 (
    .in0(IR[20:16]), .in1(IR[15:11]), .out(multiplexer_5_out), .sel(\单周期硬布线控制器_1_regdst ));
  Multiplexer #(.select(1), .width(5), .disabled("Z"), .enable("false")) multiplexer_6 (
    .in0(multiplexer_5_out), .in1({5{1'b1}}), .out(multiplexer_6_out), .sel(\单周期硬布线控制器_1_jal ));
  assign bit_extender_1_out = {{16{1'b0}}, IR[15:0]};  // Bit_Extender bit_extender_1
  Multiplexer #(.select(1), .width(32), .disabled("Z"), .enable("false")) multiplexer_7 (
    .in0(bit_extender_1_out), .in1(bit_extender_2_out), .out(multiplexer_7_out), .sel(SignedExt));
  assign bit_extender_2_out = {{16{IR[15]}}, IR[15:0]};  // Bit_Extender bit_extender_2
  // Probe on WB_PC[11:0]
  Comparator #(.width(13), .mode("twosComplement")) comparator_1 (
    .a(CNT_num), .b(13'hc), .eq(comparator_1_eq), .lt(comparator_1_lt));  // open: gt
  Clock #(.highDuration(1), .lowDuration(1)) clock_2 (.out(clock_2_out));
  Multiplexer #(.select(1), .width(5), .disabled("Z"), .enable("false")) multiplexer_8 (
    .in0(IR[20:16]), .in1(5'b00100), .out(multiplexer_8_out), .sel(Syscall));
  Multiplexer #(.select(1), .width(32), .disabled("Z"), .enable("false")) multiplexer_9 (
    .in0(multiplexer_11_out), .in1({undriven[31:28], if_id_1_pc_4o}), .out(RDin), .sel(\单周期硬布线控制器_1_jal ));
  nand nand_1 (nand_1_out, d_ff_1_q, comparator_1_eq);
  Counter #(.width(13), .max('h1fff), .ongoal("stay"), .trigger("rising"), .behavior("old")) counter_1 (
    .count(comparator_1_lt), .Q(CNT_num), .clk(clock_2_out));  // open: load, D, carry, clr, preset
  Shifter #(.width(32), .shift("ll")) shifter_1 (.in(multiplexer_7_out), .\dist (5'b00010), .out(shifter_1_out));
  assign CLK = nand_1_out ? clock_2_out : 1'bz;  // Controlled_Buffer controlled_buffer_1
  MIPS_Regifile mips_regifile_1 (
    .Din(RDin), .Clk(CLK), .R1(mips_regifile_1_r1), .R2(mips_regifile_1_r2), .WE(RegWrite), .W_num(W_num),
    .R1_num(multiplexer_4_out), .R2_num(multiplexer_8_out));
  Adder #(.width(32)) adder_2 (
    .a(shifter_1_out), .b({undriven[31:28], if_id_1_pc_4o}), .out(adder_2_out));  // open: cin, cout
  Pull_Resistor #(.pull(1)) pull_resistor_1 (.node(CLK));
  ID_EX ID_EX (
    .R1I(mips_regifile_1_r1), .R2I(mips_regifile_1_r2), .R1O(R1), .R2O(R2), .CLR(RST), .WE(1'b1), .CLK(CLK),
    .ALU_SrcI(\单周期硬布线控制器_1_alu_src ), .ALU_SrcO(ID_EX_alu_srco), .ALU_OPO(ID_EX_alu_opo),
    .imExtendedI(multiplexer_7_out), .imExtendO(ID_EX_imextendo), .shamtI(IR[10:6]),
    .shamtI_2(ID_EX_shamti_2), .ALU_OPI(\单周期硬布线控制器_1_alu_op ), .MemToRegI(\单周期硬布线控制器_1_memtoreg ),
    .MemToRegO(ID_EX_memtorego), .MemWriteI(\单周期硬布线控制器_1_memwrite ), .MemWriteO(ID_EX_memwriteo),
    .RegWriteI(\单周期硬布线控制器_1_regwrite ), .RegWriteO(ID_EX_regwriteo), .WDinI(multiplexer_6_out),
    .WDinO(ID_EX_wdino), .BeqI(\单周期硬布线控制器_1_bne ), .BeqO(ID_EX_beqo), .PPCI(ID_PC), .PPCO(EX_PC),
    .JRI(\单周期硬布线控制器_1_beq ), .JRO(ID_EX_jro), .J(1'b0), .iiI(IR[25:0]));  // open: BneI, BneO, JI, JO, iiO, PC_4I, PC_4O, JalI, JalO, IRI, IRO, SyscallI, SyscallO, LUII, SyscallO_2, LBI, LBO, BGTZI, BGTZO, rtForwardI, rtForwardO, rsForwardI, rsForwardO
  Register #(.width(32), .trigger("rising"), .Select("low")) register_2 (
    .D(R2), .en(Syscall), .Q(LedData), .clk(CLK), .clr(RST));
  and and_2 (and_2_out, ID_EX_beqo, not_2_out);
  and and_3 (and_3_out, ID_EX_jro, equal);
  not not_2 (not_2_out, equal);
  Multiplexer #(.select(1), .width(32), .disabled("Z"), .enable("false")) multiplexer_10 (
    .in0(R2), .in1(ID_EX_imextendo), .out(multiplexer_10_out), .sel(ID_EX_alu_srco));
  MIPS_ALU mips_alu_1 (
    .X(R1), .Y(multiplexer_10_out), .AluOP(ID_EX_alu_opo), .Equal(equal), .Result(mips_alu_1_result),
    .shamt(ID_EX_shamti_2));  // open: Result_2
  EX_MEM ex_mem_1 (
    .ALU_RI(mips_alu_1_result), .WDRI(R2), .MemToRegI(ID_EX_memtorego), .MemWriteI(ID_EX_memwriteo),
    .ALU_RO(ex_mem_1_alu_ro), .WDRO(MDin), .MemToRegO(ex_mem_1_memtorego), .MemWriteO(MemWrite), .CLR(RST),
    .WE(1'b1), .CLK(CLK), .RegWriteI(ID_EX_regwriteo), .RegWriteO(ex_mem_1_regwriteo), .WDinI(ID_EX_wdino),
    .WDinO(ex_mem_1_wdino), .PPCI(EX_PC), .PPCO(M_PC));  // open: JalI, JalO, IRI, IRO, SyscallI, SyscallO, LBI, LBO, equalI, equalO
  RAM #(.addrWidth(10), .dataWidth(32), .bus("separate"), .Select("high")) ram_1 (
    .addr(ex_mem_1_alu_ro[11:2]), .din(MDin), .data(ram_1_data), .str(MemWrite), .clk(CLK), .clr(RST));  // open: sel, ld
  MEM_WB mem_wb_1 (
    .ALU_RI(ex_mem_1_alu_ro), .MemRDI(ram_1_data), .MemToRegI(ex_mem_1_memtorego), .ALU_RO(mem_wb_1_alu_ro),
    .MemRDO(mem_wb_1_memrdo), .MemToRegO(mem_wb_1_memtorego), .CLR(RST), .WE(1'b1), .CLK(CLK),
    .RegWriteI(ex_mem_1_regwriteo), .RegWriteO(RegWrite), .WDinI(ex_mem_1_wdino), .WDinO(W_num), .PPCI(M_PC),
    .PPCO(WB_PC));  // open: JalI, JalO, IRI, IRO, SyscallI, SyscallO, RI, RO, LBI, LBO, equalI, equalO
  Multiplexer #(.select(1), .width(32), .disabled("Z"), .enable("false")) multiplexer_11 (
    .in0(mem_wb_1_alu_ro), .in1(mem_wb_1_memrdo), .out(multiplexer_11_out), .sel(mem_wb_1_memtorego));
  Multiplexer #(.select(2), .width(8), .disabled("Z"), .enable("false")) multiplexer_12 (
    .in0(undriven_2), .in1(undriven_3), .in3(undriven_4), .sel(mem_wb_1_alu_ro[1:0]));  // open: in2, out

  // Other names for the same wires on the sheet: MEM_PC[31:0] = M_PC; PC[31:0] = IF_PC

  // Notes on the sheet:
  //   中断源
  //   时空图监测，可删除
  //   中断等待指示
  //   数码管输出
  //   指令存储器
  //   指令字
  //   contents of rom_1 (hex, n*v repeats v):
  //   20100000 20110000 20120000 20130000 36100000 36310001 36520002 36730003 ae100000 ae110004 ae120008
  //   ae13000c 2002000a 20110000 20120000 20130000 c
  //   OP
  //   rs
  //   rt
  //   rd
  //   im
  //   ii
  //   控制位
  //   Func
  //   流水调试日志用
  //   暂停节拍，不能为0
  //   JMP
  //   JR
  //   OP
  //   Func
  //   Syscall
  //   戳工具置1进入计数暂停模式，ctrl+k时钟自动运行到对应节拍暂停
  //   ctrl+k关闭时钟连续运行，将控制位置零，进入单步调试模式调试
  //   用这个时钟源需要去掉电路中的其他时钟源
  //   Beq
  //   Bne
  //   MemToReg
  //   MemWrite
  //   AluOP
  //   AluSrcB
  //   RegWrite
  //   JAL
  //   RegDst
  //   可计数暂停的时钟源
  //   为方便自动评测，需要输出流水线各段保存的PC值，注意是PC不是PC+4，另外ID段寄存器写入信息，Mem段内存写入信息也要输出
endmodule

module \气泡流水线  (
  output RegWrite,
  output MemWrite,
  output [31:0] IF_PC,
  output [31:0] ID_PC,
  output [31:0] EX_PC,
  output [31:0] M_PC,
  output [31:0] WB_PC,
  output [31:0] RDin,
  output [31:0] MDin,
  output [31:0] LedData
);

  wire and_1_out, and_2_out, and_3_out, and_4_out, CLK, clock_1_out, clock_2_out, comparator_1_eq,
       comparator_1_lt, d_ff_1_q, DataHazard, equal, ex_mem_1_jalo, ex_mem_1_lbo, ex_mem_1_memtorego,
       ex_mem_1_syscallo, EX_regWrite, Go, ID_EX_alu_srco, ID_EX_beqo, ID_EX_bgtzo, ID_EX_bneo, ID_EX_jalo,
       ID_EX_lbo, ID_EX_memtorego, ID_EX_memwriteo, ID_EX_syscallo, ID_EX_syscallo_2, IR1, IR2, IR3, J, JAL,
       MEM_regWrite, mem_wb_1_lbo, mem_wb_1_memtorego, nand_1_out, not_1_out, not_3_out, not_4_out,
       not_5_out, or_1_out, or_3_out, RST, SignedExt, Syscall, W1, W2, W3, \单周期硬布线控制器_1_alu_src ,
       \单周期硬布线控制器_1_beq , \单周期硬布线控制器_1_bgtz , \单周期硬布线控制器_1_bne , \单周期硬布线控制器_1_jal , \单周期硬布线控制器_1_jmp ,
       \单周期硬布线控制器_1_jr , \单周期硬布线控制器_1_lb , \单周期硬布线控制器_1_lui , \单周期硬布线控制器_1_memtoreg , \单周期硬布线控制器_1_memwrite ,
       \单周期硬布线控制器_1_regdst , \单周期硬布线控制器_1_regwrite , \单周期硬布线控制器_1_syscall ;
  wire [1:0] ID_EX_jro;
  wire [3:0] ID_EX_alu_opo, \单周期硬布线控制器_1_alu_op ;
  wire [4:0] EX_Writerig_num, ID_EX_shamti_2, mem_wb_1_wdino, MEM_Writerig_num, multiplexer_4_out,
       multiplexer_9_out, rs, rt, W_num;
  wire [7:0] multiplexer_12_out;
  wire [12:0] CNT_num;
  wire [15:0] adder_2_out, \LoadUse次数 , \总周期数 , \插入气泡数 , \无条件分支数 , \条件分支成功数 ;
  wire [25:0] ID_EX_iio;
  wire [31:0] adder_1_out, adder_3_out, adder_4_out, bit_extender_1_out, bit_extender_2_out,
       bit_extender_3_out, EX_IR, ex_mem_1_alu_ro, ID_EX_imextendo, ID_EX_pc_4o, ID_EX_r2o, ID_IR,
       if_id_1_pc_4o, IF_IR, MEM_IR, mem_wb_1_alu_ro, mem_wb_1_memrdo, mem_wb_1_ro, mips_alu_1_result,
       mips_regifile_1_r1, mips_regifile_1_r2, multiplexer_1_out, multiplexer_2_out, multiplexer_8_out,
       multiplexer_10_out, multiplexer_11_out, R1, R2, ram_1_data, shifter_1_out, WB_IR;

  Button \u_总复位  (.out(RST));
  Button _1 (.out(IR1));
  Button _2 (.out(IR2));
  Button _3 (.out(IR3));
  // Probe on \总周期数 
  // Probe on \总周期数 
  Button \u_继续运行  (.out(Go));
  LED #(.active("true")) led_1 (.in(W1));
  LED #(.active("true")) led_2 (.in(W2));
  LED #(.active("true")) led_3 (.in(W3));
  or or_1 (or_1_out, and_2_out, and_4_out, and_3_out);
  Hex_Digit_Display hex_digit_display_1 (.value(LedData[31:28]));  // open: dp
  // Probe on IF_PC[19:0]
  // Mips_Probe mips_probe_1: pin names not known; wires that end beside it: IF_IR
  Multiplexer #(.select(1), .width(32), .disabled("Z"), .enable("false")) multiplexer_1 (
    .in0(adder_1_out), .in1(adder_3_out), .out(multiplexer_1_out), .sel(or_1_out));
  Hex_Digit_Display hex_digit_display_2 (.value(LedData[27:24]));  // open: dp
  Hex_Digit_Display hex_digit_display_3 (.value(LedData[23:20]));  // open: dp
  // Probe on ID_PC[19:0]
  // Mips_Probe mips_probe_2: pin names not known; wires that end beside it: ID_IR
  Multiplexer #(.select(2), .width(32), .disabled("Z"), .enable("false")) multiplexer_2 (
    .in0(multiplexer_1_out), .in1(R1), .in2({ID_EX_pc_4o[31:28], ID_EX_iio, 2'b00}), .in3(R1),
    .out(multiplexer_2_out), .sel(ID_EX_jro));
  and and_1 (and_1_out, not_1_out, 1'b1);
  not not_1 (not_1_out, DataHazard);
  Multiplexer #(.select(1), .width(1), .disabled("Z"), .enable("false")) multiplexer_3 (
    .in0(1'b1), .in1(Go), .sel(Syscall));  // open: out
  Hex_Digit_Display hex_digit_display_4 (.value(LedData[15:12]));  // open: dp
  Hex_Digit_Display hex_digit_display_5 (.value(LedData[19:16]));  // open: dp
  Register #(.width(32), .trigger("rising"), .Select("low")) PC (
    .D(multiplexer_2_out), .en(and_1_out), .Q(IF_PC), .clk(CLK), .clr(RST));
  Hex_Digit_Display hex_digit_display_6 (.value(LedData[11:8]));  // open: dp
  Hex_Digit_Display hex_digit_display_7 (.value(LedData[7:4]));  // open: dp
  Clock #(.highDuration(1), .lowDuration(1)) clock_1 (.out(clock_1_out));
  // Probe on EX_PC[19:0]
  // Mips_Probe mips_probe_3: pin names not known; wires that end beside it: clock_1_out, EX_IR, CLK
  DataHazard datahazard_1 (
    .in_1(ID_IR), .MEM_regWrite(MEM_regWrite), .EX_regWrite(EX_regWrite), .rs(rs), .rt(rt),
    .EX_Writerig_num(EX_Writerig_num), .MEM_Writerig_num(MEM_Writerig_num), .data(DataHazard));
  or or_2 (J, ID_EX_jro[0], ID_EX_jro[1], and_4_out, and_2_out, and_3_out);
  Adder #(.width(32)) adder_1 (.a(IF_PC), .b(32'h4), .out(adder_1_out));  // open: cin, cout
  Register #(.width(16), .trigger("rising"), .Select("low")) register_1 (
    .D(adder_2_out), .en(1'b1), .Q(\总周期数 ), .clk(CLK), .clr(RST));
  Hex_Digit_Display hex_digit_display_8 (.value(LedData[3:0]));  // open: dp
  ROM #(.addrWidth(10), .dataWidth(32), .Select("high")) rom_1 (.addr(IF_PC[11:2]), .data(IF_IR));
  Adder #(.width(16)) adder_2 (.a(\总周期数 ), .b(16'h1), .out(adder_2_out));  // open: cin, cout
  // NOT_Gate not_2 has open pins: in=equal, out=open
  // Probe on \总周期数 
  // Probe on M_PC[19:2]
  // Mips_Probe mips_probe_4: pin names not known; wires that end beside it: MEM_IR
  // Probe on \总周期数 
  // Probe on \无条件分支数 
  // Probe on \条件分支成功数 
  // Probe on \插入气泡数 
  // Probe on \LoadUse次数 
  // Probe on IF_PC[11:0]
  // Probe on WB_PC[19:2]
  // Mips_Probe mips_probe_5: pin names not known; wires that end beside it: WB_IR
  IF_ID if_id_1 (
    .IRI(IF_IR), .IRO(ID_IR), .CLR(RST), .WE(and_1_out), .CLK(CLK), .PC_4I(adder_1_out),
    .PC_4O(if_id_1_pc_4o), .PPCI(IF_PC), .PPCO(ID_PC), .J(J));
  // Probe on ID_PC[11:0]
  // Probe on EX_PC[11:0]
  // Probe on M_PC[11:0]
  D_Flip_Flop #(.trigger("high"), .Pre_Clr_Positions("LEGACY"), .NegatePresetClear("false"), .enable("true"), .NewFFLayout("false")) d_ff_1 (.Q(d_ff_1_q));  // open: clk, D, Qn, preset, en, reset
  // Probe on 13'hac
  Multiplexer #(.select(1), .width(5), .disabled("Z"), .enable("false")) multiplexer_4 (
    .in0(ID_IR[20:16]), .in1(ID_IR[15:11]), .out(multiplexer_4_out), .sel(\单周期硬布线控制器_1_regdst ));
  assign bit_extender_1_out = {{16{1'b0}}, ID_IR[15:0]};  // Bit_Extender bit_extender_1
  // Probe on WB_PC[11:0]
  Comparator #(.width(13), .mode("twosComplement")) comparator_1 (
    .a(CNT_num), .b(13'hac), .eq(comparator_1_eq), .lt(comparator_1_lt));  // open: gt
  Clock #(.highDuration(1), .lowDuration(1)) clock_2 (.out(clock_2_out));
  \单周期硬布线控制器  \u_单周期硬布线控制器_1  (
    .Func(ID_IR[5:0]), .OP(ID_IR[31:26]), .ALU_OP(\单周期硬布线控制器_1_alu_op ), .MemToReg(\单周期硬布线控制器_1_memtoreg ),
    .MemWrite(\单周期硬布线控制器_1_memwrite ), .ALU_SRC(\单周期硬布线控制器_1_alu_src ), .RegWrite(\单周期硬布线控制器_1_regwrite ),
    .SysCALL(\单周期硬布线控制器_1_syscall ), .SignedExt(SignedExt), .RegDst(\单周期硬布线控制器_1_regdst ),
    .JR(\单周期硬布线控制器_1_jr ), .JMP(\单周期硬布线控制器_1_jmp ), .Beq(\单周期硬布线控制器_1_beq ), .JAL(\单周期硬布线控制器_1_jal ),
    .Bne(\单周期硬布线控制器_1_bne ), .LUI(\单周期硬布线控制器_1_lui ), .LB(\单周期硬布线控制器_1_lb ), .BGTZ(\单周期硬布线控制器_1_bgtz ));  // open: ERET
  Multiplexer #(.select(1), .width(5), .disabled("Z"), .enable("false")) multiplexer_5 (
    .in0(ID_IR[25:21]), .in1(5'b00010), .out(rs), .sel(\单周期硬布线控制器_1_syscall ));
  Multiplexer #(.select(1), .width(5), .disabled("Z"), .enable("false")) multiplexer_6 (
    .in0(ID_IR[20:16]), .in1(5'b00100), .out(rt), .sel(\单周期硬布线控制器_1_syscall ));
  assign bit_extender_2_out = {{16{ID_IR[15]}}, ID_IR[15:0]};  // Bit_Extender bit_extender_2
  nand nand_1 (nand_1_out, d_ff_1_q, comparator_1_eq);
  Counter #(.width(13), .max('h1fff), .ongoal("stay"), .trigger("rising"), .behavior("old")) counter_1 (
    .count(comparator_1_lt), .Q(CNT_num), .clk(clock_2_out));  // open: load, D, carry, clr, preset
  Multiplexer #(.select(1), .width(32), .disabled("Z"), .enable("false")) multiplexer_7 (
    .in0(R2), .in1(adder_4_out), .out(RDin), .sel(JAL));
  assign CLK = nand_1_out ? clock_2_out : 1'bz;  // Controlled_Buffer controlled_buffer_1
  MIPS_Regifile mips_regifile_1 (
    .Din(RDin), .Clk(CLK), .R1(mips_regifile_1_r1), .R2(mips_regifile_1_r2), .WE(RegWrite), .W_num(W_num),
    .R1_num(rs), .R2_num(rt));
  Multiplexer #(.select(1), .width(32), .disabled("Z"), .enable("false")) multiplexer_8 (
    .in0(bit_extender_1_out), .in1(bit_extender_2_out), .out(multiplexer_8_out), .sel(SignedExt));
  Pull_Resistor #(.pull(1)) pull_resistor_1 (.node(CLK));
  ID_EX ID_EX (
    .R1I(mips_regifile_1_r1), .R2I(mips_regifile_1_r2), .R1O(R1), .R2O(ID_EX_r2o), .CLR(RST), .WE(1'b1),
    .CLK(CLK), .ALU_SrcI(\单周期硬布线控制器_1_alu_src ), .ALU_SrcO(ID_EX_alu_srco), .ALU_OPO(ID_EX_alu_opo),
    .imExtendedI(multiplexer_8_out), .imExtendO(ID_EX_imextendo), .shamtI(ID_IR[10:6]),
    .shamtI_2(ID_EX_shamti_2), .ALU_OPI(\单周期硬布线控制器_1_alu_op ), .MemToRegI(\单周期硬布线控制器_1_memtoreg ),
    .MemToRegO(ID_EX_memtorego), .MemWriteI(\单周期硬布线控制器_1_memwrite ), .MemWriteO(ID_EX_memwriteo),
    .RegWriteI(\单周期硬布线控制器_1_regwrite ), .RegWriteO(EX_regWrite), .WDinI(multiplexer_4_out),
    .WDinO(EX_Writerig_num), .BeqI(\单周期硬布线控制器_1_beq ), .BeqO(ID_EX_beqo), .BneI(\单周期硬布线控制器_1_bne ),
    .BneO(ID_EX_bneo), .PPCI(ID_PC), .PPCO(EX_PC), .JI(\单周期硬布线控制器_1_jmp ), .JO(ID_EX_jro[1]),
    .JRI(\单周期硬布线控制器_1_jr ), .JRO(ID_EX_jro[0]), .J(or_3_out), .iiI(ID_IR[25:0]), .iiO(ID_EX_iio),
    .PC_4I(if_id_1_pc_4o), .PC_4O(ID_EX_pc_4o), .JalI(\单周期硬布线控制器_1_jal ), .JalO(ID_EX_jalo), .IRI(ID_IR),
    .IRO(EX_IR), .SyscallI(\单周期硬布线控制器_1_syscall ), .SyscallO(ID_EX_syscallo), .LUII(\单周期硬布线控制器_1_lui ),
    .SyscallO_2(ID_EX_syscallo_2), .LBI(\单周期硬布线控制器_1_lb ), .LBO(ID_EX_lbo), .BGTZI(\单周期硬布线控制器_1_bgtz ),
    .BGTZO(ID_EX_bgtzo));  // open: rtForwardI, rtForwardO, rsForwardI, rsForwardO
  Register #(.width(32), .trigger("rising"), .Select("low")) register_2 (
    .D(R2), .en(Syscall), .Q(LedData), .clk(CLK), .clr(RST));
  or or_3 (or_3_out, DataHazard, J);
  and and_2 (and_2_out, ID_EX_bneo, not_3_out);
  not not_3 (not_3_out, equal);
  Multiplexer #(.select(1), .width(5), .disabled("Z"), .enable("false")) multiplexer_9 (
    .in0(ID_EX_shamti_2), .in1(5'b10000), .out(multiplexer_9_out), .sel(ID_EX_syscallo_2));
  Shifter #(.width(32), .shift("ll")) shifter_1 (.in(ID_EX_imextendo), .\dist (5'b00010), .out(shifter_1_out));
  and and_3 (and_3_out, ID_EX_beqo, equal);
  and and_4 (and_4_out, ID_EX_bgtzo, not_4_out, not_5_out);
  not not_4 (not_4_out, mips_alu_1_result[0]);
  not not_5 (not_5_out, equal);
  Multiplexer #(.select(1), .width(32), .disabled("Z"), .enable("false")) multiplexer_10 (
    .in0(ID_EX_r2o), .in1(ID_EX_imextendo), .out(multiplexer_10_out), .sel(ID_EX_alu_srco));
  Adder #(.width(32)) adder_3 (.a(shifter_1_out), .b(ID_EX_pc_4o), .out(adder_3_out));  // open: cin, cout
  MIPS_ALU mips_alu_1 (
    .X(R1), .Y(multiplexer_10_out), .AluOP(ID_EX_alu_opo), .Equal(equal), .Result(mips_alu_1_result),
    .shamt(multiplexer_9_out));  // open: Result_2
  EX_MEM ex_mem_1 (
    .ALU_RI(mips_alu_1_result), .WDRI(ID_EX_r2o), .MemToRegI(ID_EX_memtorego), .MemWriteI(ID_EX_memwriteo),
    .ALU_RO(ex_mem_1_alu_ro), .WDRO(MDin), .MemToRegO(ex_mem_1_memtorego), .MemWriteO(MemWrite), .CLR(RST),
    .WE(1'b1), .CLK(CLK), .RegWriteI(EX_regWrite), .RegWriteO(MEM_regWrite), .WDinI(EX_Writerig_num),
    .WDinO(MEM_Writerig_num), .PPCI(EX_PC), .PPCO(M_PC), .JalI(ID_EX_jalo), .JalO(ex_mem_1_jalo),
    .IRI(EX_IR), .IRO(MEM_IR), .SyscallI(ID_EX_syscallo), .SyscallO(ex_mem_1_syscallo), .LBI(ID_EX_lbo),
    .LBO(ex_mem_1_lbo));  // open: equalI, equalO
  RAM #(.addrWidth(10), .dataWidth(32), .bus("separate"), .Select("high")) ram_1 (
    .addr(ex_mem_1_alu_ro[11:2]), .din(MDin), .data(ram_1_data), .str(MemWrite), .clk(CLK), .clr(RST));  // open: sel, ld
  MEM_WB mem_wb_1 (
    .ALU_RI(ex_mem_1_alu_ro), .MemRDI(ram_1_data), .MemToRegI(ex_mem_1_memtorego), .ALU_RO(mem_wb_1_alu_ro),
    .MemRDO(mem_wb_1_memrdo), .MemToRegO(mem_wb_1_memtorego), .CLR(RST), .WE(1'b1), .CLK(CLK),
    .RegWriteI(MEM_regWrite), .RegWriteO(RegWrite), .WDinI(MEM_Writerig_num), .WDinO(mem_wb_1_wdino),
    .PPCI(M_PC), .PPCO(WB_PC), .JalI(ex_mem_1_jalo), .JalO(JAL), .IRI(MEM_IR), .IRO(WB_IR),
    .SyscallI(ex_mem_1_syscallo), .SyscallO(Syscall), .RI(MDin), .RO(mem_wb_1_ro), .LBI(ex_mem_1_lbo),
    .LBO(mem_wb_1_lbo));  // open: equalI, equalO
  Multiplexer #(.select(1), .width(32), .disabled("Z"), .enable("false")) multiplexer_11 (
    .in0(mem_wb_1_alu_ro), .in1(mem_wb_1_memrdo), .out(multiplexer_11_out), .sel(mem_wb_1_memtorego));
  Multiplexer #(.select(2), .width(8), .disabled("Z"), .enable("false")) multiplexer_12 (
    .in0(multiplexer_11_out[7:0]), .in1(multiplexer_11_out[15:8]), .in2(multiplexer_11_out[23:16]),
    .in3(multiplexer_11_out[31:24]), .out(multiplexer_12_out), .sel(mem_wb_1_alu_ro[1:0]));
  Multiplexer #(.select(1), .width(5), .disabled("Z"), .enable("false")) multiplexer_13 (
    .in0(mem_wb_1_wdino), .in1({5{1'b1}}), .out(W_num), .sel(JAL));
  Adder #(.width(32)) adder_4 (.a(WB_PC), .b(32'h4), .out(adder_4_out));  // open: cin, cout
  assign bit_extender_3_out = {{24{multiplexer_12_out[7]}}, multiplexer_12_out};  // Bit_Extender bit_extender_3
  Multiplexer #(.select(1), .width(32), .disabled("Z"), .enable("false")) multiplexer_14 (
    .in0(multiplexer_11_out), .in1(bit_extender_3_out), .out(R2), .sel(mem_wb_1_lbo));

  // Other names for the same wires on the sheet: IR[31:0] = ID_IR; MEM_PC[31:0] = M_PC; PC[31:0] = IF_PC

  // Notes on the sheet:
  //   中断源
  //   时空图监测，可删除
  //   中断等待指示
  //   数码管输出
  //   指令存储器
  //   指令字
  //   contents of rom_1 (hex, n*v repeats v):
  //   20110001 8000c05 20110001 20120002 20130003 8000c09 20110001 20120002 20130003 8000c0d 20110001
  //   20120002 20130003 8000c11 20110001 20120002 20130003 c000cb8 20100001 20110001 118fc0 112020
  //   20020022 c 118882 12200001 8000c15 112020 20020022 c 20110001 118880 112020 20020022 c 12200001
  //   8000c1f 20110001 118fc0 112020 20020022 c 1188c3 112020 20020022 c 118903 112020 20020022 c 118903
  //   112020 20020022 c 118903 112020 20020022 c 118903 112020 20020022 c 118903 112020 20020022 c 118903
  //   112020 20020022 c 118903 112020 20020022 c 20100001 109fc0 139fc3 8021 2012000c 24160003 26100001
  //   3210000f 20080008 20090001 139900 2709825 132020 20020022 c 1094022 1500fff9 22100001 2018000f
  //   2188024 108700 20080008 20090001 139902 2709825 132021 20020022 c 1094022 1500fff9 108702 2c9b022
  //   12c00001 8000c50 4020 1084027 84400 3508ffff 82021 20020022 c 2010ffff 20110000 ae300000 22100001
  //   22310004 ae300000 22100001 22310004 ae300000 22100001 22310004 ae300000 22100001 22310004 ae300000
  //   22100001 22310004 ae300000 22100001 22310004 ae300000 22100001 22310004 ae300000 22100001 22310004
  //   ae300000 22100001 22310004 ae300000 22100001 22310004 ae300000 22100001 22310004 ae300000 22100001
  //   22310004 ae300000 22100001 22310004 ae300000 22100001 22310004 ae300000 22100001 22310004 ae300000
  //   22100001 22310004 22100001 8020 2011003c 8e130000 8e340000 274402a 11000002 ae330000 ae140000
  //   2231fffc 1611fff8 102020 20020022 c 22100004 2011003c 1611fff2 20020032 c 20100000 22100001 102020
  //   20020022 c 22100002 102020 20020022 c 22100003 102020 20020022 c 22100004 102020 20020022 c 22100005
  //   102020 20020022 c 22100006 102020 20020022 c 22100007 102020 20020022 c 22100008 102020 20020022
  //   20020022 c 3e00008
  //   控制位
  //   OP
  //   Func
  //   rs
  //   rt
  //   rd
  //   im
  //   ii
  //   流水调试日志用
  //   暂停节拍，不能为0
  //   JMP
  //   JR
  //   OP
  //   Func
  //   戳工具置1进入计数暂停模式，ctrl+k时钟自动运行到对应节拍暂停
  //   ctrl+k关闭时钟连续运行，将控制位置零，进入单步调试模式调试
  //   Beq
  //   Bne
  //   MemToReg
  //   MemWrite
  //   AluOP
  //   AluSrcB
  //   RegWrite
  //   JAL
  //   RegDst
  //   Syscall
  //   可计数暂停的时钟源
  //   为方便自动评测，需要输出流水线各段保存的PC值，注意是PC不是PC+4，另外ID段寄存器写入信息，Mem段内存写入信息也要输出
endmodule

module \重定向流水线  (
  output RegWrite,
  output MemWrite,
  output [31:0] IF_PC,
  output [31:0] ID_PC,
  output [31:0] EX_PC,
  output [31:0] M_PC,
  output [31:0] WB_PC,
  output [31:0] RDin,
  output [31:0] MDin,
  output [31:0] LedData
);

  wire and_1_out, and_2_out, and_3_out, and_4_out, and_5_out, CLK, clock_1_out, clock_2_out, comparator_1_eq,
       comparator_1_lt, d_ff_1_q, equal, ex_mem_1_equalo, ex_mem_1_jalo, ex_mem_1_lbo, ex_mem_1_memtorego,
       ex_mem_1_syscallo, EX_MEMread, EX_regWrite, Go, ID_EX_alu_srco, ID_EX_beqo, ID_EX_bgtzo, ID_EX_bneo,
       ID_EX_jalo, ID_EX_lbo, ID_EX_memwriteo, ID_EX_syscallo, ID_EX_syscallo_2, IR1, IR2, IR3, J, JAL,
       load_use, MEM_regWrite, mem_wb_1_lbo, mem_wb_1_memtorego, mips_alu_1_equal, nand_1_out, not_1_out,
       not_2_out, not_3_out, not_4_out, not_5_out, or_1_out, or_3_out, power, RST, SignedExt, Syscall, W1,
       W2, W3, \单周期硬布线控制器_1_alu_src , \单周期硬布线控制器_1_beq , \单周期硬布线控制器_1_bgtz , \单周期硬布线控制器_1_bne ,
       \单周期硬布线控制器_1_jal , \单周期硬布线控制器_1_jmp , \单周期硬布线控制器_1_jr , \单周期硬布线控制器_1_lb , \单周期硬布线控制器_1_lui ,
       \单周期硬布线控制器_1_memtoreg , \单周期硬布线控制器_1_memwrite , \单周期硬布线控制器_1_regdst , \单周期硬布线控制器_1_regwrite ,
       \单周期硬布线控制器_1_syscall ;
  wire [1:0] ID_EX_jro, ID_EX_rsforwardo, ID_EX_rtforwardo, redirect_1_rs_forward, redirect_1_rt_forward;
  wire [3:0] ID_EX_alu_opo, \单周期硬布线控制器_1_alu_op ;
  wire [4:0] EX_Writerig_num, ID_EX_shamti_2, mem_wb_1_wdino, MEM_Writerig_num, multiplexer_3_out,
       multiplexer_11_out, rs, rt, W_num;
  wire [7:0] multiplexer_14_out;
  wire [12:0] CNT_num;
  wire [15:0] adder_2_out, \LoadUse次数 , \总周期数 , \插入气泡数 , \无条件分支数 , \条件分支成功数 ;
  wire [25:0] ID_EX_iio;
  wire [31:0] adder_1_out, adder_3_out, adder_4_out, ALURS, bit_extender_1_out, bit_extender_2_out,
       bit_extender_3_out, EX_IR, ID_EX_imextendo, ID_EX_pc_4o, ID_EX_r1o, ID_EX_r2o, ID_IR, if_id_1_pc_4o,
       IF_IR, LED, MEM_IR, mem_wb_1_alu_ro, mem_wb_1_memrdo, mips_alu_1_result, mips_regifile_1_r1,
       mips_regifile_1_r2, multiplexer_1_out, multiplexer_2_out, multiplexer_7_out, multiplexer_9_out,
       multiplexer_10_out, multiplexer_12_out, multiplexer_13_out, R1, ram_1_data, shifter_1_out, WB_IR, WBD;

  Button \u_总复位  (.out(RST));
  Button _1 (.out(IR1));
  Button _2 (.out(IR2));
  Button _3 (.out(IR3));
  // Probe on \总周期数 
  // Probe on \总周期数 
  Button \u_继续运行  (.out(Go));
  LED #(.active("true")) led_1 (.in(W1));
  LED #(.active("true")) led_2 (.in(W2));
  LED #(.active("true")) led_3 (.in(W3));
  or or_1 (or_1_out, and_3_out, and_4_out, and_5_out);
  Hex_Digit_Display hex_digit_display_1 (.value(LedData[31:28]));  // open: dp
  // Probe on IF_PC[19:0]
  // Mips_Probe mips_probe_1: pin names not known; wires that end beside it: IF_IR
  Multiplexer #(.select(1), .width(32), .disabled("Z"), .enable("false")) multiplexer_1 (
    .in0(adder_1_out), .in1(adder_3_out), .out(multiplexer_1_out), .sel(or_1_out));
  Hex_Digit_Display hex_digit_display_2 (.value(LedData[23:20]));  // open: dp
  Hex_Digit_Display hex_digit_display_3 (.value(LedData[27:24]));  // open: dp
  // Probe on ID_PC[19:0]
  // Mips_Probe mips_probe_2: pin names not known; wires that end beside it: ID_IR
  Multiplexer #(.select(2), .width(32), .disabled("Z"), .enable("false")) multiplexer_2 (
    .in0(multiplexer_1_out), .in1(R1), .in2({ID_EX_pc_4o[31:28], ID_EX_iio, 2'b00}), .in3(R1),
    .out(multiplexer_2_out), .sel(ID_EX_jro));
  and and_1 (and_1_out, not_1_out, power);
  not not_1 (not_1_out, load_use);
  Hex_Digit_Display hex_digit_display_4 (.value(LedData[19:16]));  // open: dp
  Hex_Digit_Display hex_digit_display_5 (.value(LedData[15:12]));  // open: dp
  Register #(.width(32), .trigger("rising"), .Select("low")) PC (
    .D(multiplexer_2_out), .en(and_1_out), .Q(IF_PC), .clk(CLK), .clr(RST));
  Hex_Digit_Display hex_digit_display_6 (.value(LedData[11:8]));  // open: dp
  Hex_Digit_Display hex_digit_display_7 (.value(LedData[7:4]));  // open: dp
  Clock #(.highDuration(1), .lowDuration(1)) clock_1 (.out(clock_1_out));
  // Probe on EX_PC[19:0]
  // Mips_Probe mips_probe_3: pin names not known; wires that end beside it: clock_1_out, EX_IR, CLK
  or or_2 (J, ID_EX_jro[0], ID_EX_jro[1], and_4_out, and_3_out, and_5_out);
  Adder #(.width(32)) adder_1 (.a(IF_PC), .b(32'h4), .out(adder_1_out));  // open: cin, cout
  Register #(.width(16), .trigger("rising"), .Select("low")) register_1 (
    .D(adder_2_out), .en(power), .Q(\总周期数 ), .clk(CLK), .clr(RST));
  Hex_Digit_Display hex_digit_display_8 (.value(LedData[3:0]));  // open: dp
  ROM #(.addrWidth(10), .dataWidth(32), .Select("high")) rom_1 (.addr(IF_PC[11:2]), .data(IF_IR));
  Adder #(.width(16)) adder_2 (.a(\总周期数 ), .b(16'h1), .out(adder_2_out));  // open: cin, cout
  // Probe on \总周期数 
  // Probe on M_PC[19:0]
  // Mips_Probe mips_probe_4: pin names not known; wires that end beside it: MEM_IR
  // Probe on \总周期数 
  // Probe on \无条件分支数 
  // Probe on \条件分支成功数 
  // Probe on \插入气泡数 
  // Probe on \LoadUse次数 
  and and_2 (and_2_out, Syscall, not_2_out);
  not not_2 (not_2_out, equal);
  // Probe on IF_PC[11:0]
  // Probe on WB_PC[19:0]
  // Mips_Probe mips_probe_5: pin names not known; wires that end beside it: WB_IR
  IF_ID if_id_1 (
    .IRI(IF_IR), .IRO(ID_IR), .CLR(RST), .WE(and_1_out), .CLK(CLK), .PC_4I(adder_1_out),
    .PC_4O(if_id_1_pc_4o), .PPCI(IF_PC), .PPCO(ID_PC), .J(J));
  J_K_Flip_Flop #(.trigger("rising"), .Pre_Clr_Positions("ABOVE_BELOW"), .NegatePresetClear("false"), .enable("false"), .NewFFLayout("true")) j_k_ff_1 (
    .J(and_2_out), .clk(CLK), .K(Go), .Qn(power), .reset(Go));  // open: Q, preset
  // Probe on ID_PC[11:0]
  // Probe on EX_PC[11:0]
  // Probe on M_PC[11:0]
  D_Flip_Flop #(.trigger("high"), .Pre_Clr_Positions("LEGACY"), .NegatePresetClear("false"), .enable("true"), .NewFFLayout("false")) d_ff_1 (.Q(d_ff_1_q));  // open: clk, D, Qn, preset, en, reset
  // Probe on 13'h8f7
  Multiplexer #(.select(1), .width(5), .disabled("Z"), .enable("false")) multiplexer_3 (
    .in0(ID_IR[20:16]), .in1(ID_IR[15:11]), .out(multiplexer_3_out), .sel(\单周期硬布线控制器_1_regdst ));
  assign bit_extender_1_out = {{16{1'b0}}, ID_IR[15:0]};  // Bit_Extender bit_extender_1
  // Probe on WB_PC[11:0]
  Comparator #(.width(13), .mode("twosComplement")) comparator_1 (
    .a(CNT_num), .b(13'h8f7), .eq(comparator_1_eq), .lt(comparator_1_lt));  // open: gt
  Clock #(.highDuration(1), .lowDuration(1)) clock_2 (.out(clock_2_out));
  Redirect redirect_1 (
    .in_1(ID_IR), .rs(rs), .rt(rt), .EX_Writerig_num(EX_Writerig_num), .MEM_Writerig_num(MEM_Writerig_num),
    .EX_regWrite(EX_regWrite), .EX_MEMRead(EX_MEMread), .MEM_regWrite(MEM_regWrite), .load_use(load_use),
    .rs_forward(redirect_1_rs_forward), .rt_forward(redirect_1_rt_forward));
  \单周期硬布线控制器  \u_单周期硬布线控制器_1  (
    .Func(ID_IR[5:0]), .OP(ID_IR[31:26]), .ALU_OP(\单周期硬布线控制器_1_alu_op ), .MemToReg(\单周期硬布线控制器_1_memtoreg ),
    .MemWrite(\单周期硬布线控制器_1_memwrite ), .ALU_SRC(\单周期硬布线控制器_1_alu_src ), .RegWrite(\单周期硬布线控制器_1_regwrite ),
    .SysCALL(\单周期硬布线控制器_1_syscall ), .SignedExt(SignedExt), .RegDst(\单周期硬布线控制器_1_regdst ),
    .JR(\单周期硬布线控制器_1_jr ), .JMP(\单周期硬布线控制器_1_jmp ), .Beq(\单周期硬布线控制器_1_beq ), .JAL(\单周期硬布线控制器_1_jal ),
    .Bne(\单周期硬布线控制器_1_bne ), .LUI(\单周期硬布线控制器_1_lui ), .LB(\单周期硬布线控制器_1_lb ), .BGTZ(\单周期硬布线控制器_1_bgtz ));  // open: ERET
  Multiplexer #(.select(1), .width(5), .disabled("Z"), .enable("false")) multiplexer_4 (
    .in0(ID_IR[25:21]), .in1(5'b00010), .out(rs), .sel(\单周期硬布线控制器_1_syscall ));
  Multiplexer #(.select(1), .width(5), .disabled("Z"), .enable("false")) multiplexer_5 (
    .in0(ID_IR[20:16]), .in1(5'b00100), .out(rt), .sel(\单周期硬布线控制器_1_syscall ));
  assign bit_extender_2_out = {{16{ID_IR[15]}}, ID_IR[15:0]};  // Bit_Extender bit_extender_2
  nand nand_1 (nand_1_out, d_ff_1_q, comparator_1_eq);
  Counter #(.width(13), .max('h1fff), .ongoal("stay"), .trigger("rising"), .behavior("old")) counter_1 (
    .count(comparator_1_lt), .Q(CNT_num), .clk(clock_2_out));  // open: load, D, carry, clr, preset
  // Probe on redirect_1_rs_forward
  Multiplexer #(.select(1), .width(32), .disabled("Z"), .enable("false")) multiplexer_6 (
    .in0(WBD), .in1(adder_4_out), .out(RDin), .sel(JAL));
  assign CLK = nand_1_out ? clock_2_out : 1'bz;  // Controlled_Buffer controlled_buffer_1
  // Probe on redirect_1_rt_forward
  MIPS_Regifile mips_regifile_1 (
    .Din(RDin), .Clk(CLK), .R1(mips_regifile_1_r1), .R2(mips_regifile_1_r2), .WE(RegWrite), .W_num(W_num),
    .R1_num(rs), .R2_num(rt));
  Multiplexer #(.select(1), .width(32), .disabled("Z"), .enable("false")) multiplexer_7 (
    .in0(bit_extender_1_out), .in1(bit_extender_2_out), .out(multiplexer_7_out), .sel(SignedExt));
  Pull_Resistor #(.pull(1)) pull_resistor_1 (.node(CLK));
  ID_EX ID_EX (
    .R1I(mips_regifile_1_r1), .R2I(mips_regifile_1_r2), .R1O(ID_EX_r1o), .R2O(ID_EX_r2o), .CLR(RST),
    .WE(power), .CLK(CLK), .ALU_SrcI(\单周期硬布线控制器_1_alu_src ), .ALU_SrcO(ID_EX_alu_srco),
    .ALU_OPO(ID_EX_alu_opo), .imExtendedI(multiplexer_7_out), .imExtendO(ID_EX_imextendo),
    .shamtI(ID_IR[10:6]), .shamtI_2(ID_EX_shamti_2), .ALU_OPI(\单周期硬布线控制器_1_alu_op ),
    .MemToRegI(\单周期硬布线控制器_1_memtoreg ), .MemToRegO(EX_MEMread), .MemWriteI(\单周期硬布线控制器_1_memwrite ),
    .MemWriteO(ID_EX_memwriteo), .RegWriteI(\单周期硬布线控制器_1_regwrite ), .RegWriteO(EX_regWrite),
    .WDinI(multiplexer_3_out), .WDinO(EX_Writerig_num), .BeqI(\单周期硬布线控制器_1_beq ), .BeqO(ID_EX_beqo),
    .BneI(\单周期硬布线控制器_1_bne ), .BneO(ID_EX_bneo), .PPCI(ID_PC), .PPCO(EX_PC), .JI(\单周期硬布线控制器_1_jmp ),
    .JO(ID_EX_jro[1]), .JRI(\单周期硬布线控制器_1_jr ), .JRO(ID_EX_jro[0]), .J(or_3_out), .iiI(ID_IR[25:0]),
    .iiO(ID_EX_iio), .PC_4I(if_id_1_pc_4o), .PC_4O(ID_EX_pc_4o), .JalI(\单周期硬布线控制器_1_jal ), .JalO(ID_EX_jalo),
    .IRI(ID_IR), .IRO(EX_IR), .SyscallI(\单周期硬布线控制器_1_syscall ), .SyscallO(ID_EX_syscallo),
    .LUII(\单周期硬布线控制器_1_lui ), .SyscallO_2(ID_EX_syscallo_2), .LBI(\单周期硬布线控制器_1_lb ), .LBO(ID_EX_lbo),
    .BGTZI(\单周期硬布线控制器_1_bgtz ), .BGTZO(ID_EX_bgtzo), .rtForwardI(redirect_1_rt_forward),
    .rtForwardO(ID_EX_rtforwardo), .rsForwardI(redirect_1_rs_forward), .rsForwardO(ID_EX_rsforwardo));
  or or_3 (or_3_out, load_use, J);
  Register #(.width(32), .trigger("rising"), .Select("low")) register_2 (
    .D(LED), .en(Syscall), .Q(LedData), .clk(CLK), .clr(RST));
  and and_3 (and_3_out, ID_EX_bneo, not_3_out);
  not not_3 (not_3_out, mips_alu_1_equal);
  Multiplexer #(.select(2), .width(32), .disabled("Z"), .enable("false")) multiplexer_8 (
    .in0(ID_EX_r1o), .in1(WBD), .in2(ALURS), .out(R1), .sel(ID_EX_rsforwardo));  // open: in3
  Multiplexer #(.select(2), .width(32), .disabled("Z"), .enable("false")) multiplexer_9 (
    .in0(ID_EX_r2o), .in1(WBD), .in2(ALURS), .out(multiplexer_9_out), .sel(ID_EX_rtforwardo));  // open: in3
  Multiplexer #(.select(1), .width(32), .disabled("Z"), .enable("false")) multiplexer_10 (
    .in0(multiplexer_9_out), .in1(ID_EX_imextendo), .out(multiplexer_10_out), .sel(ID_EX_alu_srco));
  Multiplexer #(.select(1), .width(5), .disabled("Z"), .enable("false")) multiplexer_11 (
    .in0(ID_EX_shamti_2), .in1(5'b10000), .out(multiplexer_11_out), .sel(ID_EX_syscallo_2));
  Shifter #(.width(32), .shift("ll")) shifter_1 (.in(ID_EX_imextendo), .\dist (5'b00010), .out(shifter_1_out));
  and and_4 (and_4_out, ID_EX_bgtzo, not_4_out, not_5_out);
  and and_5 (and_5_out, ID_EX_beqo, mips_alu_1_equal);
  not not_4 (not_4_out, mips_alu_1_result[0]);
  not not_5 (not_5_out, mips_alu_1_equal);
  Multiplexer #(.select(1), .width(32), .disabled("Z"), .enable("false")) multiplexer_12 (
    .in0(multiplexer_10_out), .in1(32'h22), .out(multiplexer_12_out), .sel(ID_EX_syscallo));
  Adder #(.width(32)) adder_3 (.a(shifter_1_out), .b(ID_EX_pc_4o), .out(adder_3_out));  // open: cin, cout
  MIPS_ALU mips_alu_1 (
    .X(R1), .Y(multiplexer_12_out), .AluOP(ID_EX_alu_opo), .Equal(mips_alu_1_equal),
    .Result(mips_alu_1_result), .shamt(multiplexer_11_out));  // open: Result_2
  EX_MEM ex_mem_1 (
    .ALU_RI(mips_alu_1_result), .WDRI(multiplexer_9_out), .MemToRegI(EX_MEMread),
    .MemWriteI(ID_EX_memwriteo), .ALU_RO(ALURS), .WDRO(MDin), .MemToRegO(ex_mem_1_memtorego),
    .MemWriteO(MemWrite), .CLR(RST), .WE(power), .CLK(CLK), .RegWriteI(EX_regWrite),
    .RegWriteO(MEM_regWrite), .WDinI(EX_Writerig_num), .WDinO(MEM_Writerig_num), .PPCI(EX_PC), .PPCO(M_PC),
    .JalI(ID_EX_jalo), .JalO(ex_mem_1_jalo), .IRI(EX_IR), .IRO(MEM_IR), .SyscallI(ID_EX_syscallo),
    .SyscallO(ex_mem_1_syscallo), .LBI(ID_EX_lbo), .LBO(ex_mem_1_lbo), .equalI(mips_alu_1_equal),
    .equalO(ex_mem_1_equalo));
  RAM #(.addrWidth(10), .dataWidth(32), .bus("separate"), .Select("high")) ram_1 (
    .addr(ALURS[11:2]), .din(MDin), .data(ram_1_data), .str(MemWrite), .clk(CLK), .clr(RST));  // open: sel, ld
  MEM_WB mem_wb_1 (
    .ALU_RI(ALURS), .MemRDI(ram_1_data), .MemToRegI(ex_mem_1_memtorego), .ALU_RO(mem_wb_1_alu_ro),
    .MemRDO(mem_wb_1_memrdo), .MemToRegO(mem_wb_1_memtorego), .CLR(RST), .WE(power), .CLK(CLK),
    .RegWriteI(MEM_regWrite), .RegWriteO(RegWrite), .WDinI(MEM_Writerig_num), .WDinO(mem_wb_1_wdino),
    .PPCI(M_PC), .PPCO(WB_PC), .JalI(ex_mem_1_jalo), .JalO(JAL), .IRI(MEM_IR), .IRO(WB_IR),
    .SyscallI(ex_mem_1_syscallo), .SyscallO(Syscall), .RI(MDin), .RO(LED), .LBI(ex_mem_1_lbo),
    .LBO(mem_wb_1_lbo), .equalI(ex_mem_1_equalo), .equalO(equal));
  Multiplexer #(.select(1), .width(32), .disabled("Z"), .enable("false")) multiplexer_13 (
    .in0(mem_wb_1_alu_ro), .in1(mem_wb_1_memrdo), .out(multiplexer_13_out), .sel(mem_wb_1_memtorego));
  Multiplexer #(.select(2), .width(8), .disabled("Z"), .enable("false")) multiplexer_14 (
    .in0(multiplexer_13_out[7:0]), .in1(multiplexer_13_out[15:8]), .in2(multiplexer_13_out[23:16]),
    .in3(multiplexer_13_out[31:24]), .out(multiplexer_14_out), .sel(mem_wb_1_alu_ro[1:0]));
  Multiplexer #(.select(1), .width(5), .disabled("Z"), .enable("false")) multiplexer_15 (
    .in0(mem_wb_1_wdino), .in1({5{1'b1}}), .out(W_num), .sel(JAL));
  Adder #(.width(32)) adder_4 (.a(WB_PC), .b(32'h4), .out(adder_4_out));  // open: cin, cout
  assign bit_extender_3_out = {{24{multiplexer_14_out[7]}}, multiplexer_14_out};  // Bit_Extender bit_extender_3
  Multiplexer #(.select(1), .width(32), .disabled("Z"), .enable("false")) multiplexer_16 (
    .in0(multiplexer_13_out), .in1(bit_extender_3_out), .out(WBD), .sel(mem_wb_1_lbo));

  // Other names for the same wires on the sheet: IR[31:0] = ID_IR; MEM_PC[31:0] = M_PC; PC[31:0] = IF_PC

  // Notes on the sheet:
  //   中断源
  //   时空图监测，可删除
  //   中断等待指示
  //   数码管输出
  //   指令存储器
  //   指令字
  //   contents of rom_1 (hex, n*v repeats v):
  //   20110001 8000c05 20110001 20120002 20130003 8000c09 20110001 20120002 20130003 8000c0d 20110001
  //   20120002 20130003 8000c11 20110001 20120002 20130003 c000cb8 20100001 20110001 118fc0 112020
  //   20020022 c 118882 12200001 8000c15 112020 20020022 c 20110001 118880 112020 20020022 c 12200001
  //   8000c1f 20110001 118fc0 112020 20020022 c 1188c3 112020 20020022 c 118903 112020 20020022 c 118903
  //   112020 20020022 c 118903 112020 20020022 c 118903 112020 20020022 c 118903 112020 20020022 c 118903
  //   112020 20020022 c 118903 112020 20020022 c 20100001 109fc0 139fc3 8021 2012000c 24160003 26100001
  //   3210000f 20080008 20090001 139900 2709825 132020 20020022 c 1094022 1500fff9 22100001 2018000f
  //   2188024 108700 20080008 20090001 139902 2709825 132021 20020022 c 1094022 1500fff9 108702 2c9b022
  //   12c00001 8000c50 4020 1084027 84400 3508ffff 82021 20020022 c 2010ffff 20110000 ae300000 22100001
  //   22310004 ae300000 22100001 22310004 ae300000 22100001 22310004 ae300000 22100001 22310004 ae300000
  //   22100001 22310004 ae300000 22100001 22310004 ae300000 22100001 22310004 ae300000 22100001 22310004
  //   ae300000 22100001 22310004 ae300000 22100001 22310004 ae300000 22100001 22310004 ae300000 22100001
  //   22310004 ae300000 22100001 22310004 ae300000 22100001 22310004 ae300000 22100001 22310004 ae300000
  //   22100001 22310004 22100001 8020 2011003c 8e130000 8e340000 274402a 11000002 ae330000 ae140000
  //   2231fffc 1611fff8 102020 20020022 c 22100004 2011003c 1611fff2 20020032 c 20100000 22100001 102020
  //   20020022 c 22100002 102020 20020022 c 22100003 102020 20020022 c 22100004 102020 20020022 c 22100005
  //   102020 20020022 c 22100006 102020 20020022 c 22100007 102020 20020022 c 22100008 102020 20020022
  //   20020022 c 3e00008
  //   控制位
  //   OP
  //   Func
  //   rs
  //   rt
  //   rd
  //   im
  //   ii
  //   流水调试日志用
  //   暂停节拍，不能为0
  //   JMP
  //   JR
  //   OP
  //   Func
  //   戳工具置1进入计数暂停模式，ctrl+k时钟自动运行到对应节拍暂停
  //   ctrl+k关闭时钟连续运行，将控制位置零，进入单步调试模式调试
  //   Beq
  //   Bne
  //   MemToReg
  //   MemWrite
  //   AluOP
  //   AluSrcB
  //   RegWrite
  //   JAL
  //   RegDst
  //   Syscall
  //   可计数暂停的时钟源
  //   为方便自动评测，需要输出流水线各段保存的PC值，注意是PC不是PC+4，另外ID段寄存器写入信息，Mem段内存写入信息也要输出
endmodule

module \中断按键参考电路  (
  input  \同步清零信号 ,
  output \与中断屏蔽位与 
);

  wire \_1号中断_out , and_1_out, clock_1_out, d_ff_1_q, or_1_out, or_2_out;

  Clock #(.highDuration(1), .lowDuration(1)) clock_1 (.out(clock_1_out));
  Button \_1号中断  (.out(\_1号中断_out ));
  LED #(.active("true")) \_1号中断等待指示灯  (.in(or_1_out));
  or or_1 (or_1_out, \与中断屏蔽位与 , d_ff_1_q);
  D_Flip_Flop #(.trigger("rising"), .Pre_Clr_Positions("LEGACY"), .NegatePresetClear("false"), .enable("true"), .NewFFLayout("false")) d_ff_1 (
    .clk(\_1号中断_out ), .D(1'b1), .Q(d_ff_1_q), .reset(\与中断屏蔽位与 ));  // open: Qn, preset, en
  or or_2 (or_2_out, d_ff_1_q, \与中断屏蔽位与 );
  and and_1 (and_1_out, or_2_out, ~\同步清零信号 );  // AND_Gate
  D_Flip_Flop #(.trigger("rising"), .Pre_Clr_Positions("LEGACY"), .NegatePresetClear("false"), .enable("true"), .NewFFLayout("false")) IR1 (
    .clk(clock_1_out), .D(and_1_out), .Q(\与中断屏蔽位与 ));  // open: Qn, preset, en, reset

  // Notes on the sheet:
  //   中断信号采样参考电路
  //   Reset 
endmodule
module \单周期MIPS_单级中断  (
  input  IR1,
  input  IR2,
  input  IR3,
  output RegWrite,
  output MemWrite,
  output [31:0] PC,
  output [31:0] IR,
  output [31:0] RDin,
  output [31:0] MDin,
  output [31:0] LedData
);

  wire and_1_out, and_2_out, and_3_out, and_4_out, and_5_out, and_6_out, and_7_out, and_8_out, and_9_out,
       and_10_out, and_11_out, and_12_out, CLK, clock_2_out, comparator_1_eq, comparator_2_eq,
       comparator_2_lt, comparator_3_eq, comparator_4_eq, comparator_5_eq, comparator_6_eq, d_ff_1_q,
       d_ff_2_q, d_ff_3_q, d_ff_4_q, decoder_1_out1, decoder_1_out2, decoder_1_out3, EnterInt, equal, ERET,
       Go, INT, IR1_q, IR1_t, IR2_q, IR2_t, IR3_q, IR3_t, IRA, IRB, IRC, nand_1_out, not_1_out, not_2_out,
       not_3_out, or_1_out, or_5_out, or_6_out, or_7_out, or_8_out, or_13_out, power, RST, SignedExt,
       Syscall, t_ff_1_qn, undriven, W1, W2, W3, \单周期硬布线控制器_1_alu_src , \单周期硬布线控制器_1_beq , \单周期硬布线控制器_1_bne ,
       \单周期硬布线控制器_1_jal , \单周期硬布线控制器_1_memtoreg , \单周期硬布线控制器_1_regdst ;
  wire [1:0] multiplexer_4_out, priority_encoder_1_out, register_2_q, \单周期硬布线控制器_1_jr ;
  wire [3:0] adder_1_out, \单周期硬布线控制器_1_alu_op ;
  wire [4:0] multiplexer_6_out, multiplexer_7_out, multiplexer_8_out, multiplexer_11_out;
  wire [7:0] adder_4_out, multiplexer_15_out, multiplexer_16_out, multiplexer_18_out, register_4_q,
       subtractor_1_out;
  wire [12:0] CNT_num;
  wire [15:0] adder_2_out, \总周期数 ;
  wire [27:0] adder_1_out_2;
  wire [31:0] adder_3_out, adder_5_out, bit_extender_1_out, bit_extender_2_out, INTADDR, mips_alu_1_result,
       multiplexer_1_out, multiplexer_3_out, multiplexer_5_out, multiplexer_9_out, multiplexer_13_out,
       multiplexer_14_out, multiplexer_17_out, PC_4, R1, ram_1_data, ram_2_data, RET, shifter_1_out;

  Clock #(.highDuration(1), .lowDuration(1)) clock_1 ();  // open: out
  Button _1 ();  // open: out
  Button _2 ();  // open: out
  Button _3 ();  // open: out
  or or_1 (or_1_out, and_10_out, and_11_out);
  Button \u_继续运行  (.out(Go));
  LED #(.active("true")) led_1 (.in(W1));
  LED #(.active("true")) led_2 (.in(W2));
  LED #(.active("true")) led_3 (.in(W3));
  Button button_1 (.out(RST));
  Multiplexer #(.select(1), .width(32), .disabled("Z"), .enable("false")) multiplexer_1 (
    .in0({adder_1_out, adder_1_out_2}), .in1(adder_3_out), .out(multiplexer_1_out), .sel(or_1_out));
  or or_2 (W1, IR1_q, d_ff_1_q);
  or or_3 (W2, IR2_q, d_ff_2_q);
  or or_4 (W3, IR3_q, d_ff_3_q);
  Hex_Digit_Display hex_digit_display_1 (.value(LedData[31:28]));  // open: dp
  Multiplexer #(.select(2), .width(32), .disabled("Z"), .enable("false")) multiplexer_2 (
    .in0(multiplexer_1_out), .in1(R1), .in2({adder_1_out, IR[25:0], 2'b00}), .in3(R1), .out(PC_4),
    .sel(\单周期硬布线控制器_1_jr ));
  D_Flip_Flop #(.trigger("rising"), .Pre_Clr_Positions("LEGACY"), .NegatePresetClear("false"), .enable("true"), .NewFFLayout("false")) d_ff_1 (
    .clk(IR1_t), .D(1'b1), .Q(d_ff_1_q), .reset(IR1_q));  // open: Qn, preset, en
  D_Flip_Flop #(.trigger("rising"), .Pre_Clr_Positions("LEGACY"), .NegatePresetClear("false"), .enable("true"), .NewFFLayout("false")) d_ff_2 (
    .clk(IR2_t), .D(1'b1), .Q(d_ff_2_q), .reset(IR2_q));  // open: Qn, preset, en
  D_Flip_Flop #(.trigger("rising"), .Pre_Clr_Positions("LEGACY"), .NegatePresetClear("false"), .enable("true"), .NewFFLayout("false")) d_ff_3 (
    .clk(IR3_t), .D(1'b1), .Q(d_ff_3_q), .reset(IR3_q));  // open: Qn, preset, en
  Hex_Digit_Display hex_digit_display_2 (.value(LedData[23:20]));  // open: dp
  Hex_Digit_Display hex_digit_display_3 (.value(LedData[27:24]));  // open: dp
  Register #(.width(32), .trigger("rising"), .Select("low")) u_PC (
    .D(multiplexer_3_out), .en(and_1_out), .Q(PC), .clk(CLK), .clr(RST));
  Multiplexer #(.select(1), .width(32), .disabled("Z"), .enable("false")) multiplexer_3 (
    .in0(PC_4), .in1(INTADDR), .out(multiplexer_3_out), .sel(EnterInt));
  and and_1 (and_1_out, power, power);
  or or_5 (or_5_out, d_ff_1_q, IR1_q);
  and and_2 (and_2_out, ERET, decoder_1_out1);
  or or_6 (or_6_out, d_ff_2_q, IR2_q);
  and and_3 (and_3_out, ERET, decoder_1_out2);
  or or_7 (or_7_out, d_ff_3_q, IR3_q);
  and and_4 (and_4_out, ERET, decoder_1_out3);
  Hex_Digit_Display hex_digit_display_4 (.value(LedData[19:16]));  // open: dp
  Hex_Digit_Display hex_digit_display_5 (.value(LedData[15:12]));  // open: dp
  Register #(.width(16), .trigger("rising"), .Select("low")) register_1 (
    .D(adder_2_out), .en(and_1_out), .Q(\总周期数 ), .clk(CLK), .clr(RST));
  and and_5 (and_5_out, or_5_out, ~and_2_out);  // AND_Gate
  and and_6 (and_6_out, or_6_out, ~and_3_out);  // AND_Gate
  and and_7 (and_7_out, or_7_out, ~and_4_out);  // AND_Gate
  Hex_Digit_Display hex_digit_display_6 (.value(LedData[7:4]));  // open: dp
  Hex_Digit_Display hex_digit_display_7 (.value(LedData[11:8]));  // open: dp
  // Probe on \总周期数 
  Adder #(.width(32)) adder_1 (.a(PC), .b(32'h4), .out({adder_1_out, adder_1_out_2}));  // open: cin, cout
  Adder #(.width(16)) adder_2 (.a(\总周期数 ), .b(16'h1), .out(adder_2_out));  // open: cin, cout
  D_Flip_Flop #(.trigger("rising"), .Pre_Clr_Positions("LEGACY"), .NegatePresetClear("false"), .enable("true"), .NewFFLayout("false")) u_IR1 (
    .clk(CLK), .D(and_5_out), .Q(IR1_q));  // open: Qn, preset, en, reset
  D_Flip_Flop #(.trigger("rising"), .Pre_Clr_Positions("LEGACY"), .NegatePresetClear("false"), .enable("true"), .NewFFLayout("false")) u_IR2 (
    .clk(CLK), .D(and_6_out), .Q(IR2_q));  // open: Qn, preset, en, reset
  D_Flip_Flop #(.trigger("rising"), .Pre_Clr_Positions("LEGACY"), .NegatePresetClear("false"), .enable("true"), .NewFFLayout("false")) u_IR3 (
    .clk(CLK), .D(and_7_out), .Q(IR3_q));  // open: Qn, preset, en, reset
  Hex_Digit_Display hex_digit_display_8 (.value(LedData[3:0]));  // open: dp
  ROM #(.addrWidth(10), .dataWidth(32), .Select("high")) rom_1 (.addr(PC[11:2]), .data(IR));
  or or_8 (or_8_out, ERET, comparator_1_eq);
  Multiplexer #(.select(1), .width(2), .disabled("Z"), .enable("false")) multiplexer_4 (
    .in0(priority_encoder_1_out), .in1(2'b00), .out(multiplexer_4_out), .sel(ERET));
  or or_9 (IR1_t, IR1, IRA);
  Priority_Encoder #(.select(2), .disabled("Z")) priority_encoder_1 (
    .in0(1'b0), .in1(IR1_q), .in2(IR2_q), .in3(IR3_q), .out(priority_encoder_1_out), .gs(INT), .en_in(1'b1));  // open: en_out
  Register #(.width(2), .trigger("rising"), .Select("high")) register_2 (
    .D(multiplexer_4_out), .en(or_8_out), .Q(register_2_q), .clk(CLK));  // open: clr
  Decoder #(.select(2), .tristate("false"), .disabled("Z"), .enable("false")) decoder_1 (
    .out1(decoder_1_out1), .out2(decoder_1_out2), .out3(decoder_1_out3), .sel(register_2_q));  // open: out0
  or or_10 (IR2_t, IR2, IRB);
  Comparator #(.width(2), .mode("unsigned")) comparator_1 (
    .a(register_2_q), .b(2'b00), .eq(comparator_1_eq));  // open: gt, lt
  D_Flip_Flop #(.trigger("high"), .Pre_Clr_Positions("LEGACY"), .NegatePresetClear("false"), .enable("true"), .NewFFLayout("false")) d_ff_4 (.Q(d_ff_4_q));  // open: clk, D, Qn, preset, en, reset
  // Probe on 13'h2f5
  // Mips_Probe mips_probe_1: pin names not known; wires that end beside it: IR
  Multiplexer #(.select(2), .width(32), .disabled("Z"), .enable("false")) multiplexer_5 (
    .in1(32'h30ac), .in2(32'h3150), .in3(32'h31f4), .out(multiplexer_5_out), .sel(priority_encoder_1_out));  // open: in0
  T_Flip_Flop #(.trigger("rising"), .Pre_Clr_Positions("ABOVE_BELOW"), .NegatePresetClear("false"), .enable("false"), .NewFFLayout("true")) t_ff_1 (
    .clk(CLK), .T(EnterInt), .Qn(t_ff_1_qn));  // open: Q, preset, reset
  Comparator #(.width(13), .mode("twosComplement")) comparator_2 (
    .a(CNT_num), .b(13'h2f5), .eq(comparator_2_eq), .lt(comparator_2_lt));  // open: gt
  Clock #(.highDuration(1), .lowDuration(1)) clock_2 (.out(clock_2_out));
  or or_11 (IR3_t, IR3, IRC);
  assign bit_extender_1_out = {{16{1'b0}}, IR[15:0]};  // Bit_Extender bit_extender_1
  assign bit_extender_2_out = {{16{IR[15]}}, IR[15:0]};  // Bit_Extender bit_extender_2
  and and_8 (and_8_out, Syscall, not_1_out);
  not not_1 (not_1_out, equal);
  and and_9 (and_9_out, INT, t_ff_1_qn);
  nand nand_1 (nand_1_out, d_ff_4_q, comparator_2_eq);
  Counter #(.width(13), .max('h1fff), .ongoal("stay"), .trigger("rising"), .behavior("old")) counter_1 (
    .count(comparator_2_lt), .Q(CNT_num), .clk(clock_2_out));  // open: load, D, carry, clr, preset
  \单周期硬布线控制器  \u_单周期硬布线控制器_1  (
    .Func(IR[5:0]), .OP(IR[31:26]), .ALU_OP(\单周期硬布线控制器_1_alu_op ), .MemToReg(\单周期硬布线控制器_1_memtoreg ),
    .MemWrite(MemWrite), .ALU_SRC(\单周期硬布线控制器_1_alu_src ), .RegWrite(RegWrite), .SysCALL(Syscall),
    .SignedExt(SignedExt), .RegDst(\单周期硬布线控制器_1_regdst ), .JR(\单周期硬布线控制器_1_jr [0]),
    .JMP(\单周期硬布线控制器_1_jr [1]), .Beq(\单周期硬布线控制器_1_beq ), .JAL(\单周期硬布线控制器_1_jal ), .Bne(\单周期硬布线控制器_1_bne ),
    .ERET(ERET));  // open: LUI, LB, BGTZ
  Multiplexer #(.select(1), .width(5), .disabled("Z"), .enable("false")) multiplexer_6 (
    .in0(IR[25:21]), .in1(5'b00010), .out(multiplexer_6_out), .sel(Syscall));
  Multiplexer #(.select(1), .width(5), .disabled("Z"), .enable("false")) multiplexer_7 (
    .in0(IR[20:16]), .in1(5'b00100), .out(multiplexer_7_out), .sel(Syscall));
  Multiplexer #(.select(1), .width(5), .disabled("Z"), .enable("false")) multiplexer_8 (
    .in0(IR[20:16]), .in1(IR[15:11]), .out(multiplexer_8_out), .sel(\单周期硬布线控制器_1_regdst ));
  Multiplexer #(.select(1), .width(32), .disabled("Z"), .enable("false")) multiplexer_9 (
    .in0(bit_extender_1_out), .in1(bit_extender_2_out), .out(multiplexer_9_out), .sel(SignedExt));
  J_K_Flip_Flop #(.trigger("rising"), .Pre_Clr_Positions("ABOVE_BELOW"), .NegatePresetClear("false"), .enable("false"), .NewFFLayout("true")) j_k_ff_1 (
    .J(and_8_out), .clk(CLK), .K(Go), .Qn(power), .reset(Go));  // open: Q, preset
  Multiplexer #(.select(1), .width(32), .disabled("Z"), .enable("false")) multiplexer_10 (
    .in0(multiplexer_5_out), .in1(RET), .out(INTADDR), .sel(ERET));
  assign CLK = nand_1_out ? clock_2_out : 1'bz;  // Controlled_Buffer controlled_buffer_1
  and and_10 (and_10_out, \单周期硬布线控制器_1_beq , equal);
  Multiplexer #(.select(1), .width(5), .disabled("Z"), .enable("false")) multiplexer_11 (
    .in0(multiplexer_8_out), .in1({5{1'b1}}), .out(multiplexer_11_out), .sel(\单周期硬布线控制器_1_jal ));
  Multiplexer #(.select(1), .width(32), .disabled("Z"), .enable("false")) multiplexer_12 (
    .in0(multiplexer_17_out), .in1({adder_1_out, adder_1_out_2}), .out(RDin), .sel(\单周期硬布线控制器_1_jal ));
  Register #(.width(32), .trigger("falling"), .Select("low")) register_3 (
    .D(PC_4), .Q(RET), .clk(EnterInt));  // open: en, clr
  or or_12 (EnterInt, and_9_out, ERET);
  Pull_Resistor #(.pull(1)) pull_resistor_1 (.node(CLK));
  MIPS_Regifile mips_regifile_1 (
    .Din(RDin), .Clk(CLK), .R1(R1), .R2(MDin), .WE(RegWrite), .W_num(multiplexer_11_out),
    .R1_num(multiplexer_6_out), .R2_num(multiplexer_7_out));
  Shifter #(.width(32), .shift("ll")) shifter_1 (.in(multiplexer_9_out), .\dist (5'b00010), .out(shifter_1_out));
  and and_11 (and_11_out, \单周期硬布线控制器_1_bne , not_2_out);
  not not_2 (not_2_out, equal);
  Adder #(.width(32)) adder_3 (
    .a(shifter_1_out), .b({adder_1_out, adder_1_out_2}), .out(adder_3_out));  // open: cin, cout
  Multiplexer #(.select(1), .width(32), .disabled("Z"), .enable("false")) multiplexer_13 (
    .in0(MDin), .in1(multiplexer_9_out), .out(multiplexer_13_out), .sel(\单周期硬布线控制器_1_alu_src ));
  and and_12 (and_12_out, Syscall, equal);
  Multiplexer #(.select(1), .width(32), .disabled("Z"), .enable("false")) multiplexer_14 (
    .in0(multiplexer_13_out), .in1(32'h22), .out(multiplexer_14_out), .sel(Syscall));
  Register #(.width(8), .trigger("rising"), .Select("low")) register_4 (
    .D(multiplexer_15_out), .en(1'b1), .Q(register_4_q), .clk(EnterInt));  // open: clr
  MIPS_ALU mips_alu_1 (
    .X(R1), .Y(multiplexer_14_out), .AluOP(\单周期硬布线控制器_1_alu_op ), .Equal(equal), .Result(mips_alu_1_result),
    .shamt(IR[10:6]));  // open: Result_2
  Subtractor #(.width(8)) subtractor_1 (.a(register_4_q), .b(8'h1), .out(subtractor_1_out));  // open: bin, bout
  Adder #(.width(8)) adder_4 (.a(register_4_q), .b(8'h1), .out(adder_4_out));  // open: cin, cout
  Register #(.width(32), .trigger("rising"), .Select("low")) register_5 (
    .D(MDin), .en(and_12_out), .Q(LedData), .clk(CLK), .clr(RST));
  Multiplexer #(.select(1), .width(8), .disabled("Z"), .enable("false")) multiplexer_15 (
    .in0(subtractor_1_out), .in1(adder_4_out), .out(multiplexer_15_out), .sel(undriven));
  Multiplexer #(.select(1), .width(8), .disabled("Z"), .enable("false")) multiplexer_16 (
    .in0(register_4_q), .in1(subtractor_1_out), .out(multiplexer_16_out), .sel(undriven));
  Adder #(.width(32)) adder_5 (.a(PC_4), .b(32'h4), .out(adder_5_out));  // open: cin, cout
  not not_3 (not_3_out, ERET);
  Comparator #(.width(16), .mode("twosComplement")) comparator_3 (
    .a(16'h23b), .b(\总周期数 ), .eq(comparator_3_eq));  // open: gt, lt
  Comparator #(.width(16), .mode("twosComplement")) comparator_4 (
    .a(\总周期数 ), .b(16'h1), .eq(comparator_4_eq));  // open: gt, lt
  Comparator #(.width(16), .mode("twosComplement")) comparator_5 (
    .a(\总周期数 ), .b(16'h4), .eq(comparator_5_eq));  // open: gt, lt
  Comparator #(.width(16), .mode("twosComplement")) comparator_6 (
    .a(\总周期数 ), .b(16'h7), .eq(comparator_6_eq));  // open: gt, lt
  or or_13 (or_13_out, comparator_3_eq, comparator_4_eq);
  Pull_Resistor #(.pull(0)) pull_resistor_2 (.node(IRA));
  assign IRA = or_13_out ? ~CLK : 1'bz;  // Controlled_Inverter controlled_inverter_1
  Pull_Resistor #(.pull(0)) pull_resistor_3 (.node(IRB));
  assign IRB = comparator_5_eq ? ~CLK : 1'bz;  // Controlled_Inverter controlled_inverter_2
  Pull_Resistor #(.pull(0)) pull_resistor_4 (.node(IRC));
  assign IRC = comparator_6_eq ? ~CLK : 1'bz;  // Controlled_Inverter controlled_inverter_3
  RAM #(.addrWidth(8), .dataWidth(32), .bus("separate"), .Select("low")) ram_1 (
    .addr(multiplexer_16_out), .din(adder_5_out), .data(ram_1_data), .str(not_3_out), .clk(EnterInt),
    .ld(1'b1));  // open: sel, clr
  RAM #(.addrWidth(10), .dataWidth(32), .bus("separate"), .Select("high")) ram_2 (
    .addr(mips_alu_1_result[11:2]), .din(MDin), .data(ram_2_data), .str(MemWrite), .clk(CLK), .clr(RST));  // open: sel, ld
  Multiplexer #(.select(1), .width(32), .disabled("Z"), .enable("false")) multiplexer_17 (
    .in0(mips_alu_1_result), .in1(ram_2_data), .out(multiplexer_17_out), .sel(\单周期硬布线控制器_1_memtoreg ));
  Multiplexer #(.select(2), .width(8), .disabled("Z"), .enable("false")) multiplexer_18 (
    .in0(multiplexer_17_out[7:0]), .in1(multiplexer_17_out[15:8]), .in2(multiplexer_17_out[23:16]),
    .in3(multiplexer_17_out[31:24]), .out(multiplexer_18_out), .sel(mips_alu_1_result[1:0]));
  Bit_Extender #(.in_width(8), .out_width(16), .\type ("sign")) bit_extender_3 (.in(multiplexer_18_out));  // open: out

  // Other names for the same wires on the sheet: R2[31:0] = MDin

  // Notes on the sheet:
  //   中断源
  //   中断等待指示
  //   总复位信号应将除ROM以外所有存储组件全部清零
  //   中断信号采样参考电路
  //   中断信号采样参考电路
  //   数码管输出
  //   Reset 
  //   Reset 
  //   Reset 
  //   数码管输出应该用寄存器锁存，否则显示数据只能一闪而过
  //   指令存储器
  //   指令字
  //   contents of rom_1 (hex, n*v repeats v):
  //   201d07d0 20100001 109fc0 139fc3 8021 2012000c 24160008 26100001 3210000f 20080008 20090001 139900
  //   2709825 132020 20020022 c 1094022 1500fff9 22100001 2018000f 2188024 108700 20080008 20090001 139902
  //   2709825 132021 20020022 c 1094022 1500fff9 108702 2c9b022 12c00001 8000c07 4020 1084027 84400
  //   3508ffff 82021 20020022 c 8000c01 afa20000 23bd0004 afa40000 23bd0004 afb00000 23bd0004 afb30000
  //   23bd0004 afb40000 23bd0004 afb50000 23bd0004 afb60000 23bd0004 20160001 20140003 20150001 168020
  //   108100 2149825 132020 20020022 c 1600fffa 295a022 1680fff7 23bdfffc 8fb60000 23bdfffc 8fb50000
  //   23bdfffc 8fb40000 23bdfffc 8fb30000 23bdfffc 8fb00000 23bdfffc 8fa40000 23bdfffc 8fa20000 42000018
  //   afa20000 23bd0004 afa40000 23bd0004 afb00000 23bd0004 afb30000 23bd0004 afb40000 23bd0004 afb50000
  //   23bd0004 afb60000 23bd0004 20160002 20140003 20150001 168020 108100 2149825 132020 20020022 c
  //   1600fffa 295a022 1680fff7 23bdfffc 8fb60000 23bdfffc 8fb50000 23bdfffc 8fb40000 23bdfffc 8fb30000
  //   23bdfffc 8fb00000 23bdfffc 8fa40000 23bdfffc 8fa20000 42000018 afa20000 23bd0004 afa40000 23bd0004
  //   afb00000 23bd0004 afb30000 23bd0004 afb40000 23bd0004 afb50000 23bd0004 afb60000 23bd0004 20160003
  //   20140003 20150001 168020 108100 2149825 132020 20020022 c 1600fffa 295a022 1680fff7 23bdfffc
  //   8fb60000 23bdfffc 8fb50000 23bdfffc 8fb40000 23bdfffc 8fb30000 23bdfffc 8fb00000 23bdfffc 8fa40000
  //   23bdfffc 8fa20000 42000018
  //   控制位
  //   暂停节拍，不能为0
  //   OP
  //   Func
  //   rs
  //   rt
  //   rd
  //   im
  //   ii
  //   戳工具置1进入计数暂停模式，ctrl+k时钟自动运行到对应节拍暂停
  //   ctrl+k关闭时钟连续运行，将控制位置零，进入单步调试模式调试
  //   JMP
  //   JR
  //   OP
  //   Func
  //   Beq
  //   Bne
  //   MemToReg
  //   MemWrite
  //   AluOP
  //   AluSrcB
  //   RegWrite
  //   JAL
  //   RegDst
  //   Syscall
  //   可计数暂停的时钟源
  //   为方便自动评测，需要输出PC，IR，寄存器堆写如数据RDin
  //   RAM写使能MemWrite、RAM写入数据MDin等信号
  //   单级中断测试信号模拟器
endmodule

module \单周期MIPS_多级中断  (
  input  IR1,
  input  IR2,
  input  IR3,
  output RegWrite,
  output MemWrite,
  output [31:0] PC,
  output [31:0] IR,
  output [31:0] RDin,
  output [31:0] MDin,
  output [31:0] LedData
);

  wire and_1_out, and_2_out, and_3_out, and_4_out, and_5_out, and_6_out, and_7_out, and_8_out, and_9_out,
       and_10_out, and_11_out, and_13_out, and_14_out, and_15_out, and_16_out, CLK, clock_2_out,
       comparator_1_lt, comparator_2_eq, comparator_2_lt, comparator_3_eq, comparator_4_eq, comparator_5_eq,
       comparator_6_eq, comparator_7_eq, comparator_8_eq, comparator_9_eq, comparator_10_eq, d_ff_1_q,
       d_ff_2_q, d_ff_3_q, d_ff_4_q, EnterInt, equal, ERET, Go, INT, INT1, INT2, INT3, IR1_q, IR1_t, IR2_q,
       IR2_t, IR3_q, IR3_t, IRA, IRB, IRC, MFC0, mips_probe_1_p2, MTC0, nand_1_out, not_1_out, not_2_out,
       not_3_out, not_4_out, not_5_out, not_6_out, not_7_out, or_1_out, or_2_out, or_3_out, or_4_out,
       or_5_out, or_6_out, or_7_out, or_8_out, or_9_out, or_10_out, or_14_out, or_15_out, or_16_out,
       or_17_out, or_18_out, power, RST, SignedExt, Syscall, t_ff_1_qn, t_ff_2_q, t_ff_3_q, t_ff_4_q, W1, W2,
       W3, \单周期硬布线控制器_1_alu_src , \单周期硬布线控制器_1_beq , \单周期硬布线控制器_1_bne , \单周期硬布线控制器_1_jal ,
       \单周期硬布线控制器_1_memtoreg , \单周期硬布线控制器_1_regdst ;
  wire [1:0] multiplexer_4_out, priority_encoder_1_out, priority_encoder_2_out, register_2_q,
       \单周期硬布线控制器_1_jr ;
  wire [3:0] adder_1_out, \单周期硬布线控制器_1_alu_op ;
  wire [4:0] multiplexer_7_out, multiplexer_8_out, multiplexer_9_out, multiplexer_12_out;
  wire [7:0] adder_4_out, multiplexer_16_out, multiplexer_17_out, multiplexer_19_out, register_7_q,
       subtractor_1_out;
  wire [12:0] CNT_num;
  wire [15:0] adder_2_out, \总周期数 ;
  wire [27:0] adder_1_out_2;
  wire [31:0] adder_3_out, adder_5_out, bit_extender_1_out, bit_extender_2_out, INTADDR, mips_alu_1_result,
       multiplexer_1_out, multiplexer_3_out, multiplexer_5_out, multiplexer_6_out, multiplexer_10_out,
       multiplexer_14_out, multiplexer_15_out, multiplexer_18_out, PC_4, R1, ram_1_data, ram_2_data, RET,
       RET1, RET2, RET3, shifter_1_out;

  Clock #(.highDuration(1), .lowDuration(1)) clock_1 ();  // open: out
  Button _1 ();  // open: out
  Button _2 ();  // open: out
  Button _3 ();  // open: out
  or or_1 (or_1_out, and_11_out, and_13_out);
  Button \u_继续运行  (.out(Go));
  LED #(.active("true")) led_1 (.in(W1));
  LED #(.active("true")) led_2 (.in(W2));
  LED #(.active("true")) led_3 (.in(W3));
  Button button_1 (.out(RST));
  Multiplexer #(.select(1), .width(32), .disabled("Z"), .enable("false")) multiplexer_1 (
    .in0({adder_1_out, adder_1_out_2}), .in1(adder_3_out), .out(multiplexer_1_out), .sel(or_1_out));
  or or_2 (or_2_out, IR1_q, d_ff_1_q);
  or or_3 (or_3_out, IR2_q, d_ff_2_q);
  or or_4 (or_4_out, IR3_q, d_ff_3_q);
  Hex_Digit_Display hex_digit_display_1 (.value(LedData[31:28]));  // open: dp
  or or_5 (or_5_out, ERET, EnterInt);
  Multiplexer #(.select(2), .width(32), .disabled("Z"), .enable("false")) multiplexer_2 (
    .in0(multiplexer_1_out), .in1(R1), .in2({adder_1_out, IR[25:0], 2'b00}), .in3(R1), .out(PC_4),
    .sel(\单周期硬布线控制器_1_jr ));
  D_Flip_Flop #(.trigger("rising"), .Pre_Clr_Positions("LEGACY"), .NegatePresetClear("false"), .enable("true"), .NewFFLayout("false")) d_ff_1 (
    .clk(IR1_t), .D(1'b1), .Q(d_ff_1_q), .reset(IR1_q));  // open: Qn, preset, en
  D_Flip_Flop #(.trigger("rising"), .Pre_Clr_Positions("LEGACY"), .NegatePresetClear("false"), .enable("true"), .NewFFLayout("false")) d_ff_2 (
    .clk(IR2_t), .D(1'b1), .Q(d_ff_2_q), .reset(IR2_q));  // open: Qn, preset, en
  D_Flip_Flop #(.trigger("rising"), .Pre_Clr_Positions("LEGACY"), .NegatePresetClear("false"), .enable("true"), .NewFFLayout("false")) d_ff_3 (
    .clk(IR3_t), .D(1'b1), .Q(d_ff_3_q), .reset(IR3_q));  // open: Qn, preset, en
  Hex_Digit_Display hex_digit_display_2 (.value(LedData[27:24]));  // open: dp
  Hex_Digit_Display hex_digit_display_3 (.value(LedData[23:20]));  // open: dp
  Register #(.width(32), .trigger("rising"), .Select("low")) u_PC (
    .D(multiplexer_3_out), .en(and_1_out), .Q(PC), .clk(CLK), .clr(RST));
  Multiplexer #(.select(1), .width(32), .disabled("Z"), .enable("false")) multiplexer_3 (
    .in0(PC_4), .in1(INTADDR), .out(multiplexer_3_out), .sel(or_5_out));
  and and_1 (and_1_out, power, power);
  or or_6 (or_6_out, d_ff_1_q, IR1_q);
  and and_2 (and_2_out, ERET, INT1);
  or or_7 (or_7_out, d_ff_2_q, IR2_q);
  and and_3 (and_3_out, ERET, INT2);
  or or_8 (or_8_out, d_ff_3_q, IR3_q);
  and and_4 (and_4_out, ERET, INT3);
  Hex_Digit_Display hex_digit_display_4 (.value(LedData[15:12]));  // open: dp
  Hex_Digit_Display hex_digit_display_5 (.value(LedData[19:16]));  // open: dp
  Register #(.width(16), .trigger("rising"), .Select("low")) register_1 (
    .D(adder_2_out), .en(and_1_out), .Q(\总周期数 ), .clk(CLK), .clr(RST));
  and and_5 (and_5_out, or_6_out, ~and_2_out);  // AND_Gate
  and and_6 (and_6_out, or_7_out, ~and_3_out);  // AND_Gate
  and and_7 (and_7_out, or_8_out, ~and_4_out);  // AND_Gate
  Hex_Digit_Display hex_digit_display_6 (.value(LedData[11:8]));  // open: dp
  Hex_Digit_Display hex_digit_display_7 (.value(LedData[7:4]));  // open: dp
  // Probe on \总周期数 
  Adder #(.width(32)) adder_1 (.a(PC), .b(32'h4), .out({adder_1_out, adder_1_out_2}));  // open: cin, cout
  Adder #(.width(16)) adder_2 (.a(\总周期数 ), .b(16'h1), .out(adder_2_out));  // open: cin, cout
  D_Flip_Flop #(.trigger("rising"), .Pre_Clr_Positions("LEGACY"), .NegatePresetClear("false"), .enable("true"), .NewFFLayout("false")) u_IR1 (
    .clk(CLK), .D(and_5_out), .Q(IR1_q));  // open: Qn, preset, en, reset
  D_Flip_Flop #(.trigger("rising"), .Pre_Clr_Positions("LEGACY"), .NegatePresetClear("false"), .enable("true"), .NewFFLayout("false")) u_IR2 (
    .clk(CLK), .D(and_6_out), .Q(IR2_q));  // open: Qn, preset, en, reset
  D_Flip_Flop #(.trigger("rising"), .Pre_Clr_Positions("LEGACY"), .NegatePresetClear("false"), .enable("true"), .NewFFLayout("false")) u_IR3 (
    .clk(CLK), .D(and_7_out), .Q(IR3_q));  // open: Qn, preset, en, reset
  Hex_Digit_Display hex_digit_display_8 (.value(LedData[3:0]));  // open: dp
  ROM #(.addrWidth(10), .dataWidth(32), .Select("high")) rom_1 (.addr(PC[11:2]), .data(IR));
  and and_8 (and_8_out, t_ff_1_qn, comparator_1_lt);
  Multiplexer #(.select(1), .width(2), .disabled("Z"), .enable("false")) multiplexer_4 (
    .in0(priority_encoder_1_out), .in1(priority_encoder_2_out), .out(multiplexer_4_out), .sel(ERET));
  or or_9 (or_9_out, and_8_out, ERET);
  or or_10 (or_10_out, MFC0, EnterInt);
  or or_11 (IR1_t, IR1, IRA);
  Priority_Encoder #(.select(2), .disabled("Z")) priority_encoder_1 (
    .in0(1'b1), .in1(IR1_q), .in2(IR2_q), .in3(IR3_q), .out(priority_encoder_1_out), .gs(INT), .en_in(1'b1));  // open: en_out
  Register #(.width(2), .trigger("rising"), .Select("high")) register_2 (
    .D(multiplexer_4_out), .en(or_9_out), .Q(register_2_q), .clk(CLK));  // open: clr
  Decoder #(.select(2), .tristate("false"), .disabled("Z"), .enable("false")) decoder_1 (
    .out1(INT1), .out2(INT2), .out3(INT3), .sel(priority_encoder_1_out));  // open: out0
  D_Flip_Flop #(.trigger("high"), .Pre_Clr_Positions("LEGACY"), .NegatePresetClear("false"), .enable("true"), .NewFFLayout("false")) d_ff_4 (.Q(d_ff_4_q));  // open: clk, D, Qn, preset, en, reset
  // Probe on 13'hcc
  or or_12 (IR2_t, IR2, IRB);
  Comparator #(.width(2), .mode("unsigned")) comparator_1 (
    .a(register_2_q), .b(priority_encoder_1_out), .lt(comparator_1_lt));  // open: gt, eq
  T_Flip_Flop #(.trigger("rising"), .Pre_Clr_Positions("LEGACY"), .NegatePresetClear("false"), .enable("true"), .NewFFLayout("false")) t_ff_1 (
    .clk(CLK), .T(or_10_out), .Qn(t_ff_1_qn), .reset(ERET));  // open: Q, preset, en
  Comparator #(.width(13), .mode("twosComplement")) comparator_2 (
    .a(CNT_num), .b(13'hcc), .eq(comparator_2_eq), .lt(comparator_2_lt));  // open: gt
  Clock #(.highDuration(1), .lowDuration(1)) clock_2 (.out(clock_2_out));
  // Mips_Probe mips_probe_1: pin names not known; wires that end beside it: IR, mips_probe_1_p2
  Multiplexer #(.select(2), .width(32), .disabled("Z"), .enable("false")) multiplexer_5 (
    .in1(32'h30ac), .in2(32'h3158), .in3(32'h3204), .out(multiplexer_5_out), .sel(priority_encoder_1_out));  // open: in0
  nand nand_1 (nand_1_out, d_ff_4_q, comparator_2_eq);
  Counter #(.width(13), .max('h1fff), .ongoal("stay"), .trigger("rising"), .behavior("old")) counter_1 (
    .count(comparator_2_lt), .Q(CNT_num), .clk(clock_2_out));  // open: load, D, carry, clr, preset
  or or_13 (IR3_t, IR3, IRC);
  assign bit_extender_1_out = {{16{1'b0}}, IR[15:0]};  // Bit_Extender bit_extender_1
  assign bit_extender_2_out = {{16{IR[15]}}, IR[15:0]};  // Bit_Extender bit_extender_2
  and and_9 (and_9_out, Syscall, not_1_out);
  not not_1 (not_1_out, equal);
  Multiplexer #(.select(2), .width(32), .disabled("Z"), .enable("false")) multiplexer_6 (
    .in1(RET1), .in2(RET2), .in3(RET3), .out(multiplexer_6_out), .sel(priority_encoder_1_out));  // open: in0
  and and_10 (and_10_out, INT, comparator_1_lt);
  assign CLK = nand_1_out ? clock_2_out : 1'bz;  // Controlled_Buffer controlled_buffer_1
  \单周期硬布线控制器  \u_单周期硬布线控制器_1  (
    .Func(IR[5:0]), .OP(IR[31:26]), .ALU_OP(\单周期硬布线控制器_1_alu_op ), .MemToReg(\单周期硬布线控制器_1_memtoreg ),
    .MemWrite(MemWrite), .ALU_SRC(\单周期硬布线控制器_1_alu_src ), .RegWrite(RegWrite), .SysCALL(Syscall),
    .SignedExt(SignedExt), .RegDst(\单周期硬布线控制器_1_regdst ), .JR(\单周期硬布线控制器_1_jr [0]),
    .JMP(\单周期硬布线控制器_1_jr [1]), .Beq(\单周期硬布线控制器_1_beq ), .JAL(\单周期硬布线控制器_1_jal ), .Bne(\单周期硬布线控制器_1_bne ),
    .ERET(mips_probe_1_p2));  // open: LUI, LB, BGTZ
  Multiplexer #(.select(1), .width(5), .disabled("Z"), .enable("false")) multiplexer_7 (
    .in0(IR[25:21]), .in1(5'b00010), .out(multiplexer_7_out), .sel(Syscall));
  Multiplexer #(.select(1), .width(5), .disabled("Z"), .enable("false")) multiplexer_8 (
    .in0(IR[20:16]), .in1(5'b00100), .out(multiplexer_8_out), .sel(Syscall));
  Multiplexer #(.select(1), .width(5), .disabled("Z"), .enable("false")) multiplexer_9 (
    .in0(IR[20:16]), .in1(IR[15:11]), .out(multiplexer_9_out), .sel(\单周期硬布线控制器_1_regdst ));
  Multiplexer #(.select(1), .width(32), .disabled("Z"), .enable("false")) multiplexer_10 (
    .in0(bit_extender_1_out), .in1(bit_extender_2_out), .out(multiplexer_10_out), .sel(SignedExt));
  J_K_Flip_Flop #(.trigger("rising"), .Pre_Clr_Positions("ABOVE_BELOW"), .NegatePresetClear("false"), .enable("false"), .NewFFLayout("true")) j_k_ff_1 (
    .J(and_9_out), .clk(CLK), .K(Go), .Qn(power), .reset(Go));  // open: Q, preset
  Multiplexer #(.select(1), .width(32), .disabled("Z"), .enable("false")) multiplexer_11 (
    .in0(multiplexer_5_out), .in1(multiplexer_6_out), .out(INTADDR), .sel(ERET));
  Pull_Resistor #(.pull(1)) pull_resistor_1 (.node(CLK));
  and and_11 (and_11_out, \单周期硬布线控制器_1_beq , equal);
  Multiplexer #(.select(1), .width(5), .disabled("Z"), .enable("false")) multiplexer_12 (
    .in0(multiplexer_9_out), .in1({5{1'b1}}), .out(multiplexer_12_out), .sel(\单周期硬布线控制器_1_jal ));
  Multiplexer #(.select(1), .width(32), .disabled("Z"), .enable("false")) multiplexer_13 (
    .in0(multiplexer_18_out), .in1({adder_1_out, adder_1_out_2}), .out(RDin), .sel(\单周期硬布线控制器_1_jal ));
  and and_12 (EnterInt, and_10_out, t_ff_1_qn);
  MIPS_Regifile mips_regifile_1 (
    .Din(RDin), .Clk(CLK), .R1(R1), .R2(MDin), .WE(RegWrite), .W_num(multiplexer_12_out),
    .R1_num(multiplexer_7_out), .R2_num(multiplexer_8_out));
  Shifter #(.width(32), .shift("ll")) shifter_1 (.in(multiplexer_10_out), .\dist (5'b00010), .out(shifter_1_out));
  and and_13 (and_13_out, \单周期硬布线控制器_1_bne , not_2_out);
  not not_2 (not_2_out, equal);
  Adder #(.width(32)) adder_3 (
    .a(shifter_1_out), .b({adder_1_out, adder_1_out_2}), .out(adder_3_out));  // open: cin, cout
  or or_14 (or_14_out, EnterInt, ERET);
  or or_15 (or_15_out, EnterInt, ERET);
  or or_16 (or_16_out, EnterInt, ERET);
  Multiplexer #(.select(1), .width(32), .disabled("Z"), .enable("false")) multiplexer_14 (
    .in0(MDin), .in1(multiplexer_10_out), .out(multiplexer_14_out), .sel(\单周期硬布线控制器_1_alu_src ));
  and and_14 (and_14_out, or_15_out, INT2);
  and and_15 (and_15_out, or_16_out, INT3);
  and and_16 (and_16_out, Syscall, equal);
  Multiplexer #(.select(1), .width(32), .disabled("Z"), .enable("false")) multiplexer_15 (
    .in0(multiplexer_14_out), .in1(32'h22), .out(multiplexer_15_out), .sel(Syscall));
  Comparator #(.width(6), .mode("unsigned")) comparator_3 (
    .a(IR[31:26]), .b(6'b010000), .eq(comparator_3_eq));  // open: gt, lt
  Comparator #(.width(5), .mode("unsigned")) comparator_4 (
    .a(IR[25:21]), .b(5'b00100), .eq(comparator_4_eq));  // open: gt, lt
  Comparator #(.width(5), .mode("unsigned")) comparator_5 (
    .a(IR[25:21]), .b({5{1'b0}}), .eq(comparator_5_eq));  // open: gt, lt
  Register #(.width(32), .trigger("falling"), .Select("low")) register_3 (
    .D(PC_4), .en(INT1), .Q(RET1), .clk(EnterInt));  // open: clr
  Register #(.width(32), .trigger("falling"), .Select("low")) register_4 (
    .D(PC_4), .en(INT2), .Q(RET2), .clk(EnterInt));  // open: clr
  Register #(.width(32), .trigger("falling"), .Select("low")) register_5 (
    .D(PC_4), .en(INT3), .Q(RET3), .clk(EnterInt));  // open: clr
  T_Flip_Flop #(.trigger("rising"), .Pre_Clr_Positions("LEGACY"), .NegatePresetClear("false"), .enable("true"), .NewFFLayout("false")) t_ff_2 (
    .clk(or_14_out), .T(INT1), .Q(t_ff_2_q));  // open: Qn, preset, reset, en
  T_Flip_Flop #(.trigger("rising"), .Pre_Clr_Positions("LEGACY"), .NegatePresetClear("false"), .enable("true"), .NewFFLayout("false")) t_ff_3 (
    .clk(and_14_out), .T(INT2), .Q(t_ff_3_q), .en(not_3_out));  // open: Qn, preset, reset
  not not_3 (not_3_out, t_ff_4_q);
  T_Flip_Flop #(.trigger("rising"), .Pre_Clr_Positions("LEGACY"), .NegatePresetClear("false"), .enable("true"), .NewFFLayout("false")) t_ff_4 (
    .clk(and_15_out), .T(INT3), .Q(t_ff_4_q));  // open: Qn, preset, reset, en
  MIPS_ALU mips_alu_1 (
    .X(R1), .Y(multiplexer_15_out), .AluOP(\单周期硬布线控制器_1_alu_op ), .Equal(equal), .Result(mips_alu_1_result),
    .shamt(IR[10:6]));  // open: Result_2
  not not_4 (not_4_out, comparator_4_eq);
  not not_5 (not_5_out, comparator_5_eq);
  Priority_Encoder #(.select(2), .disabled("Z")) priority_encoder_2 (
    .in0(1'b1), .in1(t_ff_2_q), .in2(t_ff_3_q), .in3(t_ff_4_q), .out(priority_encoder_2_out));  // open: gs, en_out, en_in
  Register #(.width(32), .trigger("rising"), .Select("low")) register_6 (
    .D(MDin), .en(and_16_out), .Q(LedData), .clk(CLK), .clr(RST));
  and and_17 (MTC0, comparator_3_eq, comparator_4_eq);
  and and_18 (ERET, comparator_3_eq, not_4_out, not_5_out);
  and and_19 (MFC0, comparator_5_eq, comparator_3_eq);
  Register #(.width(8), .trigger("falling"), .Select("low")) register_7 (
    .D(multiplexer_16_out), .en(1'b1), .Q(register_7_q), .clk(EnterInt));  // open: clr
  RAM #(.addrWidth(10), .dataWidth(32), .bus("separate"), .Select("high")) ram_1 (
    .addr(mips_alu_1_result[11:2]), .din(MDin), .data(ram_1_data), .str(MemWrite), .clk(CLK), .clr(RST));  // open: sel, ld
  Subtractor #(.width(8)) subtractor_1 (.a(register_7_q), .b(8'h1), .out(subtractor_1_out));  // open: bin, bout
  Adder #(.width(8)) adder_4 (.a(register_7_q), .b(8'h1), .out(adder_4_out));  // open: cin, cout
  not not_6 (not_6_out, ERET);
  Multiplexer #(.select(1), .width(8), .disabled("Z"), .enable("false")) multiplexer_16 (
    .in0(subtractor_1_out), .in1(adder_4_out), .out(multiplexer_16_out), .sel(not_6_out));
  Multiplexer #(.select(1), .width(8), .disabled("Z"), .enable("false")) multiplexer_17 (
    .in0(register_7_q), .in1(subtractor_1_out), .out(multiplexer_17_out), .sel(ERET));
  Adder #(.width(32)) adder_5 (.a(PC_4), .b(32'h4), .out(adder_5_out));  // open: cin, cout
  not not_7 (not_7_out, ERET);
  Comparator #(.width(16), .mode("twosComplement")) comparator_6 (
    .a(16'h258), .b(\总周期数 ), .eq(comparator_6_eq));  // open: gt, lt
  Comparator #(.width(16), .mode("twosComplement")) comparator_7 (
    .a(\总周期数 ), .b(16'h1), .eq(comparator_7_eq));  // open: gt, lt
  Comparator #(.width(16), .mode("twosComplement")) comparator_8 (
    .a(\总周期数 ), .b(16'h4), .eq(comparator_8_eq));  // open: gt, lt
  Comparator #(.width(16), .mode("twosComplement")) comparator_9 (
    .a(\总周期数 ), .b(16'h7), .eq(comparator_9_eq));  // open: gt, lt
  or or_17 (or_17_out, comparator_9_eq, comparator_10_eq);
  Comparator #(.width(16), .mode("twosComplement")) comparator_10 (
    .a(\总周期数 ), .b(16'h241), .eq(comparator_10_eq));  // open: gt, lt
  Multiplexer #(.select(1), .width(32), .disabled("Z"), .enable("false")) multiplexer_18 (
    .in0(mips_alu_1_result), .in1(ram_1_data), .out(multiplexer_18_out), .sel(\单周期硬布线控制器_1_memtoreg ));
  Multiplexer #(.select(2), .width(8), .disabled("Z"), .enable("false")) multiplexer_19 (
    .in0(multiplexer_18_out[7:0]), .in1(multiplexer_18_out[15:8]), .in2(multiplexer_18_out[23:16]),
    .in3(multiplexer_18_out[31:24]), .out(multiplexer_19_out), .sel(mips_alu_1_result[1:0]));
  Bit_Extender #(.in_width(8), .out_width(16), .\type ("sign")) bit_extender_3 (.in(multiplexer_19_out));  // open: out
  or or_18 (or_18_out, comparator_6_eq, comparator_7_eq);
  Pull_Resistor #(.pull(0)) pull_resistor_2 (.node(IRA));
  assign IRA = or_18_out ? ~CLK : 1'bz;  // Controlled_Inverter controlled_inverter_1
  Pull_Resistor #(.pull(0)) pull_resistor_3 (.node(IRB));
  assign IRB = comparator_8_eq ? ~CLK : 1'bz;  // Controlled_Inverter controlled_inverter_2
  Pull_Resistor #(.pull(0)) pull_resistor_4 (.node(IRC));
  assign IRC = or_17_out ? ~CLK : 1'bz;  // Controlled_Inverter controlled_inverter_3
  RAM #(.addrWidth(8), .dataWidth(32), .bus("separate"), .Select("low")) ram_2 (
    .addr(multiplexer_17_out), .din(adder_5_out), .data(ram_2_data), .str(not_7_out), .clk(EnterInt),
    .ld(1'b1));  // open: sel, clr
  Register #(.width(32), .trigger("falling"), .Select("low")) register_8 (
    .D(ram_2_data), .Q(RET), .clk(CLK));  // open: en, clr

  // Other names for the same wires on the sheet: RS[4:0] = IR[25:21]; OP[5:0] = IR[31:26]; R2[31:0] = MDin

  // Notes on the sheet:
  //   中断源
  //   中断等待指示
  //   总复位信号应将除ROM以外所有存储组件全部清零
  //   中断信号采样参考电路
  //   中断信号采样参考电路
  //   数码管输出
  //   Reset 
  //   Reset 
  //   Reset 
  //   数码管输出应该用寄存器锁存，否则显示数据只能一闪而过
  //   指令存储器
  //   指令字
  //   contents of rom_1 (hex, n*v repeats v):
  //   201d07d0 20100001 109fc0 139fc3 8021 2012000c 24160008 26100001 3210000f 20080008 20090001 139900
  //   2709825 132020 20020022 c 1094022 1500fff9 22100001 2018000f 2188024 108700 20080008 20090001 139902
  //   2709825 132021 20020022 c 1094022 1500fff9 108702 2c9b022 12c00001 8000c07 4020 1084027 84400
  //   3508ffff 82021 20020022 c 8000c01 afa20000 23bd0004 afa40000 23bd0004 afb00000 23bd0004 afb30000
  //   23bd0004 afb40000 23bd0004 afb50000 23bd0004 afb60000 23bd0004 40000000 20160001 20140003 20150001
  //   168020 108100 2149825 132020 20020022 c 1600fffa 295a022 1680fff7 40800000 23bdfffc 8fb60000
  //   23bdfffc 8fb50000 23bdfffc 8fb40000 23bdfffc 8fb30000 23bdfffc 8fb00000 23bdfffc 8fa40000 23bdfffc
  //   8fa20000 42000018 afa20000 23bd0004 afa40000 23bd0004 afb00000 23bd0004 afb30000 23bd0004 afb40000
  //   23bd0004 afb50000 23bd0004 afb60000 23bd0004 40000000 20160002 20140003 20150001 168020 108100
  //   2149825 132020 20020022 c 1600fffa 295a022 1680fff7 40800000 23bdfffc 8fb60000 23bdfffc 8fb50000
  //   23bdfffc 8fb40000 23bdfffc 8fb30000 23bdfffc 8fb00000 23bdfffc 8fa40000 23bdfffc 8fa20000 42000018
  //   afa20000 23bd0004 afa40000 23bd0004 afb00000 23bd0004 afb30000 23bd0004 afb40000 23bd0004 afb50000
  //   23bd0004 afb60000 23bd0004 40000000 20160003 20140003 20150001 168020 108100 2149825 132020 20020022
  //   c 1600fffa 295a022 1680fff7 40800000 23bdfffc 8fb60000 23bdfffc 8fb50000 23bdfffc 8fb40000 23bdfffc
  //   8fb30000 23bdfffc 8fb00000 23bdfffc 8fa40000 23bdfffc 8fa20000 42000018
  //   控制位
  //   暂停节拍，不能为0
  //   戳工具置1进入计数暂停模式，ctrl+k时钟自动运行到对应节拍暂停
  //   ctrl+k关闭时钟连续运行，将控制位置零，进入单步调试模式调试
  //   OP
  //   Func
  //   rs
  //   rt
  //   rd
  //   im
  //   ii
  //   JMP
  //   JR
  //   OP
  //   Func
  //   可计数暂停的时钟源
  //   Beq
  //   Bne
  //   MemToReg
  //   MemWrite
  //   AluOP
  //   AluSrcB
  //   RegWrite
  //   JAL
  //   RegDst
  //   Syscall
  //   为方便自动评测，需要输出PC，IR，寄存器堆写如数据RDin
  //   RAM写使能MemWrite、RAM写入数据MDin等信号
  //   多级中断测试信号模拟器
endmodule

module \封装正确性测试  (
);

  wire IR1, IR2, IR3, MemW, RegW;
  wire [31:0] EX_PC, ID_PC, IF_PC, IR, LED, MDin, MDinr, MEM_PC, PC, RDin, RDinr, WB_PC;

  \单周期MIPS  \u_单周期mips_1  (
    .IR1(IR1), .IR2(IR2), .IR3(IR3), .RegWrite(RegW), .MemWrite(MemW), .PC(PC), .IR(IR), .RDin(RDin),
    .MDin(MDin), .LedData(LED));
  \气泡流水线  \u_气泡流水线_1  (
    .RegWrite(RegW), .MemWrite(MemW), .IF_PC(IF_PC), .ID_PC(ID_PC), .EX_PC(EX_PC), .M_PC(MEM_PC),
    .WB_PC(WB_PC), .RDin(RDinr), .MDin(MDinr), .LedData(LED));
  \单周期MIPS_单级中断  \u_单周期mips_单级中断_1  (
    .IR1(IR1), .IR2(IR2), .IR3(IR3), .RegWrite(RegW), .MemWrite(MemW), .PC(PC), .IR(IR), .RDin(RDin),
    .MDin(MDin), .LedData(LED));
  \理想流水线  \u_理想流水线_1  (
    .RegWrite(RegW), .MemWrite(MemW), .IF_PC(IF_PC), .ID_PC(ID_PC), .EX_PC(EX_PC), .M_PC(MEM_PC),
    .WB_PC(WB_PC), .RDin(RDinr), .MDin(MDinr), .LedData(LED));
  \重定向流水线  \u_重定向流水线_1  (
    .RegWrite(RegW), .MemWrite(MemW), .IF_PC(IF_PC), .ID_PC(ID_PC), .EX_PC(EX_PC), .M_PC(MEM_PC),
    .WB_PC(WB_PC), .RDin(RDinr), .MDin(MDinr), .LedData(LED));
  \单周期MIPS_多级中断  \u_单周期mips_多级中断_1  (
    .IR1(IR1), .IR2(IR2), .IR3(IR3), .RegWrite(RegW), .MemWrite(MemW), .PC(PC), .IR(IR), .RDin(RDin),
    .MDin(MDin), .LedData(LED));

  // Notes on the sheet:
  //   单周期封装测试
  //   气泡流水封装测试
  //   单周期+单级中断封装测试
  //   请检查上面封装有无位宽不匹配，引脚标签是否和连接的标签相对应，否则无法在educoder平台上正确测试
  //   理想流水封装测试
  //   重定向流水封装测试
  //   单周期+多级中断封装测试
endmodule

module IF_ID (
  input  J,
  input  CLR,
  input  WE,
  input  CLK,
  input  [31:0] IRI,
  input  [31:0] PC_4I,
  input  [31:0] PPCI,
  output [31:0] IRO,
  output [31:0] PC_4O,
  output [31:0] PPCO
);

  wire [31:0] multiplexer_1_out, multiplexer_2_out, multiplexer_3_out;

  Multiplexer #(.select(1), .width(32), .disabled("Z"), .enable("false")) multiplexer_1 (
    .in0(IRI), .in1({32{1'b0}}), .out(multiplexer_1_out), .sel(J));
  Multiplexer #(.select(1), .width(32), .disabled("Z"), .enable("false")) multiplexer_2 (
    .in0(PC_4I), .in1({32{1'b0}}), .out(multiplexer_2_out), .sel(J));
  Multiplexer #(.select(1), .width(32), .disabled("Z"), .enable("false")) multiplexer_3 (
    .in0(PPCI), .in1({32{1'b0}}), .out(multiplexer_3_out), .sel(J));
  Register #(.width(32), .trigger("rising"), .Select("low")) register_1 (
    .D(multiplexer_1_out), .en(WE), .Q(IRO), .clk(CLK), .clr(CLR));
  Register #(.width(32), .trigger("rising"), .Select("low")) register_2 (
    .D(multiplexer_2_out), .en(WE), .Q(PC_4O), .clk(CLK), .clr(CLR));
  Register #(.width(32), .trigger("rising"), .Select("low")) register_3 (
    .D(multiplexer_3_out), .en(WE), .Q(PPCO), .clk(CLK), .clr(CLR));
endmodule

module ID_EX (
  input  J,
  input  CLR,
  input  WE,
  input  CLK,
  input  [31:0] R1I,
  input  [31:0] R2I,
  input  ALU_SrcI,
  input  RegWriteI,
  input  [3:0] ALU_OPI,
  input  [31:0] imExtendedI,
  input  [4:0] shamtI,
  input  MemToRegI,
  input  MemWriteI,
  input  [4:0] WDinI,
  input  BeqI,
  input  BneI,
  input  [31:0] PPCI,
  input  JI,
  input  JRI,
  input  [25:0] iiI,
  input  [31:0] PC_4I,
  input  JalI,
  input  [31:0] IRI,
  input  SyscallI,
  input  LUII,
  input  LBI,
  input  BGTZI,
  input  [1:0] rtForwardI,
  input  [1:0] rsForwardI,
  output [31:0] R1O,
  output [31:0] R2O,
  output ALU_SrcO,
  output RegWriteO,
  output [3:0] ALU_OPO,
  output [31:0] imExtendO,
  output [4:0] shamtI_2,
  output MemToRegO,
  output MemWriteO,
  output [4:0] WDinO,
  output BeqO,
  output BneO,
  output [31:0] PPCO,
  output JO,
  output JRO,
  output [25:0] iiO,
  output [31:0] PC_4O,
  output JalO,
  output [31:0] IRO,
  output SyscallO,
  output SyscallO_2,
  output LBO,
  output BGTZO,
  output [1:0] rtForwardO,
  output [1:0] rsForwardO
);

  wire multiplexer_3_out, multiplexer_4_out, multiplexer_8_out, multiplexer_9_out, multiplexer_11_out,
       multiplexer_12_out, multiplexer_14_out, multiplexer_15_out, multiplexer_18_out, multiplexer_20_out,
       multiplexer_21_out, multiplexer_22_out, multiplexer_23_out;
  wire [1:0] multiplexer_24_out, multiplexer_25_out;
  wire [3:0] multiplexer_5_out;
  wire [4:0] multiplexer_7_out, multiplexer_10_out;
  wire [25:0] multiplexer_16_out;
  wire [31:0] multiplexer_1_out, multiplexer_2_out, multiplexer_6_out, multiplexer_13_out,
       multiplexer_17_out, multiplexer_19_out;

  Multiplexer #(.select(1), .width(32), .disabled("Z"), .enable("false")) multiplexer_1 (
    .in0(R1I), .in1({32{1'b0}}), .out(multiplexer_1_out), .sel(J));
  Multiplexer #(.select(1), .width(32), .disabled("Z"), .enable("false")) multiplexer_2 (
    .in0(R2I), .in1({32{1'b0}}), .out(multiplexer_2_out), .sel(J));
  Multiplexer #(.select(1), .width(1), .disabled("Z"), .enable("false")) multiplexer_3 (
    .in0(ALU_SrcI), .in1(1'b0), .out(multiplexer_3_out), .sel(J));
  Multiplexer #(.select(1), .width(1), .disabled("Z"), .enable("false")) multiplexer_4 (
    .in0(RegWriteI), .in1(1'b0), .out(multiplexer_4_out), .sel(J));
  Multiplexer #(.select(1), .width(4), .disabled("Z"), .enable("false")) multiplexer_5 (
    .in0(ALU_OPI), .in1(4'b0000), .out(multiplexer_5_out), .sel(J));
  Multiplexer #(.select(1), .width(32), .disabled("Z"), .enable("false")) multiplexer_6 (
    .in0(imExtendedI), .in1({32{1'b0}}), .out(multiplexer_6_out), .sel(J));
  Multiplexer #(.select(1), .width(5), .disabled("Z"), .enable("false")) multiplexer_7 (
    .in0(shamtI), .in1({5{1'b0}}), .out(multiplexer_7_out), .sel(J));
  Multiplexer #(.select(1), .width(1), .disabled("Z"), .enable("false")) multiplexer_8 (
    .in0(MemToRegI), .in1(1'b0), .out(multiplexer_8_out), .sel(J));
  Multiplexer #(.select(1), .width(1), .disabled("Z"), .enable("false")) multiplexer_9 (
    .in0(MemWriteI), .in1(1'b0), .out(multiplexer_9_out), .sel(J));
  Multiplexer #(.select(1), .width(5), .disabled("Z"), .enable("false")) multiplexer_10 (
    .in0(WDinI), .in1({5{1'b0}}), .out(multiplexer_10_out), .sel(J));
  Multiplexer #(.select(1), .width(1), .disabled("Z"), .enable("false")) multiplexer_11 (
    .in0(BeqI), .in1(1'b0), .out(multiplexer_11_out), .sel(J));
  Multiplexer #(.select(1), .width(1), .disabled("Z"), .enable("false")) multiplexer_12 (
    .in0(BneI), .in1(1'b0), .out(multiplexer_12_out), .sel(J));
  Multiplexer #(.select(1), .width(32), .disabled("Z"), .enable("false")) multiplexer_13 (
    .in0(PPCI), .in1({32{1'b0}}), .out(multiplexer_13_out), .sel(J));
  Multiplexer #(.select(1), .width(1), .disabled("Z"), .enable("false")) multiplexer_14 (
    .in0(JI), .in1(1'b0), .out(multiplexer_14_out), .sel(J));
  Multiplexer #(.select(1), .width(1), .disabled("Z"), .enable("false")) multiplexer_15 (
    .in0(JRI), .in1(1'b0), .out(multiplexer_15_out), .sel(J));
  Multiplexer #(.select(1), .width(26), .disabled("Z"), .enable("false")) multiplexer_16 (
    .in0(iiI), .in1({26{1'b0}}), .out(multiplexer_16_out), .sel(J));
  Multiplexer #(.select(1), .width(32), .disabled("Z"), .enable("false")) multiplexer_17 (
    .in0(PC_4I), .in1({32{1'b0}}), .out(multiplexer_17_out), .sel(J));
  Multiplexer #(.select(1), .width(1), .disabled("Z"), .enable("false")) multiplexer_18 (
    .in0(JalI), .in1(1'b0), .out(multiplexer_18_out), .sel(J));
  Multiplexer #(.select(1), .width(32), .disabled("Z"), .enable("false")) multiplexer_19 (
    .in0(IRI), .in1({32{1'b0}}), .out(multiplexer_19_out), .sel(J));
  Multiplexer #(.select(1), .width(1), .disabled("Z"), .enable("false")) multiplexer_20 (
    .in0(SyscallI), .in1(1'b0), .out(multiplexer_20_out), .sel(J));
  Multiplexer #(.select(1), .width(1), .disabled("Z"), .enable("false")) multiplexer_21 (
    .in0(LUII), .in1(1'b0), .out(multiplexer_21_out), .sel(J));
  Multiplexer #(.select(1), .width(1), .disabled("Z"), .enable("false")) multiplexer_22 (
    .in0(LBI), .in1(1'b0), .out(multiplexer_22_out), .sel(J));
  Multiplexer #(.select(1), .width(1), .disabled("Z"), .enable("false")) multiplexer_23 (
    .in0(BGTZI), .in1(1'b0), .out(multiplexer_23_out), .sel(J));
  Multiplexer #(.select(1), .width(2), .disabled("Z"), .enable("false")) multiplexer_24 (
    .in0(rtForwardI), .in1(2'b00), .out(multiplexer_24_out), .sel(J));
  Multiplexer #(.select(1), .width(2), .disabled("Z"), .enable("false")) multiplexer_25 (
    .in0(rsForwardI), .in1(2'b00), .out(multiplexer_25_out), .sel(J));
  Register #(.width(32), .trigger("rising"), .Select("low")) register_1 (
    .D(multiplexer_1_out), .en(WE), .Q(R1O), .clk(CLK), .clr(CLR));
  Register #(.width(32), .trigger("rising"), .Select("low")) register_2 (
    .D(multiplexer_2_out), .en(WE), .Q(R2O), .clk(CLK), .clr(CLR));
  Register #(.width(1), .trigger("rising"), .Select("low")) register_3 (
    .D(multiplexer_3_out), .en(WE), .Q(ALU_SrcO), .clk(CLK), .clr(CLR));
  Register #(.width(1), .trigger("rising"), .Select("low")) register_4 (
    .D(multiplexer_4_out), .en(WE), .Q(RegWriteO), .clk(CLK), .clr(CLR));
  Register #(.width(4), .trigger("rising"), .Select("low")) register_5 (
    .D(multiplexer_5_out), .en(WE), .Q(ALU_OPO), .clk(CLK), .clr(CLR));
  Register #(.width(32), .trigger("rising"), .Select("low")) register_6 (
    .D(multiplexer_6_out), .en(WE), .Q(imExtendO), .clk(CLK), .clr(CLR));
  Register #(.width(5), .trigger("rising"), .Select("low")) register_7 (
    .D(multiplexer_7_out), .en(WE), .Q(shamtI_2), .clk(CLK), .clr(CLR));
  Register #(.width(1), .trigger("rising"), .Select("low")) register_8 (
    .D(multiplexer_8_out), .en(WE), .Q(MemToRegO), .clk(CLK), .clr(CLR));
  Register #(.width(1), .trigger("rising"), .Select("low")) register_9 (
    .D(multiplexer_9_out), .en(WE), .Q(MemWriteO), .clk(CLK), .clr(CLR));
  Register #(.width(5), .trigger("rising"), .Select("low")) register_10 (
    .D(multiplexer_10_out), .en(WE), .Q(WDinO), .clk(CLK), .clr(CLR));
  Register #(.width(1), .trigger("rising"), .Select("low")) register_11 (
    .D(multiplexer_11_out), .en(WE), .Q(BeqO), .clk(CLK), .clr(CLR));
  Register #(.width(1), .trigger("rising"), .Select("low")) register_12 (
    .D(multiplexer_12_out), .en(WE), .Q(BneO), .clk(CLK), .clr(CLR));
  Register #(.width(32), .trigger("rising"), .Select("low")) register_13 (
    .D(multiplexer_13_out), .en(WE), .Q(PPCO), .clk(CLK), .clr(CLR));
  Register #(.width(1), .trigger("rising"), .Select("low")) register_14 (
    .D(multiplexer_14_out), .en(WE), .Q(JO), .clk(CLK), .clr(CLR));
  Register #(.width(1), .trigger("rising"), .Select("low")) register_15 (
    .D(multiplexer_15_out), .en(WE), .Q(JRO), .clk(CLK), .clr(CLR));
  Register #(.width(26), .trigger("rising"), .Select("low")) register_16 (
    .D(multiplexer_16_out), .en(WE), .Q(iiO), .clk(CLK), .clr(CLR));
  Register #(.width(32), .trigger("rising"), .Select("low")) register_17 (
    .D(multiplexer_17_out), .en(WE), .Q(PC_4O), .clk(CLK), .clr(CLR));
  Register #(.width(1), .trigger("rising"), .Select("low")) register_18 (
    .D(multiplexer_18_out), .en(WE), .Q(JalO), .clk(CLK), .clr(CLR));
  Register #(.width(32), .trigger("rising"), .Select("low")) register_19 (
    .D(multiplexer_19_out), .en(WE), .Q(IRO), .clk(CLK), .clr(CLR));
  Register #(.width(1), .trigger("rising"), .Select("low")) register_20 (
    .D(multiplexer_20_out), .en(WE), .Q(SyscallO), .clk(CLK), .clr(CLR));
  Register #(.width(1), .trigger("rising"), .Select("low")) register_21 (
    .D(multiplexer_21_out), .en(WE), .Q(SyscallO_2), .clk(CLK), .clr(CLR));
  Register #(.width(1), .trigger("rising"), .Select("low")) register_22 (
    .D(multiplexer_22_out), .en(WE), .Q(LBO), .clk(CLK), .clr(CLR));
  Register #(.width(1), .trigger("rising"), .Select("low")) register_23 (
    .D(multiplexer_23_out), .en(WE), .Q(BGTZO), .clk(CLK), .clr(CLR));
  Register #(.width(2), .trigger("rising"), .Select("low")) register_24 (
    .D(multiplexer_24_out), .en(WE), .Q(rtForwardO), .clk(CLK), .clr(CLR));
  Register #(.width(2), .trigger("rising"), .Select("low")) register_25 (
    .D(multiplexer_25_out), .en(WE), .Q(rsForwardO), .clk(CLK), .clr(CLR));
endmodule

module EX_MEM (
  input  CLR,
  input  WE,
  input  CLK,
  input  [31:0] ALU_RI,
  input  [31:0] WDRI,
  input  MemToRegI,
  input  MemWriteI,
  input  RegWriteI,
  input  [4:0] WDinI,
  input  [31:0] PPCI,
  input  JalI,
  input  [31:0] IRI,
  input  SyscallI,
  input  LBI,
  input  equalI,
  output [31:0] ALU_RO,
  output [31:0] WDRO,
  output MemToRegO,
  output MemWriteO,
  output RegWriteO,
  output [4:0] WDinO,
  output [31:0] PPCO,
  output JalO,
  output [31:0] IRO,
  output SyscallO,
  output LBO,
  output equalO
);

  Register #(.width(32), .trigger("rising"), .Select("low")) register_1 (
    .D(ALU_RI), .en(WE), .Q(ALU_RO), .clk(CLK), .clr(CLR));
  Register #(.width(32), .trigger("rising"), .Select("low")) register_2 (
    .D(WDRI), .en(WE), .Q(WDRO), .clk(CLK), .clr(CLR));
  Register #(.width(1), .trigger("rising"), .Select("low")) register_3 (
    .D(MemToRegI), .en(WE), .Q(MemToRegO), .clk(CLK), .clr(CLR));
  Register #(.width(1), .trigger("rising"), .Select("low")) register_4 (
    .D(MemWriteI), .en(WE), .Q(MemWriteO), .clk(CLK), .clr(CLR));
  Register #(.width(1), .trigger("rising"), .Select("low")) register_5 (
    .D(RegWriteI), .en(WE), .Q(RegWriteO), .clk(CLK), .clr(CLR));
  Register #(.width(5), .trigger("rising"), .Select("low")) register_6 (
    .D(WDinI), .en(WE), .Q(WDinO), .clk(CLK), .clr(CLR));
  Register #(.width(32), .trigger("rising"), .Select("low")) register_7 (
    .D(PPCI), .en(WE), .Q(PPCO), .clk(CLK), .clr(CLR));
  Register #(.width(1), .trigger("rising"), .Select("low")) register_8 (
    .D(JalI), .en(WE), .Q(JalO), .clk(CLK), .clr(CLR));
  Register #(.width(32), .trigger("rising"), .Select("low")) register_9 (
    .D(IRI), .en(WE), .Q(IRO), .clk(CLK), .clr(CLR));
  Register #(.width(1), .trigger("rising"), .Select("low")) register_10 (
    .D(SyscallI), .en(WE), .Q(SyscallO), .clk(CLK), .clr(CLR));
  Register #(.width(1), .trigger("rising"), .Select("low")) register_11 (
    .D(LBI), .en(WE), .Q(LBO), .clk(CLK), .clr(CLR));
  Register #(.width(1), .trigger("rising"), .Select("low")) register_12 (
    .D(equalI), .en(WE), .Q(equalO), .clk(CLK), .clr(CLR));
endmodule

module MEM_WB (
  input  CLR,
  input  WE,
  input  CLK,
  input  [31:0] ALU_RI,
  input  [31:0] MemRDI,
  input  MemToRegI,
  input  RegWriteI,
  input  [4:0] WDinI,
  input  [31:0] PPCI,
  input  JalI,
  input  [31:0] IRI,
  input  SyscallI,
  input  [31:0] RI,
  input  LBI,
  input  equalI,
  output [31:0] ALU_RO,
  output [31:0] MemRDO,
  output MemToRegO,
  output RegWriteO,
  output [4:0] WDinO,
  output [31:0] PPCO,
  output JalO,
  output [31:0] IRO,
  output SyscallO,
  output [31:0] RO,
  output LBO,
  output equalO
);

  Register #(.width(32), .trigger("rising"), .Select("low")) register_1 (
    .D(ALU_RI), .en(WE), .Q(ALU_RO), .clk(CLK), .clr(CLR));
  Register #(.width(32), .trigger("rising"), .Select("low")) register_2 (
    .D(MemRDI), .en(WE), .Q(MemRDO), .clk(CLK), .clr(CLR));
  Register #(.width(1), .trigger("rising"), .Select("low")) register_3 (
    .D(MemToRegI), .en(WE), .Q(MemToRegO), .clk(CLK), .clr(CLR));
  Register #(.width(1), .trigger("rising"), .Select("low")) register_4 (
    .D(RegWriteI), .en(WE), .Q(RegWriteO), .clk(CLK), .clr(CLR));
  Register #(.width(5), .trigger("rising"), .Select("low")) register_5 (
    .D(WDinI), .en(WE), .Q(WDinO), .clk(CLK), .clr(CLR));
  Register #(.width(32), .trigger("rising"), .Select("low")) register_6 (
    .D(PPCI), .en(WE), .Q(PPCO), .clk(CLK), .clr(CLR));
  Register #(.width(1), .trigger("rising"), .Select("low")) register_7 (
    .D(JalI), .en(WE), .Q(JalO), .clk(CLK), .clr(CLR));
  Register #(.width(32), .trigger("rising"), .Select("low")) register_8 (
    .D(IRI), .en(WE), .Q(IRO), .clk(CLK), .clr(CLR));
  Register #(.width(1), .trigger("rising"), .Select("low")) register_9 (
    .D(SyscallI), .en(WE), .Q(SyscallO), .clk(CLK), .clr(CLR));
  Register #(.width(32), .trigger("rising"), .Select("low")) register_10 (
    .D(RI), .en(WE), .Q(RO), .clk(CLK), .clr(CLR));
  Register #(.width(1), .trigger("rising"), .Select("low")) register_11 (
    .D(LBI), .en(WE), .Q(LBO), .clk(CLK), .clr(CLR));
  Register #(.width(1), .trigger("rising"), .Select("low")) register_12 (
    .D(equalI), .en(WE), .Q(equalO), .clk(CLK), .clr(CLR));
endmodule

module DataHazard (
  input  [31:0] in_1,
  input  MEM_regWrite,
  input  EX_regWrite,
  input  [4:0] rs,
  input  [4:0] rt,
  input  [4:0] EX_Writerig_num,
  input  [4:0] MEM_Writerig_num,
  output data
);

  wire and_1_out, and_2_out, and_3_out, and_4_out, and_5_out, and_6_out, comparator_1_eq, comparator_2_eq,
       comparator_3_eq, comparator_4_eq, comparator_5_eq, comparator_6_eq, not_1_out, not_2_out, or_1_out,
       or_2_out, RS_USED, RT_USED;

  Comparator #(.width(5), .mode("twosComplement")) comparator_1 (
    .a(rs), .b({5{1'b0}}), .eq(comparator_1_eq));  // open: gt, lt
  Comparator #(.width(5), .mode("twosComplement")) comparator_2 (
    .a(rt), .b({5{1'b0}}), .eq(comparator_2_eq));  // open: gt, lt
  reg_detect reg_detect_1 (
    .OP0(in_1[26]), .OP1(in_1[27]), .OP2(in_1[28]), .OP3(in_1[29]), .OP4(in_1[30]), .OP5(in_1[31]),
    .F0(in_1[0]), .F1(in_1[1]), .F2(in_1[2]), .F3(in_1[3]), .F4(in_1[4]), .F5(in_1[5]), .rs_used(RS_USED),
    .rt_used(RT_USED));
  Comparator #(.width(5), .mode("twosComplement")) comparator_3 (
    .a(rs), .b(EX_Writerig_num), .eq(comparator_3_eq));  // open: gt, lt
  Comparator #(.width(5), .mode("twosComplement")) comparator_4 (
    .a(rs), .b(MEM_Writerig_num), .eq(comparator_4_eq));  // open: gt, lt
  not not_1 (not_1_out, comparator_1_eq);
  Comparator #(.width(5), .mode("twosComplement")) comparator_5 (
    .a(rt), .b(EX_Writerig_num), .eq(comparator_5_eq));  // open: gt, lt
  Comparator #(.width(5), .mode("twosComplement")) comparator_6 (
    .a(rt), .b(MEM_Writerig_num), .eq(comparator_6_eq));  // open: gt, lt
  not not_2 (not_2_out, comparator_2_eq);
  and and_1 (and_1_out, EX_regWrite, comparator_3_eq);
  and and_2 (and_2_out, MEM_regWrite, comparator_4_eq);
  and and_3 (and_3_out, EX_regWrite, comparator_5_eq);
  and and_4 (and_4_out, MEM_regWrite, comparator_6_eq);
  or or_1 (or_1_out, and_1_out, and_2_out);
  or or_2 (or_2_out, and_3_out, and_4_out);
  and and_5 (and_5_out, RS_USED, or_1_out, not_1_out);
  and and_6 (and_6_out, RT_USED, or_2_out, not_2_out);
  or or_3 (data, and_5_out, and_6_out);
endmodule

module reg_detect (
  input  OP0,
  input  OP1,
  input  OP2,
  input  OP3,
  input  OP4,
  input  OP5,
  input  F0,
  input  F1,
  input  F2,
  input  F3,
  input  F4,
  input  F5,
  output rs_used,
  output rt_used
);

  wire and_1_out, and_2_out, and_3_out, and_4_out, and_5_out, and_6_out, and_7_out, and_8_out, and_9_out,
       and_10_out, and_11_out, and_12_out, and_13_out, and_14_out, and_15_out, and_16_out, and_17_out,
       and_18_out, and_19_out, and_20_out, and_21_out, and_22_out, and_23_out, and_24_out, and_25_out,
       and_26_out, and_27_out, and_28_out, and_29_out, and_30_out, not_1_out, not_2_out, not_3_out,
       not_4_out, not_5_out, not_6_out, not_7_out, not_8_out, not_9_out, not_10_out, not_11_out, not_12_out,
       not_13_out, not_14_out, not_15_out, not_16_out, not_17_out, not_18_out, not_19_out, not_20_out,
       not_21_out, not_22_out, not_23_out, not_24_out, not_25_out, not_26_out, not_27_out, not_28_out,
       not_29_out, not_30_out, not_31_out, not_32_out, not_33_out, not_34_out, not_35_out, not_36_out,
       not_37_out, not_38_out, not_39_out, not_40_out, not_41_out, not_42_out, not_43_out, not_44_out,
       not_45_out, not_46_out, not_47_out, not_48_out, not_49_out, not_50_out, not_51_out, not_52_out,
       not_53_out, not_54_out, not_55_out, not_56_out, not_57_out, not_58_out, not_59_out, not_60_out,
       not_61_out, not_62_out, not_63_out, not_64_out, not_65_out, not_66_out, not_67_out, not_68_out,
       not_69_out, not_70_out, not_71_out, not_72_out, not_73_out, not_74_out, not_75_out, not_76_out,
       not_77_out, not_78_out, not_79_out, not_80_out, not_81_out, not_82_out, not_83_out, not_84_out,
       not_85_out, not_86_out, not_87_out, not_88_out, not_89_out, not_90_out, not_91_out, not_92_out,
       not_93_out, not_94_out, not_95_out, not_96_out, not_97_out, not_98_out, not_99_out, not_100_out,
       not_101_out, not_102_out, not_103_out, not_104_out, not_105_out, not_106_out, not_107_out,
       not_108_out, not_109_out, not_110_out, not_111_out, not_112_out, not_113_out, not_114_out,
       not_115_out, not_116_out, not_117_out, not_118_out, not_119_out, not_120_out, not_121_out,
       not_122_out, not_123_out, not_124_out, not_125_out, not_126_out, not_127_out, not_128_out,
       not_129_out, not_130_out, not_131_out, not_132_out, not_133_out, not_134_out, not_135_out,
       not_136_out, not_137_out, not_138_out, not_139_out, not_140_out, not_141_out, not_142_out,
       not_143_out, not_144_out, not_145_out, not_146_out, not_147_out, not_148_out, not_149_out,
       not_150_out, not_151_out, not_152_out, not_153_out, not_154_out, not_155_out, not_156_out,
       not_157_out, not_158_out, not_159_out, not_160_out, not_161_out, not_162_out, not_163_out,
       not_164_out, not_165_out, not_166_out, not_167_out, not_168_out, not_169_out, not_170_out,
       not_171_out, not_172_out, not_173_out, not_174_out, not_175_out, not_176_out, not_177_out,
       not_178_out, not_179_out, not_180_out, not_181_out, not_182_out, not_183_out, not_184_out,
       not_185_out, not_186_out, not_187_out, not_188_out, not_189_out, not_190_out, not_191_out,
       not_192_out, not_193_out, not_194_out, not_195_out, not_196_out;

  not not_1 (not_1_out, OP5);
  not not_2 (not_2_out, OP4);
  not not_3 (not_3_out, OP3);
  not not_4 (not_4_out, OP2);
  not not_5 (not_5_out, OP1);
  not not_6 (not_6_out, OP0);
  not not_7 (not_7_out, F4);
  not not_8 (not_8_out, F3);
  not not_9 (not_9_out, F2);
  not not_10 (not_10_out, F1);
  not not_11 (not_11_out, F0);
  not not_12 (not_12_out, OP5);
  not not_13 (not_13_out, OP4);
  not not_14 (not_14_out, OP3);
  not not_15 (not_15_out, OP2);
  not not_16 (not_16_out, OP1);
  not not_17 (not_17_out, OP0);
  not not_18 (not_18_out, F4);
  not not_19 (not_19_out, F3);
  not not_20 (not_20_out, F2);
  not not_21 (not_21_out, F1);
  not not_22 (not_22_out, OP5);
  not not_23 (not_23_out, OP4);
  not not_24 (not_24_out, OP3);
  not not_25 (not_25_out, OP2);
  not not_26 (not_26_out, OP1);
  not not_27 (not_27_out, OP0);
  not not_28 (not_28_out, F4);
  not not_29 (not_29_out, F3);
  not not_30 (not_30_out, F2);
  not not_31 (not_31_out, F0);
  not not_32 (not_32_out, OP5);
  not not_33 (not_33_out, OP4);
  not not_34 (not_34_out, OP3);
  not not_35 (not_35_out, OP2);
  not not_36 (not_36_out, OP1);
  not not_37 (not_37_out, OP0);
  not not_38 (not_38_out, F4);
  not not_39 (not_39_out, F3);
  not not_40 (not_40_out, F1);
  not not_41 (not_41_out, F0);
  not not_42 (not_42_out, OP5);
  not not_43 (not_43_out, OP4);
  not not_44 (not_44_out, OP3);
  not not_45 (not_45_out, OP2);
  not not_46 (not_46_out, OP1);
  not not_47 (not_47_out, OP0);
  not not_48 (not_48_out, F4);
  not not_49 (not_49_out, F3);
  not not_50 (not_50_out, F1);
  not not_51 (not_51_out, OP5);
  not not_52 (not_52_out, OP4);
  not not_53 (not_53_out, OP3);
  not not_54 (not_54_out, OP2);
  not not_55 (not_55_out, OP1);
  not not_56 (not_56_out, OP0);
  not not_57 (not_57_out, F4);
  not not_58 (not_58_out, F3);
  not not_59 (not_59_out, OP5);
  not not_60 (not_60_out, OP4);
  not not_61 (not_61_out, OP3);
  not not_62 (not_62_out, OP2);
  not not_63 (not_63_out, OP1);
  not not_64 (not_64_out, OP0);
  not not_65 (not_65_out, F4);
  not not_66 (not_66_out, F2);
  not not_67 (not_67_out, F0);
  not not_68 (not_68_out, OP5);
  not not_69 (not_69_out, OP4);
  not not_70 (not_70_out, OP3);
  not not_71 (not_71_out, OP2);
  not not_72 (not_72_out, OP1);
  not not_73 (not_73_out, OP0);
  not not_74 (not_74_out, F4);
  not not_75 (not_75_out, F2);
  not not_76 (not_76_out, OP5);
  not not_77 (not_77_out, OP4);
  not not_78 (not_78_out, OP3);
  not not_79 (not_79_out, OP2);
  not not_80 (not_80_out, OP1);
  not not_81 (not_81_out, OP0);
  not not_82 (not_82_out, F5);
  not not_83 (not_83_out, F4);
  not not_84 (not_84_out, F2);
  not not_85 (not_85_out, F1);
  not not_86 (not_86_out, F0);
  not not_87 (not_87_out, OP5);
  not not_88 (not_88_out, OP4);
  not not_89 (not_89_out, OP3);
  not not_90 (not_90_out, OP2);
  not not_91 (not_91_out, OP1);
  not not_92 (not_92_out, OP0);
  not not_93 (not_93_out, F5);
  not not_94 (not_94_out, F4);
  not not_95 (not_95_out, F1);
  not not_96 (not_96_out, F0);
  not not_97 (not_97_out, OP5);
  not not_98 (not_98_out, OP4);
  not not_99 (not_99_out, OP3);
  not not_100 (not_100_out, OP1);
  not not_101 (not_101_out, OP0);
  not not_102 (not_102_out, OP5);
  not not_103 (not_103_out, OP4);
  not not_104 (not_104_out, OP3);
  not not_105 (not_105_out, OP1);
  not not_106 (not_106_out, OP5);
  not not_107 (not_107_out, OP4);
  not not_108 (not_108_out, OP2);
  not not_109 (not_109_out, OP1);
  not not_110 (not_110_out, OP0);
  not not_111 (not_111_out, OP5);
  not not_112 (not_112_out, OP4);
  not not_113 (not_113_out, OP1);
  not not_114 (not_114_out, OP0);
  not not_115 (not_115_out, OP5);
  not not_116 (not_116_out, OP4);
  not not_117 (not_117_out, OP2);
  not not_118 (not_118_out, OP1);
  not not_119 (not_119_out, OP5);
  not not_120 (not_120_out, OP4);
  not not_121 (not_121_out, OP2);
  not not_122 (not_122_out, OP0);
  not not_123 (not_123_out, OP5);
  not not_124 (not_124_out, OP4);
  not not_125 (not_125_out, OP1);
  not not_126 (not_126_out, OP4);
  not not_127 (not_127_out, OP3);
  not not_128 (not_128_out, OP2);
  not not_129 (not_129_out, OP4);
  not not_130 (not_130_out, OP2);
  not not_131 (not_131_out, OP5);
  not not_132 (not_132_out, OP4);
  not not_133 (not_133_out, OP2);
  not not_134 (not_134_out, OP4);
  not not_135 (not_135_out, OP3);
  not not_136 (not_136_out, OP2);
  not not_137 (not_137_out, OP1);
  not not_138 (not_138_out, OP0);
  not not_139 (not_139_out, OP5);
  not not_140 (not_140_out, OP4);
  not not_141 (not_141_out, OP3);
  not not_142 (not_142_out, OP0);
  not not_143 (not_143_out, OP1);
  not not_144 (not_144_out, OP3);
  not not_145 (not_145_out, OP4);
  not not_146 (not_146_out, OP5);
  not not_147 (not_147_out, F0);
  not not_148 (not_148_out, F2);
  not not_149 (not_149_out, F3);
  not not_150 (not_150_out, F4);
  not not_151 (not_151_out, OP0);
  not not_152 (not_152_out, OP1);
  not not_153 (not_153_out, OP3);
  not not_154 (not_154_out, OP4);
  not not_155 (not_155_out, OP5);
  not not_156 (not_156_out, F1);
  not not_157 (not_157_out, F3);
  not not_158 (not_158_out, F4);
  not not_159 (not_159_out, OP0);
  not not_160 (not_160_out, OP1);
  not not_161 (not_161_out, OP3);
  not not_162 (not_162_out, OP4);
  not not_163 (not_163_out, OP5);
  not not_164 (not_164_out, F0);
  not not_165 (not_165_out, F1);
  not not_166 (not_166_out, F4);
  not not_167 (not_167_out, F5);
  not not_168 (not_168_out, OP0);
  not not_169 (not_169_out, OP1);
  not not_170 (not_170_out, OP3);
  not not_171 (not_171_out, OP4);
  not not_172 (not_172_out, OP5);
  not not_173 (not_173_out, F2);
  not not_174 (not_174_out, F3);
  not not_175 (not_175_out, F4);
  not not_176 (not_176_out, F5);
  not not_177 (not_177_out, OP0);
  not not_178 (not_178_out, OP1);
  not not_179 (not_179_out, OP3);
  not not_180 (not_180_out, OP4);
  not not_181 (not_181_out, OP5);
  not not_182 (not_182_out, F2);
  not not_183 (not_183_out, F4);
  not not_184 (not_184_out, OP0);
  not not_185 (not_185_out, OP1);
  not not_186 (not_186_out, OP3);
  not not_187 (not_187_out, OP4);
  not not_188 (not_188_out, OP5);
  not not_189 (not_189_out, F3);
  not not_190 (not_190_out, F4);
  not not_191 (not_191_out, OP1);
  not not_192 (not_192_out, OP3);
  not not_193 (not_193_out, OP4);
  not not_194 (not_194_out, OP5);
  not not_195 (not_195_out, OP2);
  not not_196 (not_196_out, OP4);
  and and_1 (and_1_out, not_1_out, not_2_out, not_3_out, not_4_out, not_5_out, not_6_out, F5, not_7_out, not_8_out, not_9_out, not_10_out, not_11_out);
  and and_2 (and_2_out, not_12_out, not_13_out, not_14_out, not_15_out, not_16_out, not_17_out, F5, not_18_out, not_19_out, not_20_out, not_21_out, F0);
  and and_3 (and_3_out, not_22_out, not_23_out, not_24_out, not_25_out, not_26_out, not_27_out, F5, not_28_out, not_29_out, not_30_out, F1, not_31_out);
  and and_4 (and_4_out, not_32_out, not_33_out, not_34_out, not_35_out, not_36_out, not_37_out, F5, not_38_out, not_39_out, F2, not_40_out, not_41_out);
  and and_5 (and_5_out, not_42_out, not_43_out, not_44_out, not_45_out, not_46_out, not_47_out, F5, not_48_out, not_49_out, F2, not_50_out, F0);
  and and_6 (and_6_out, not_51_out, not_52_out, not_53_out, not_54_out, not_55_out, not_56_out, F5, not_57_out, not_58_out, F2, F1, F0);
  and and_7 (and_7_out, not_59_out, not_60_out, not_61_out, not_62_out, not_63_out, not_64_out, F5, not_65_out, F3, not_66_out, F1, not_67_out);
  and and_8 (and_8_out, not_68_out, not_69_out, not_70_out, not_71_out, not_72_out, not_73_out, F5, not_74_out, F3, not_75_out, F1, F0);
  and and_9 (and_9_out, not_76_out, not_77_out, not_78_out, not_79_out, not_80_out, not_81_out, not_82_out, not_83_out, F3, not_84_out, not_85_out, not_86_out);
  and and_10 (and_10_out, not_87_out, not_88_out, not_89_out, not_90_out, not_91_out, not_92_out, not_93_out, not_94_out, F3, F2, not_95_out, not_96_out);
  and and_11 (and_11_out, not_97_out, not_98_out, not_99_out, OP2, not_100_out, not_101_out);
  and and_12 (and_12_out, not_102_out, not_103_out, not_104_out, OP2, not_105_out, OP0);
  and and_13 (and_13_out, not_106_out, not_107_out, OP3, not_108_out, not_109_out, not_110_out);
  and and_14 (and_14_out, not_111_out, not_112_out, OP3, OP2, not_113_out, not_114_out);
  and and_15 (and_15_out, not_115_out, not_116_out, OP3, not_117_out, not_118_out, OP0);
  and and_16 (and_16_out, not_119_out, not_120_out, OP3, not_121_out, OP1, not_122_out);
  and and_17 (and_17_out, not_123_out, not_124_out, OP3, OP2, not_125_out, OP0);
  and and_18 (and_18_out, OP5, not_126_out, not_127_out, not_128_out, OP1, OP0);
  and and_19 (and_19_out, OP5, not_129_out, OP3, not_130_out, OP1, OP0);
  and and_20 (and_20_out, not_131_out, not_132_out, OP3, not_133_out, OP1, OP0);
  and and_21 (and_21_out, OP5, not_134_out, not_135_out, not_136_out, not_137_out, not_138_out);
  and and_22 (and_22_out, not_139_out, not_140_out, not_141_out, OP2, OP1, OP0);
  and and_23 (and_23_out, not_142_out, not_143_out, not_144_out, not_145_out, not_146_out, not_147_out, not_148_out, not_149_out, not_150_out);
  and and_24 (and_24_out, not_151_out, not_152_out, not_153_out, not_154_out, not_155_out, not_156_out, not_157_out, not_158_out, F5);
  and and_25 (and_25_out, not_159_out, not_160_out, not_161_out, not_162_out, not_163_out, not_164_out, not_165_out, F2, F3, not_166_out, not_167_out);
  and and_26 (and_26_out, not_168_out, not_169_out, not_170_out, not_171_out, not_172_out, F1, not_173_out, not_174_out, not_175_out, not_176_out);
  and and_27 (and_27_out, not_177_out, not_178_out, not_179_out, not_180_out, not_181_out, F1, not_182_out, F3, not_183_out, F5);
  and and_28 (and_28_out, not_184_out, not_185_out, not_186_out, not_187_out, not_188_out, F0, F2, not_189_out, not_190_out, F5);
  and and_29 (and_29_out, not_191_out, OP2, not_192_out, not_193_out, not_194_out);
  and and_30 (and_30_out, OP0, OP1, not_195_out, OP3, not_196_out, OP5);
  or or_1 (rt_used, and_23_out, and_24_out, and_25_out, and_26_out, and_27_out, and_28_out, and_29_out, and_30_out);
  or or_2 (rs_used, and_1_out, and_2_out, and_3_out, and_4_out, and_5_out, and_6_out, and_7_out, and_8_out, and_9_out, and_10_out, and_11_out, and_12_out, and_13_out, and_14_out, and_15_out, and_16_out, and_17_out, and_18_out, and_19_out, and_20_out, and_21_out, and_22_out);
endmodule

module Redirect (
  input  [31:0] in_1,
  input  [4:0] rs,
  input  [4:0] rt,
  input  [4:0] EX_Writerig_num,
  input  [4:0] MEM_Writerig_num,
  input  EX_regWrite,
  input  EX_MEMRead,
  input  MEM_regWrite,
  output load_use,
  output [1:0] rs_forward,
  output [1:0] rt_forward
);

  wire and_1_out, and_2_out, and_3_out, and_4_out, and_5_out, and_6_out, and_7_out, and_8_out, and_9_out,
       and_10_out, and_11_out, and_12_out, comparator_1_eq, comparator_2_eq, comparator_3_eq,
       comparator_4_eq, comparator_5_eq, comparator_6_eq, comparator_7_eq, comparator_8_eq, comparator_9_eq,
       comparator_10_eq, comparator_11_eq, comparator_12_eq, not_1_out, not_2_out, not_3_out, not_4_out,
       not_5_out, not_6_out, or_1_out, RS_USED, RT_USED;
  wire [1:0] and_14_out, and_16_out;

  Comparator #(.width(5), .mode("twosComplement")) comparator_1 (
    .a(rs), .b({5{1'b0}}), .eq(comparator_1_eq));  // open: gt, lt
  Comparator #(.width(5), .mode("twosComplement")) comparator_2 (
    .a(rs), .b({5{1'b0}}), .eq(comparator_2_eq));  // open: gt, lt
  Comparator #(.width(5), .mode("twosComplement")) comparator_3 (
    .a(rt), .b({5{1'b0}}), .eq(comparator_3_eq));  // open: gt, lt
  Comparator #(.width(5), .mode("twosComplement")) comparator_4 (
    .a(rt), .b({5{1'b0}}), .eq(comparator_4_eq));  // open: gt, lt
  not not_1 (not_1_out, comparator_5_eq);
  Comparator #(.width(5), .mode("twosComplement")) comparator_5 (
    .a(rs), .b({5{1'b0}}), .eq(comparator_5_eq));  // open: gt, lt
  Comparator #(.width(5), .mode("twosComplement")) comparator_6 (
    .a(rs), .b(EX_Writerig_num), .eq(comparator_6_eq));  // open: gt, lt
  Comparator #(.width(5), .mode("twosComplement")) comparator_7 (
    .a(rt), .b({5{1'b0}}), .eq(comparator_7_eq));  // open: gt, lt
  not not_2 (not_2_out, comparator_7_eq);
  Comparator #(.width(5), .mode("twosComplement")) comparator_8 (
    .a(rt), .b(EX_Writerig_num), .eq(comparator_8_eq));  // open: gt, lt
  not not_3 (not_3_out, comparator_1_eq);
  Comparator #(.width(5), .mode("twosComplement")) comparator_9 (
    .a(rs), .b(EX_Writerig_num), .eq(comparator_9_eq));  // open: gt, lt
  not not_4 (not_4_out, comparator_2_eq);
  Comparator #(.width(5), .mode("twosComplement")) comparator_10 (
    .a(rs), .b(MEM_Writerig_num), .eq(comparator_10_eq));  // open: gt, lt
  not not_5 (not_5_out, comparator_3_eq);
  Comparator #(.width(5), .mode("twosComplement")) comparator_11 (
    .a(rt), .b(EX_Writerig_num), .eq(comparator_11_eq));  // open: gt, lt
  not not_6 (not_6_out, comparator_4_eq);
  Comparator #(.width(5), .mode("twosComplement")) comparator_12 (
    .a(rt), .b(MEM_Writerig_num), .eq(comparator_12_eq));  // open: gt, lt
  reg_detect reg_detect_1 (
    .OP0(in_1[26]), .OP1(in_1[27]), .OP2(in_1[28]), .OP3(in_1[29]), .OP4(in_1[30]), .OP5(in_1[31]),
    .F0(in_1[0]), .F1(in_1[1]), .F2(in_1[2]), .F3(in_1[3]), .F4(in_1[4]), .F5(in_1[5]), .rs_used(RS_USED),
    .rt_used(RT_USED));
  and and_1 (and_1_out, RS_USED, not_1_out);
  and and_2 (and_2_out, RT_USED, not_2_out);
  and and_3 (and_3_out, RS_USED, not_3_out);
  and and_4 (and_4_out, RS_USED, not_4_out);
  and and_5 (and_5_out, RT_USED, not_5_out);
  and and_6 (and_6_out, RT_USED, not_6_out);
  and and_7 (and_7_out, and_1_out, comparator_6_eq);
  and and_8 (and_8_out, and_2_out, comparator_8_eq);
  and and_9 (and_9_out, and_3_out, comparator_9_eq);
  and and_10 (and_10_out, and_4_out, comparator_10_eq);
  and and_11 (and_11_out, and_5_out, comparator_11_eq);
  and and_12 (and_12_out, and_6_out, comparator_12_eq);
  or or_1 (or_1_out, and_7_out, and_8_out);
  and and_13 (and_14_out[1], and_9_out, EX_regWrite);
  and and_14 (and_14_out[0], MEM_regWrite, and_10_out);
  and and_15 (and_16_out[1], and_11_out, EX_regWrite);
  and and_16 (and_16_out[0], MEM_regWrite, and_12_out);
  and and_17 (load_use, or_1_out, EX_MEMRead);
  Multiplexer #(.select(2), .width(2), .disabled("Z"), .enable("false")) multiplexer_1 (
    .in0(2'b00), .in1(2'b01), .in2(2'b10), .in3(2'b10), .out(rs_forward), .sel(and_14_out));
  Multiplexer #(.select(2), .width(2), .disabled("Z"), .enable("false")) multiplexer_2 (
    .in0(2'b00), .in1(2'b01), .in2(2'b10), .in3(2'b10), .out(rt_forward), .sel(and_16_out));
endmodule
